// Logisim project 范唯_CS1703_U201714670_cpu24_动态分支l流水中断.circ as structural Verilog: 22 circuits, main circuit ◇单周期MIPS
module \单周期MIPS  (
  input  IR1,
  input  IR2,
  input  IR3,
  output RegWrite,
  output MemWrite,
  output [31:0] PC,
  output [31:0] IR,
  output [31:0] RDin,
  output [31:0] MDin,
  output [31:0] LedData
);

  wire and_1_out, and_2_out, and_3_out, and_5_out, and_6_out, and_7_out, and_8_out, and_9_out, B, BLEZ, CLK,
       comparator_3_eq, comparator_5_eq, comparator_6_gt, Go, Halt, IR1_t, IR2_t, IR3_t, IRA, IRB, IRC, JAL,
       JMP, JR, mips_alu_3_equal, not_1_out, not_2_out, not_3_out, not_4_out, not_5_out, not_6_out,
       not_7_out, not_8_out, or_1_out, or_4_out, RegDst, RST, SH, SignedExt, SLLV, SRLV, Syscall, W1, W2, W3,
       \单周期硬布线控制器_1_alu_src , \单周期硬布线控制器_1_beq , \单周期硬布线控制器_1_bne , \单周期硬布线控制器_1_memtoreg ;
  wire [3:0] \单周期硬布线控制器_1_alu_op ;
  wire [4:0] multiplexer_4_out, multiplexer_5_out, multiplexer_6_out, multiplexer_7_out, multiplexer_10_out;
  wire [15:0] \总周期数 ;
  wire [31:0] bit_extender_1_out, bit_extender_2_out, bit_extender_3_out, bit_extender_4_out, \J跳转地址 , MDout,
       mips_alu_2_result, mips_alu_3_result, multiplexer_1_out, multiplexer_2_out, multiplexer_9_out,
       multiplexer_12_out, multiplexer_13_out, PC_4, PC_next, R1, R2, shifter_1_out, shifter_2_out,
       shifter_3_out, \立即数I扩展 ;

  Clock clock_1 (.out(CLK));
  Button _1 (.out(IRA));
  Button _2 (.out(IRB));
  Button _3 (.out(IRC));
  // Mips_Probe mips_probe_1: pin names not known; wires that end beside it: IR, CLK
  Button \u_继续运行  (.out(Go));
  LED led_1 (.in(W1));
  LED led_2 (.in(W2));
  LED led_3 (.in(W3));
  Comparator #(.width(6)) comparator_1 (.a(IR[5:0]), .b(6'b000100), .eq(SLLV));  // open: gt, lt
  Comparator #(.width(6)) comparator_2 (.a(IR[5:0]), .b(6'b000110), .eq(SRLV));  // open: gt, lt
  Comparator #(.width(32)) comparator_3 (.a(R1), .b(32'h22), .eq(comparator_3_eq));  // open: gt, lt
  not not_1 (not_1_out, Halt);
  MIPS_ALU mips_alu_1 (.X(PC), .Y(32'h4), .AluOP(4'b0101), .Result(PC_4));  // open: Equal, Result_2, shamt
  Multiplexer #(.width(32), .enable("false")) multiplexer_1 (
    .in0(PC_4), .in1(mips_alu_2_result), .out(multiplexer_1_out), .sel(B));
  Hex_Digit_Display hex_digit_display_1 (.value(LedData[31:28]));  // open: dp
  and and_1 (and_1_out, Syscall, not_2_out);
  not not_2 (not_2_out, comparator_3_eq);
  and and_2 (and_2_out, Syscall, comparator_3_eq);
  Register #(.width(32)) u_PC (.D(PC_next), .en(not_1_out), .Q(PC), .clk(CLK), .clr(RST));
  Multiplexer #(.width(32), .enable("false")) multiplexer_2 (
    .in0(multiplexer_1_out), .in1(R1), .out(multiplexer_2_out), .sel(JR));
  Hex_Digit_Display hex_digit_display_2 (.value(LedData[23:20]));  // open: dp
  Hex_Digit_Display hex_digit_display_3 (.value(LedData[27:24]));  // open: dp
  Comparator #(.width(6)) comparator_4 (.a(IR[31:26]), .b(6'b101001), .eq(SH));  // open: gt, lt
  Comparator #(.width(6)) comparator_5 (.a(IR[31:26]), .b(6'b000110), .eq(comparator_5_eq));  // open: gt, lt
  not not_3 (not_3_out, comparator_6_gt);
  Comparator #(.width(32)) comparator_6 (.a(R1), .b({32{1'b0}}), .gt(comparator_6_gt));  // open: eq, lt
  Counter #(.width(1), .max('h1)) counter_1 (
    .load(and_1_out), .D(and_1_out), .count(1'b0), .Q(Halt), .clk(CLK), .clr(or_1_out));  // open: carry
  or or_1 (or_1_out, Go, RST);
  Register #(.width(32)) register_1 (.D(R2), .en(and_2_out), .Q(LedData), .clk(CLK), .clr(RST));
  Shifter #(.width(32)) shifter_1 (.in(\立即数I扩展 ), .\dist (5'b00010), .out(shifter_1_out));
  and and_3 (and_3_out, JMP, not_4_out);
  Hex_Digit_Display hex_digit_display_4 (.value(LedData[19:16]));  // open: dp
  Hex_Digit_Display hex_digit_display_5 (.value(LedData[15:12]));  // open: dp
  and and_4 (BLEZ, comparator_5_eq, not_3_out);
  ROM #(.addrWidth(10), .dataWidth(32)) rom_1 (.addr(PC[11:2]), .data(IR));  // open: sel
  MIPS_ALU mips_alu_2 (
    .X(PC_4), .Y(shifter_1_out), .AluOP(4'b0101), .Result(mips_alu_2_result));  // open: Equal, Result_2, shamt
  Multiplexer #(.width(32), .enable("false")) multiplexer_3 (
    .in0(multiplexer_2_out), .in1(\J跳转地址 ), .out(PC_next), .sel(and_3_out));
  not not_4 (not_4_out, JR);
  Hex_Digit_Display hex_digit_display_6 (.value(LedData[11:8]));  // open: dp
  Hex_Digit_Display hex_digit_display_7 (.value(LedData[7:4]));  // open: dp
  // Probe on \总周期数 
  Hex_Digit_Display hex_digit_display_8 (.value(LedData[3:0]));  // open: dp
  \单周期硬布线控制器  \u_单周期硬布线控制器_1  (
    .Func(IR[5:0]), .OP(IR[31:26]), .ALU_OP(\单周期硬布线控制器_1_alu_op ), .MemToReg(\单周期硬布线控制器_1_memtoreg ),
    .MemWrite(MemWrite), .ALU_SRC(\单周期硬布线控制器_1_alu_src ), .RegWrite(RegWrite), .SysCALL(Syscall),
    .SignedExt(SignedExt), .RegDst(RegDst), .JR(JR), .JMP(JMP), .Beq(\单周期硬布线控制器_1_beq ), .JAL(JAL),
    .Bne(\单周期硬布线控制器_1_bne ));
  Multiplexer #(.width(5), .enable("false")) multiplexer_4 (
    .in0(IR[25:21]), .in1(5'b00010), .out(multiplexer_4_out), .sel(Syscall));
  Multiplexer #(.width(5), .enable("false")) multiplexer_5 (
    .in0(IR[20:16]), .in1(5'b00100), .out(multiplexer_5_out), .sel(Syscall));
  Multiplexer #(.width(5), .enable("false")) multiplexer_6 (
    .in0(IR[20:16]), .in1(IR[15:11]), .out(multiplexer_6_out), .sel(RegDst));
  assign bit_extender_1_out = {{6{1'b0}}, IR[25:0]};  // Bit_Extender bit_extender_1
  assign bit_extender_2_out = {{28{1'b0}}, PC_4[31:28]};  // Bit_Extender bit_extender_2
  not not_5 (not_5_out, Halt);
  and and_5 (and_5_out, not_5_out, RegWrite);
  Multiplexer #(.width(5), .enable("false")) multiplexer_7 (
    .in0(multiplexer_6_out), .in1({5{1'b1}}), .out(multiplexer_7_out), .sel(JAL));
  assign bit_extender_3_out = {{16{1'b0}}, IR[15:0]};  // Bit_Extender bit_extender_3
  assign bit_extender_4_out = {{16{IR[15]}}, IR[15:0]};  // Bit_Extender bit_extender_4
  Shifter #(.width(32)) shifter_2 (.in(bit_extender_1_out), .\dist (5'b00010), .out(shifter_2_out));
  Shifter #(.width(32)) shifter_3 (.in(bit_extender_2_out), .\dist (5'b11100), .out(shifter_3_out));
  or or_2 (IR1_t, IR1, IRA);
  MIPS_Regifile mips_regifile_1 (
    .Din(RDin), .Clk(CLK), .R1(R1), .R2(R2), .WE(and_5_out), .W_num(multiplexer_7_out),
    .R1_num(multiplexer_4_out), .R2_num(multiplexer_5_out));
  Multiplexer #(.width(32), .enable("false")) multiplexer_8 (
    .in0(bit_extender_3_out), .in1(bit_extender_4_out), .out(\立即数I扩展 ), .sel(SignedExt));
  Adder #(.width(32)) adder_1 (.a(shifter_2_out), .b(shifter_3_out), .out(\J跳转地址 ));  // open: cin, cout
  or or_3 (IR2_t, IR2, IRB);
  Multiplexer #(.width(32), .enable("false")) multiplexer_9 (
    .in0(R2), .in1(\立即数I扩展 ), .out(multiplexer_9_out), .sel(\单周期硬布线控制器_1_alu_src ));
  // Probe on nothing
  or or_4 (or_4_out, SLLV, SRLV);
  Multiplexer #(.width(5), .enable("false")) multiplexer_10 (
    .in0(IR[10:6]), .in1(R1[4:0]), .out(multiplexer_10_out), .sel(or_4_out));
  or or_5 (IR3_t, IR3, IRC);
  not not_6 (not_6_out, mips_alu_3_equal);
  MIPS_ALU mips_alu_3 (
    .X(R1), .Y(multiplexer_9_out), .AluOP(\单周期硬布线控制器_1_alu_op ), .Equal(mips_alu_3_equal),
    .Result(mips_alu_3_result), .shamt(multiplexer_10_out));  // open: Result_2
  Multiplexer #(.width(32), .enable("false")) multiplexer_11 (
    .in0(multiplexer_13_out), .in1(PC_4), .out(RDin), .sel(JAL));
  and and_6 (and_6_out, mips_alu_3_equal, \单周期硬布线控制器_1_beq );
  or or_6 (B, BLEZ, and_6_out, and_7_out);
  and and_7 (and_7_out, not_6_out, \单周期硬布线控制器_1_bne );
  not not_7 (not_7_out, Halt);
  Button \u_总复位  (.out(RST));
  and and_8 (and_8_out, CLK, not_8_out);
  not not_8 (not_8_out, Halt);
  RAM #(.addrWidth(10), .dataWidth(32), .bus("separate")) ram_1 (
    .addr(mips_alu_3_result[11:2]), .din(MDin), .data(MDout), .str(MemWrite), .sel(not_7_out), .clk(CLK),
    .clr(RST));  // open: ld
  and and_9 (and_9_out, SH, mips_alu_3_result[1]);
  Multiplexer #(.width(32), .enable("false")) multiplexer_12 (
    .in0(R2), .in1({MDout[31:16], R2[15:0]}), .out(multiplexer_12_out), .sel(SH));
  Counter #(.width(16), .max('hffff)) counter_2 (
    .Q(\总周期数 ), .clk(and_8_out), .clr(RST));  // open: load, D, count, carry
  Multiplexer #(.width(32), .enable("false")) multiplexer_13 (
    .in0(mips_alu_3_result), .in1(MDout), .out(multiplexer_13_out), .sel(\单周期硬布线控制器_1_memtoreg ));
  Multiplexer #(.width(32), .enable("false")) multiplexer_14 (
    .in0(multiplexer_12_out), .in1({R2[15:0], MDout[15:0]}), .out(MDin), .sel(and_9_out));

  // Other names for the same wires on the sheet: Func[5:0] = IR[5:0]; OP[5:0] = IR[31:26];
  //   R2_H[31:0] = {R2[15:0], MDout[15:0]}; R2_L[31:0] = {MDout[31:16], R2[15:0]}

  // Notes on the sheet:
  //   中断源
  //   中断等待指示
  //   总复位信号应将除ROM以外所有存储组件全部清零
  //   指令存储器
  //   数码管输出
  //   指令字
  //   contents of rom_1 (hex, n*v repeats v):
  //   20110001 8000c05 20110001 20120002 20130003 8000c09 20110001 20120002 20130003 8000c0d 20110001
  //   20120002 20130003 8000c11 20110001 20120002 20130003 c000cf7 20100001 20110001 118fc0 112020
  //   20020022 c 118882 12200001 8000c15 112020 20020022 c 20110001 118880 112020 20020022 c 12200001
  //   8000c1f 20110001 118fc0 112020 20020022 c 1188c3 112020 20020022 c 118903 112020 20020022 c 118903
  //   112020 20020022 c 118903 112020 20020022 c 118903 112020 20020022 c 118903 112020 20020022 c 118903
  //   112020 20020022 c 118903 112020 20020022 c 20100001 109fc0 139fc3 8021 2012000c 24160003 26100001
  //   3210000f 20080008 20090001 139900 2709825 132020 20020022 c 1094022 1500fff9 22100001 2018000f
  //   2188024 108700 20080008 20090001 139902 2709825 132021 20020022 c 1094022 1500fff9 108702 2c9b022
  //   12c00001 8000c50 4020 1084027 84400 3508ffff 82021 20020022 c 2010ffff 20110000 ae300000 22100001
  //   22310004 ae300000 22100001 22310004 ae300000 22100001 22310004 ae300000 22100001 22310004 ae300000
  //   22100001 22310004 ae300000 22100001 22310004 ae300000 22100001 22310004 ae300000 22100001 22310004
  //   ae300000 22100001 22310004 ae300000 22100001 22310004 ae300000 22100001 22310004 ae300000 22100001
  //   22310004 ae300000 22100001 22310004 ae300000 22100001 22310004 ae300000 22100001 22310004 ae300000
  //   22100001 22310004 22100001 8020 2011003c 8e130000 8e340000 274402a 11000002 ae330000 ae140000
  //   2231fffc 1611fff8 102020 20020022 c 22100004 2011003c 1611fff2 20020032 c 20080001 20090003 20110876
  //   112020 20020022 c 200b0008 1118804 1318804 112020 20020022 c 216bffff 1560fff9 2002000a c 20090003
  //   20110876 118d00 112020 20020022 c 200b0008 1118806 1318806 112020 20020022 c 216bffff 1560fff9
  //   2002000a c 20090000 200b0020 20110001 20120001 a5310000 112020 20020022 c 2328820 21290002 216bffff
  //   1560fff8 200b0010 20090000 8d310000 112020 20020022 c 21290004 216bffff 1560fff9 2002000a c 2011fff1
  //   112020 20020022 c 22310001 1a20fffb 2002000a c 20100000 22100001 102020 20020022 c 22100002 102020
  //   20020022 c 22100003 102020 20020022 c 22100004 102020 20020022 c 22100005 102020 20020022 c 22100006
  //   102020 20020022 c 22100007 102020 20020022 c 22100008 102020 20020022 20020022 c 3e00008
  //   数码管输出应该用寄存器锁存，否则显示数据只能一闪而过
  //   OP
  //   Func
  //   rs
  //   rt
  //   rd
  //   shamt
  //   立即数I
  //   立即数J
  //   JMP
  //   JR
  //   OP
  //   Func
  //   Syscall
  //   Beq
  //   Bne
  //   MemToReg
  //   MemWrite
  //   AluOP
  //   AluSrcB
  //   RegWrite
  //   JAL
  //   RegDst
  //   为方便自动评测，需要输出PC，IR，寄存器堆写如数据RDin
  //   RAM写使能MemWrite、RAM写入数据MDin等信号
endmodule

// 单周期硬布线控制器
module \单周期硬布线控制器  (
  input  [5:0] OP,
  input  [5:0] Func,
  output [3:0] ALU_OP,
  output MemToReg,
  output MemWrite,
  output ALU_SRC,
  output RegWrite,
  output SysCALL,
  output SignedExt,
  output RegDst,
  output Beq,
  output Bne,
  output JR,
  output JMP,
  output JAL
);

  \运算控制器自动生成  \u_运算控制器自动生成_1  (
    .OP0(OP[0]), .OP1(OP[1]), .OP2(OP[2]), .OP3(OP[3]), .OP4(OP[4]), .OP5(OP[5]), .F0(Func[0]), .F1(Func[1]),
    .F2(Func[2]), .F3(Func[3]), .F4(Func[4]), .F5(Func[5]), .S0(ALU_OP[0]), .S1(ALU_OP[1]), .S2(ALU_OP[2]),
    .S3(ALU_OP[3]));
  \控制信号自动生成  \u_控制信号自动生成_1  (
    .OP0(OP[0]), .OP1(OP[1]), .OP2(OP[2]), .OP3(OP[3]), .OP4(OP[4]), .OP5(OP[5]), .F0(Func[0]), .F1(Func[1]),
    .F2(Func[2]), .F3(Func[3]), .F4(Func[4]), .F5(Func[5]), .MemToReg(MemToReg), .MemWrite(MemWrite),
    .ALU_SRC(ALU_SRC), .RegWrite(RegWrite), .SysCALL(SysCALL), .SignedExt(SignedExt), .RegDst(RegDst),
    .BEQ(Beq), .BNE(Bne), .JR(JR), .JUMP(JMP), .JAL(JAL));

  // Other names for the same wires on the sheet: OP_CODE[5:0] = OP

  // Notes on the sheet:
  //   运算器控制器，根据指令生成运算器功能选择信号
  //   控制信号生成，产生数据通路需要的其他控制信号
endmodule

// 运算器控制器
module \运算控制器自动生成  (
  input  OP0,
  input  OP1,
  input  OP2,
  input  OP3,
  input  OP4,
  input  OP5,
  input  F0,
  input  F1,
  input  F2,
  input  F3,
  input  F4,
  input  F5,
  output S0,
  output S1,
  output S2,
  output S3
);

  wire and_1_out, and_2_out, and_3_out, and_4_out, and_5_out, and_6_out, and_7_out, and_8_out, and_9_out,
       and_10_out, and_11_out, and_12_out, and_13_out, and_14_out, and_15_out, and_16_out, and_17_out,
       and_18_out, and_19_out, and_20_out, and_21_out, and_22_out, and_23_out, and_24_out, and_25_out,
       not_1_out, not_2_out, not_3_out, not_4_out, not_5_out, not_6_out, not_7_out, not_8_out, not_9_out,
       not_10_out, not_11_out, not_12_out, not_13_out, not_14_out, not_15_out, not_16_out, not_17_out,
       not_18_out, not_19_out, not_20_out, not_21_out, not_22_out, not_23_out, not_24_out, not_25_out,
       not_26_out, not_27_out, not_28_out, not_29_out, not_30_out, not_31_out, not_32_out, not_33_out,
       not_34_out, not_35_out, not_36_out, not_37_out, not_38_out, not_39_out, not_40_out, not_41_out,
       not_42_out, not_43_out, not_44_out, not_45_out, not_46_out, not_47_out, not_48_out, not_49_out,
       not_50_out, not_51_out, not_52_out, not_53_out, not_54_out, not_55_out, not_56_out, not_57_out,
       not_58_out, not_59_out, not_60_out, not_61_out, not_62_out, not_63_out, not_64_out, not_65_out,
       not_66_out, not_67_out, not_68_out, not_69_out, not_70_out, not_71_out, not_72_out, not_73_out,
       not_74_out, not_75_out, not_76_out, not_77_out, not_78_out, not_79_out, not_80_out, not_81_out,
       not_82_out, not_83_out, not_84_out, not_85_out, not_86_out, not_87_out, not_88_out, not_89_out,
       not_90_out, not_91_out, not_92_out, not_93_out, not_94_out, not_95_out, not_96_out, not_97_out,
       not_98_out, not_99_out, not_100_out, not_101_out, not_102_out, not_103_out, not_104_out, not_105_out,
       not_106_out, not_107_out, not_108_out, not_109_out, not_110_out, not_111_out, not_112_out,
       not_113_out, not_114_out, not_115_out, not_116_out, not_117_out, not_118_out, not_119_out,
       not_120_out, not_121_out, not_122_out, not_123_out, not_124_out, not_125_out, not_126_out,
       not_127_out, not_128_out, not_129_out, not_130_out, not_131_out, not_132_out, not_133_out,
       not_134_out, not_135_out, not_136_out, not_137_out, not_138_out, not_139_out, not_140_out,
       not_141_out, not_142_out, not_143_out, not_144_out, not_145_out, not_146_out, not_147_out,
       not_148_out, not_149_out, not_150_out, not_151_out, not_152_out, not_153_out, not_154_out,
       not_155_out, not_156_out, not_157_out, not_158_out, not_159_out;

  not not_1 (not_1_out, OP0);
  not not_2 (not_2_out, OP1);
  not not_3 (not_3_out, OP2);
  not not_4 (not_4_out, OP4);
  not not_5 (not_5_out, OP5);
  not not_6 (not_6_out, F0);
  not not_7 (not_7_out, F1);
  not not_8 (not_8_out, F3);
  not not_9 (not_9_out, F4);
  not not_10 (not_10_out, OP0);
  not not_11 (not_11_out, OP1);
  not not_12 (not_12_out, OP2);
  not not_13 (not_13_out, OP4);
  not not_14 (not_14_out, OP5);
  not not_15 (not_15_out, F1);
  not not_16 (not_16_out, F2);
  not not_17 (not_17_out, F3);
  not not_18 (not_18_out, F4);
  not not_19 (not_19_out, OP0);
  not not_20 (not_20_out, OP1);
  not not_21 (not_21_out, OP2);
  not not_22 (not_22_out, OP4);
  not not_23 (not_23_out, OP5);
  not not_24 (not_24_out, F0);
  not not_25 (not_25_out, F2);
  not not_26 (not_26_out, F4);
  not not_27 (not_27_out, OP0);
  not not_28 (not_28_out, OP1);
  not not_29 (not_29_out, OP2);
  not not_30 (not_30_out, OP4);
  not not_31 (not_31_out, OP5);
  not not_32 (not_32_out, F2);
  not not_33 (not_33_out, F3);
  not not_34 (not_34_out, F4);
  not not_35 (not_35_out, F5);
  not not_36 (not_36_out, OP0);
  not not_37 (not_37_out, OP1);
  not not_38 (not_38_out, OP4);
  not not_39 (not_39_out, OP5);
  not not_40 (not_40_out, OP0);
  not not_41 (not_41_out, OP2);
  not not_42 (not_42_out, OP4);
  not not_43 (not_43_out, OP5);
  not not_44 (not_44_out, OP1);
  not not_45 (not_45_out, OP2);
  not not_46 (not_46_out, OP4);
  not not_47 (not_47_out, OP2);
  not not_48 (not_48_out, OP4);
  not not_49 (not_49_out, OP0);
  not not_50 (not_50_out, OP1);
  not not_51 (not_51_out, OP2);
  not not_52 (not_52_out, OP3);
  not not_53 (not_53_out, OP4);
  not not_54 (not_54_out, OP5);
  not not_55 (not_55_out, F0);
  not not_56 (not_56_out, F1);
  not not_57 (not_57_out, F3);
  not not_58 (not_58_out, F4);
  not not_59 (not_59_out, OP0);
  not not_60 (not_60_out, OP1);
  not not_61 (not_61_out, OP2);
  not not_62 (not_62_out, OP3);
  not not_63 (not_63_out, OP4);
  not not_64 (not_64_out, OP5);
  not not_65 (not_65_out, F0);
  not not_66 (not_66_out, F3);
  not not_67 (not_67_out, F4);
  not not_68 (not_68_out, F5);
  not not_69 (not_69_out, OP0);
  not not_70 (not_70_out, OP1);
  not not_71 (not_71_out, OP2);
  not not_72 (not_72_out, OP3);
  not not_73 (not_73_out, OP4);
  not not_74 (not_74_out, OP5);
  not not_75 (not_75_out, F0);
  not not_76 (not_76_out, F2);
  not not_77 (not_77_out, F4);
  not not_78 (not_78_out, OP0);
  not not_79 (not_79_out, OP1);
  not not_80 (not_80_out, OP2);
  not not_81 (not_81_out, OP3);
  not not_82 (not_82_out, OP4);
  not not_83 (not_83_out, OP5);
  not not_84 (not_84_out, F3);
  not not_85 (not_85_out, F4);
  not not_86 (not_86_out, OP0);
  not not_87 (not_87_out, OP1);
  not not_88 (not_88_out, OP4);
  not not_89 (not_89_out, OP5);
  not not_90 (not_90_out, OP0);
  not not_91 (not_91_out, OP2);
  not not_92 (not_92_out, OP4);
  not not_93 (not_93_out, OP5);
  not not_94 (not_94_out, OP0);
  not not_95 (not_95_out, OP1);
  not not_96 (not_96_out, OP2);
  not not_97 (not_97_out, OP4);
  not not_98 (not_98_out, OP5);
  not not_99 (not_99_out, F0);
  not not_100 (not_100_out, F1);
  not not_101 (not_101_out, F3);
  not not_102 (not_102_out, F4);
  not not_103 (not_103_out, OP0);
  not not_104 (not_104_out, OP1);
  not not_105 (not_105_out, OP2);
  not not_106 (not_106_out, OP4);
  not not_107 (not_107_out, OP5);
  not not_108 (not_108_out, F0);
  not not_109 (not_109_out, F2);
  not not_110 (not_110_out, F3);
  not not_111 (not_111_out, F4);
  not not_112 (not_112_out, OP0);
  not not_113 (not_113_out, OP1);
  not not_114 (not_114_out, OP2);
  not not_115 (not_115_out, OP4);
  not not_116 (not_116_out, OP5);
  not not_117 (not_117_out, F1);
  not not_118 (not_118_out, F2);
  not not_119 (not_119_out, F3);
  not not_120 (not_120_out, F4);
  not not_121 (not_121_out, OP0);
  not not_122 (not_122_out, OP1);
  not not_123 (not_123_out, OP2);
  not not_124 (not_124_out, OP4);
  not not_125 (not_125_out, OP5);
  not not_126 (not_126_out, F2);
  not not_127 (not_127_out, F4);
  not not_128 (not_128_out, OP0);
  not not_129 (not_129_out, OP1);
  not not_130 (not_130_out, OP4);
  not not_131 (not_131_out, OP5);
  not not_132 (not_132_out, OP1);
  not not_133 (not_133_out, OP2);
  not not_134 (not_134_out, OP4);
  not not_135 (not_135_out, OP2);
  not not_136 (not_136_out, OP4);
  not not_137 (not_137_out, OP0);
  not not_138 (not_138_out, OP1);
  not not_139 (not_139_out, OP2);
  not not_140 (not_140_out, OP3);
  not not_141 (not_141_out, OP4);
  not not_142 (not_142_out, OP5);
  not not_143 (not_143_out, F2);
  not not_144 (not_144_out, F4);
  not not_145 (not_145_out, OP0);
  not not_146 (not_146_out, OP1);
  not not_147 (not_147_out, OP2);
  not not_148 (not_148_out, OP3);
  not not_149 (not_149_out, OP4);
  not not_150 (not_150_out, OP5);
  not not_151 (not_151_out, F3);
  not not_152 (not_152_out, F4);
  not not_153 (not_153_out, OP0);
  not not_154 (not_154_out, OP2);
  not not_155 (not_155_out, OP4);
  not not_156 (not_156_out, OP5);
  not not_157 (not_157_out, OP1);
  not not_158 (not_158_out, OP4);
  not not_159 (not_159_out, OP5);
  and and_1 (and_1_out, not_1_out, not_2_out, not_3_out, not_4_out, not_5_out, not_6_out, not_7_out, not_8_out, not_9_out, F5);
  and and_2 (and_2_out, not_10_out, not_11_out, not_12_out, not_13_out, not_14_out, not_15_out, not_16_out, not_17_out, not_18_out, F5);
  and and_3 (and_3_out, not_19_out, not_20_out, not_21_out, not_22_out, not_23_out, not_24_out, F1, not_25_out, F3, not_26_out, F5);
  and and_4 (and_4_out, not_27_out, not_28_out, not_29_out, not_30_out, not_31_out, F0, F1, not_32_out, not_33_out, not_34_out, not_35_out);
  and and_5 (and_5_out, not_36_out, not_37_out, OP3, not_38_out, not_39_out);
  and and_6 (and_6_out, not_40_out, not_41_out, OP3, not_42_out, not_43_out);
  and and_7 (and_7_out, OP0, not_44_out, not_45_out, OP3, not_46_out);
  and and_8 (and_8_out, OP0, OP1, not_47_out, not_48_out, OP5);
  and and_9 (and_9_out, not_49_out, not_50_out, not_51_out, not_52_out, not_53_out, not_54_out, not_55_out, not_56_out, F2, not_57_out, not_58_out, F5);
  and and_10 (and_10_out, not_59_out, not_60_out, not_61_out, not_62_out, not_63_out, not_64_out, not_65_out, F1, not_66_out, not_67_out, not_68_out);
  and and_11 (and_11_out, not_69_out, not_70_out, not_71_out, not_72_out, not_73_out, not_74_out, not_75_out, F1, not_76_out, not_77_out, F5);
  and and_12 (and_12_out, not_78_out, not_79_out, not_80_out, not_81_out, not_82_out, not_83_out, F0, F1, F2, not_84_out, not_85_out, F5);
  and and_13 (and_13_out, not_86_out, not_87_out, OP2, OP3, not_88_out, not_89_out);
  and and_14 (and_14_out, not_90_out, OP1, not_91_out, OP3, not_92_out, not_93_out);
  and and_15 (and_15_out, not_94_out, not_95_out, not_96_out, not_97_out, not_98_out, not_99_out, not_100_out, not_101_out, not_102_out, F5);
  and and_16 (and_16_out, not_103_out, not_104_out, not_105_out, not_106_out, not_107_out, not_108_out, not_109_out, not_110_out, not_111_out, F5);
  and and_17 (and_17_out, not_112_out, not_113_out, not_114_out, not_115_out, not_116_out, not_117_out, not_118_out, not_119_out, not_120_out, F5);
  and and_18 (and_18_out, not_121_out, not_122_out, not_123_out, not_124_out, not_125_out, F0, F1, not_126_out, F3, not_127_out, F5);
  and and_19 (and_19_out, not_128_out, not_129_out, OP3, not_130_out, not_131_out);
  and and_20 (and_20_out, OP0, not_132_out, not_133_out, OP3, not_134_out);
  and and_21 (and_21_out, OP0, OP1, not_135_out, not_136_out, OP5);
  and and_22 (and_22_out, not_137_out, not_138_out, not_139_out, not_140_out, not_141_out, not_142_out, F1, not_143_out, F3, not_144_out, F5);
  and and_23 (and_23_out, not_145_out, not_146_out, not_147_out, not_148_out, not_149_out, not_150_out, F0, F2, not_151_out, not_152_out, F5);
  and and_24 (and_24_out, not_153_out, OP1, not_154_out, OP3, not_155_out, not_156_out);
  and and_25 (and_25_out, OP0, not_157_out, OP2, OP3, not_158_out, not_159_out);
  or or_1 (S0, and_1_out, and_2_out, and_3_out, and_4_out, and_5_out, and_6_out, and_7_out, and_8_out);
  or or_2 (S1, and_9_out, and_10_out, and_11_out, and_12_out, and_13_out, and_14_out);
  or or_3 (S2, and_15_out, and_16_out, and_17_out, and_18_out, and_19_out, and_20_out, and_21_out);
  or or_4 (S3, and_22_out, and_23_out, and_24_out, and_25_out);
endmodule

// 控制信号生成
module \控制信号自动生成  (
  input  OP0,
  input  OP1,
  input  OP2,
  input  OP3,
  input  OP4,
  input  OP5,
  input  F0,
  input  F1,
  input  F2,
  input  F3,
  input  F4,
  input  F5,
  output MemToReg,
  output MemWrite,
  output ALU_SRC,
  output RegWrite,
  output SysCALL,
  output SignedExt,
  output RegDst,
  output BEQ,
  output BNE,
  output JR,
  output JUMP,
  output JAL
);

  wire and_3_out, and_4_out, and_5_out, and_6_out, and_7_out, and_8_out, and_9_out, and_10_out, and_11_out,
       and_12_out, and_13_out, and_14_out, and_15_out, and_17_out, and_18_out, and_19_out, and_20_out,
       and_21_out, and_22_out, and_23_out, and_24_out, and_25_out, and_26_out, and_27_out, and_31_out,
       and_32_out, not_1_out, not_2_out, not_3_out, not_4_out, not_5_out, not_6_out, not_7_out, not_8_out,
       not_9_out, not_10_out, not_11_out, not_12_out, not_13_out, not_14_out, not_15_out, not_16_out,
       not_17_out, not_18_out, not_19_out, not_20_out, not_21_out, not_22_out, not_23_out, not_24_out,
       not_25_out, not_26_out, not_27_out, not_28_out, not_29_out, not_30_out, not_31_out, not_32_out,
       not_33_out, not_34_out, not_35_out, not_36_out, not_37_out, not_38_out, not_39_out, not_40_out,
       not_41_out, not_42_out, not_43_out, not_44_out, not_45_out, not_46_out, not_47_out, not_48_out,
       not_49_out, not_50_out, not_51_out, not_52_out, not_53_out, not_54_out, not_55_out, not_56_out,
       not_57_out, not_58_out, not_59_out, not_60_out, not_61_out, not_62_out, not_63_out, not_64_out,
       not_65_out, not_66_out, not_67_out, not_68_out, not_69_out, not_70_out, not_71_out, not_72_out,
       not_73_out, not_74_out, not_75_out, not_76_out, not_77_out, not_78_out, not_79_out, not_80_out,
       not_81_out, not_82_out, not_83_out, not_84_out, not_85_out, not_86_out, not_87_out, not_88_out,
       not_89_out, not_90_out, not_91_out, not_92_out, not_93_out, not_94_out, not_95_out, not_96_out,
       not_97_out, not_98_out, not_99_out, not_100_out, not_101_out, not_102_out, not_103_out, not_104_out,
       not_105_out, not_106_out, not_107_out, not_108_out, not_109_out, not_110_out, not_111_out,
       not_112_out, not_113_out, not_114_out, not_115_out, not_116_out, not_117_out, not_118_out,
       not_119_out, not_120_out, not_121_out, not_122_out, not_123_out, not_124_out, not_125_out,
       not_126_out, not_127_out, not_128_out, not_129_out, not_130_out, not_131_out, not_132_out,
       not_133_out, not_134_out, not_135_out, not_136_out, not_137_out, not_138_out, not_139_out,
       not_140_out, not_141_out, not_142_out, not_143_out, not_144_out, not_145_out, not_146_out,
       not_147_out, not_148_out, not_149_out, not_150_out, not_151_out, not_152_out, not_153_out,
       not_154_out, not_155_out, not_156_out, not_157_out, not_158_out, not_159_out, not_160_out,
       not_161_out, not_162_out, not_163_out, not_164_out, not_165_out, not_166_out, not_167_out,
       not_168_out, not_169_out, not_170_out, not_171_out, not_172_out, not_173_out, not_174_out,
       not_175_out, not_176_out, not_177_out, not_178_out, not_179_out, not_180_out, not_181_out,
       not_182_out, not_183_out, not_184_out, not_185_out, not_186_out, not_187_out, not_188_out,
       not_189_out, not_190_out, not_191_out, not_192_out, not_193_out, not_194_out, not_195_out, not_196_out;

  not not_1 (not_1_out, OP2);
  not not_2 (not_2_out, OP3);
  not not_3 (not_3_out, OP4);
  not not_4 (not_4_out, OP2);
  not not_5 (not_5_out, OP4);
  not not_6 (not_6_out, OP0);
  not not_7 (not_7_out, OP2);
  not not_8 (not_8_out, OP4);
  not not_9 (not_9_out, OP5);
  not not_10 (not_10_out, OP1);
  not not_11 (not_11_out, OP4);
  not not_12 (not_12_out, OP5);
  not not_13 (not_13_out, OP1);
  not not_14 (not_14_out, OP2);
  not not_15 (not_15_out, OP4);
  not not_16 (not_16_out, OP2);
  not not_17 (not_17_out, OP4);
  not not_18 (not_18_out, OP0);
  not not_19 (not_19_out, OP1);
  not not_20 (not_20_out, OP2);
  not not_21 (not_21_out, OP4);
  not not_22 (not_22_out, OP5);
  not not_23 (not_23_out, F0);
  not not_24 (not_24_out, F2);
  not not_25 (not_25_out, F3);
  not not_26 (not_26_out, F4);
  not not_27 (not_27_out, OP0);
  not not_28 (not_28_out, OP1);
  not not_29 (not_29_out, OP2);
  not not_30 (not_30_out, OP4);
  not not_31 (not_31_out, OP5);
  not not_32 (not_32_out, F0);
  not not_33 (not_33_out, F3);
  not not_34 (not_34_out, F4);
  not not_35 (not_35_out, F5);
  not not_36 (not_36_out, OP0);
  not not_37 (not_37_out, OP1);
  not not_38 (not_38_out, OP2);
  not not_39 (not_39_out, OP4);
  not not_40 (not_40_out, OP5);
  not not_41 (not_41_out, F1);
  not not_42 (not_42_out, F3);
  not not_43 (not_43_out, F4);
  not not_44 (not_44_out, OP0);
  not not_45 (not_45_out, OP1);
  not not_46 (not_46_out, OP2);
  not not_47 (not_47_out, OP4);
  not not_48 (not_48_out, OP5);
  not not_49 (not_49_out, F2);
  not not_50 (not_50_out, F3);
  not not_51 (not_51_out, F4);
  not not_52 (not_52_out, F5);
  not not_53 (not_53_out, OP0);
  not not_54 (not_54_out, OP1);
  not not_55 (not_55_out, OP2);
  not not_56 (not_56_out, OP4);
  not not_57 (not_57_out, OP5);
  not not_58 (not_58_out, F2);
  not not_59 (not_59_out, F4);
  not not_60 (not_60_out, OP0);
  not not_61 (not_61_out, OP1);
  not not_62 (not_62_out, OP2);
  not not_63 (not_63_out, OP4);
  not not_64 (not_64_out, OP5);
  not not_65 (not_65_out, F3);
  not not_66 (not_66_out, F4);
  not not_67 (not_67_out, OP0);
  not not_68 (not_68_out, OP2);
  not not_69 (not_69_out, OP4);
  not not_70 (not_70_out, OP5);
  not not_71 (not_71_out, OP1);
  not not_72 (not_72_out, OP4);
  not not_73 (not_73_out, OP5);
  not not_74 (not_74_out, OP2);
  not not_75 (not_75_out, OP3);
  not not_76 (not_76_out, OP4);
  not not_77 (not_77_out, OP0);
  not not_78 (not_78_out, OP1);
  not not_79 (not_79_out, OP2);
  not not_80 (not_80_out, OP3);
  not not_81 (not_81_out, OP4);
  not not_82 (not_82_out, OP5);
  not not_83 (not_83_out, F0);
  not not_84 (not_84_out, F1);
  not not_85 (not_85_out, F4);
  not not_86 (not_86_out, F5);
  not not_87 (not_87_out, OP0);
  not not_88 (not_88_out, OP2);
  not not_89 (not_89_out, OP4);
  not not_90 (not_90_out, OP5);
  not not_91 (not_91_out, OP0);
  not not_92 (not_92_out, OP3);
  not not_93 (not_93_out, OP4);
  not not_94 (not_94_out, OP5);
  not not_95 (not_95_out, OP1);
  not not_96 (not_96_out, OP3);
  not not_97 (not_97_out, OP4);
  not not_98 (not_98_out, OP5);
  not not_99 (not_99_out, OP1);
  not not_100 (not_100_out, OP2);
  not not_101 (not_101_out, OP4);
  not not_102 (not_102_out, OP2);
  not not_103 (not_103_out, OP4);
  not not_104 (not_104_out, OP0);
  not not_105 (not_105_out, OP1);
  not not_106 (not_106_out, OP2);
  not not_107 (not_107_out, OP3);
  not not_108 (not_108_out, OP4);
  not not_109 (not_109_out, OP5);
  not not_110 (not_110_out, F0);
  not not_111 (not_111_out, F2);
  not not_112 (not_112_out, F3);
  not not_113 (not_113_out, F4);
  not not_114 (not_114_out, OP0);
  not not_115 (not_115_out, OP1);
  not not_116 (not_116_out, OP2);
  not not_117 (not_117_out, OP3);
  not not_118 (not_118_out, OP4);
  not not_119 (not_119_out, OP5);
  not not_120 (not_120_out, F0);
  not not_121 (not_121_out, F3);
  not not_122 (not_122_out, F4);
  not not_123 (not_123_out, F5);
  not not_124 (not_124_out, OP0);
  not not_125 (not_125_out, OP1);
  not not_126 (not_126_out, OP2);
  not not_127 (not_127_out, OP3);
  not not_128 (not_128_out, OP4);
  not not_129 (not_129_out, OP5);
  not not_130 (not_130_out, F1);
  not not_131 (not_131_out, F3);
  not not_132 (not_132_out, F4);
  not not_133 (not_133_out, OP0);
  not not_134 (not_134_out, OP1);
  not not_135 (not_135_out, OP2);
  not not_136 (not_136_out, OP3);
  not not_137 (not_137_out, OP4);
  not not_138 (not_138_out, OP5);
  not not_139 (not_139_out, F2);
  not not_140 (not_140_out, F3);
  not not_141 (not_141_out, F4);
  not not_142 (not_142_out, F5);
  not not_143 (not_143_out, OP0);
  not not_144 (not_144_out, OP1);
  not not_145 (not_145_out, OP2);
  not not_146 (not_146_out, OP3);
  not not_147 (not_147_out, OP4);
  not not_148 (not_148_out, OP5);
  not not_149 (not_149_out, F2);
  not not_150 (not_150_out, F4);
  not not_151 (not_151_out, OP0);
  not not_152 (not_152_out, OP1);
  not not_153 (not_153_out, OP2);
  not not_154 (not_154_out, OP3);
  not not_155 (not_155_out, OP4);
  not not_156 (not_156_out, OP5);
  not not_157 (not_157_out, F3);
  not not_158 (not_158_out, F4);
  not not_159 (not_159_out, OP0);
  not not_160 (not_160_out, OP1);
  not not_161 (not_161_out, OP3);
  not not_162 (not_162_out, OP4);
  not not_163 (not_163_out, OP5);
  not not_164 (not_164_out, OP1);
  not not_165 (not_165_out, OP3);
  not not_166 (not_166_out, OP4);
  not not_167 (not_167_out, OP5);
  not not_168 (not_168_out, OP0);
  not not_169 (not_169_out, OP1);
  not not_170 (not_170_out, OP2);
  not not_171 (not_171_out, OP3);
  not not_172 (not_172_out, OP4);
  not not_173 (not_173_out, OP5);
  not not_174 (not_174_out, F0);
  not not_175 (not_175_out, F1);
  not not_176 (not_176_out, F2);
  not not_177 (not_177_out, F4);
  not not_178 (not_178_out, F5);
  not not_179 (not_179_out, OP0);
  not not_180 (not_180_out, OP2);
  not not_181 (not_181_out, OP3);
  not not_182 (not_182_out, OP4);
  not not_183 (not_183_out, OP5);
  not not_184 (not_184_out, F0);
  not not_185 (not_185_out, F1);
  not not_186 (not_186_out, F2);
  not not_187 (not_187_out, F4);
  not not_188 (not_188_out, F5);
  not not_189 (not_189_out, OP2);
  not not_190 (not_190_out, OP3);
  not not_191 (not_191_out, OP4);
  not not_192 (not_192_out, OP5);
  not not_193 (not_193_out, OP2);
  not not_194 (not_194_out, OP3);
  not not_195 (not_195_out, OP4);
  not not_196 (not_196_out, OP5);
  and and_1 (MemToReg, OP0, OP1, not_1_out, not_2_out, not_3_out, OP5);
  and and_2 (MemWrite, OP0, not_4_out, OP3, not_5_out, OP5);
  and and_3 (and_3_out, not_6_out, not_7_out, OP3, not_8_out, not_9_out);
  and and_4 (and_4_out, not_10_out, OP3, not_11_out, not_12_out);
  and and_5 (and_5_out, OP0, not_13_out, not_14_out, OP3, not_15_out);
  and and_6 (and_6_out, OP0, OP1, not_16_out, not_17_out, OP5);
  and and_7 (and_7_out, not_18_out, not_19_out, not_20_out, not_21_out, not_22_out, not_23_out, not_24_out, not_25_out, not_26_out);
  and and_8 (and_8_out, not_27_out, not_28_out, not_29_out, not_30_out, not_31_out, not_32_out, not_33_out, not_34_out, not_35_out);
  and and_9 (and_9_out, not_36_out, not_37_out, not_38_out, not_39_out, not_40_out, not_41_out, not_42_out, not_43_out, F5);
  and and_10 (and_10_out, not_44_out, not_45_out, not_46_out, not_47_out, not_48_out, F1, not_49_out, not_50_out, not_51_out, not_52_out);
  and and_11 (and_11_out, not_53_out, not_54_out, not_55_out, not_56_out, not_57_out, F1, not_58_out, F3, not_59_out, F5);
  and and_12 (and_12_out, not_60_out, not_61_out, not_62_out, not_63_out, not_64_out, F0, F2, not_65_out, not_66_out, F5);
  and and_13 (and_13_out, not_67_out, not_68_out, OP3, not_69_out, not_70_out);
  and and_14 (and_14_out, not_71_out, OP3, not_72_out, not_73_out);
  and and_15 (and_15_out, OP0, OP1, not_74_out, not_75_out, not_76_out);
  and and_16 (SysCALL, not_77_out, not_78_out, not_79_out, not_80_out, not_81_out, not_82_out, not_83_out, not_84_out, F2, F3, not_85_out, not_86_out);
  and and_17 (and_17_out, not_87_out, not_88_out, OP3, not_89_out, not_90_out);
  and and_18 (and_18_out, not_91_out, OP2, not_92_out, not_93_out, not_94_out);
  and and_19 (and_19_out, not_95_out, OP2, not_96_out, not_97_out, not_98_out);
  and and_20 (and_20_out, OP0, not_99_out, not_100_out, OP3, not_101_out);
  and and_21 (and_21_out, OP0, OP1, not_102_out, not_103_out, OP5);
  and and_22 (and_22_out, not_104_out, not_105_out, not_106_out, not_107_out, not_108_out, not_109_out, not_110_out, not_111_out, not_112_out, not_113_out);
  and and_23 (and_23_out, not_114_out, not_115_out, not_116_out, not_117_out, not_118_out, not_119_out, not_120_out, not_121_out, not_122_out, not_123_out);
  and and_24 (and_24_out, not_124_out, not_125_out, not_126_out, not_127_out, not_128_out, not_129_out, not_130_out, not_131_out, not_132_out, F5);
  and and_25 (and_25_out, not_133_out, not_134_out, not_135_out, not_136_out, not_137_out, not_138_out, F1, not_139_out, not_140_out, not_141_out, not_142_out);
  and and_26 (and_26_out, not_143_out, not_144_out, not_145_out, not_146_out, not_147_out, not_148_out, F1, not_149_out, F3, not_150_out, F5);
  and and_27 (and_27_out, not_151_out, not_152_out, not_153_out, not_154_out, not_155_out, not_156_out, F0, F2, not_157_out, not_158_out, F5);
  and and_28 (BEQ, not_159_out, not_160_out, OP2, not_161_out, not_162_out, not_163_out);
  and and_29 (BNE, OP0, not_164_out, OP2, not_165_out, not_166_out, not_167_out);
  and and_30 (JR, not_168_out, not_169_out, not_170_out, not_171_out, not_172_out, not_173_out, not_174_out, not_175_out, not_176_out, F3, not_177_out, not_178_out);
  and and_31 (and_31_out, not_179_out, not_180_out, not_181_out, not_182_out, not_183_out, not_184_out, not_185_out, not_186_out, F3, not_187_out, not_188_out);
  and and_32 (and_32_out, OP1, not_189_out, not_190_out, not_191_out, not_192_out);
  and and_33 (JAL, OP0, OP1, not_193_out, not_194_out, not_195_out, not_196_out);
  or or_1 (ALU_SRC, and_3_out, and_4_out, and_5_out, and_6_out);
  or or_2 (RegWrite, and_7_out, and_8_out, and_9_out, and_10_out, and_11_out, and_12_out, and_13_out, and_14_out, and_15_out);
  or or_3 (SignedExt, and_17_out, and_18_out, and_19_out, and_20_out, and_21_out);
  or or_4 (RegDst, and_22_out, and_23_out, and_24_out, and_25_out, and_26_out, and_27_out);
  or or_5 (JUMP, and_31_out, and_32_out);
endmodule

// ALU
module MIPS_ALU (
  input  [4:0] shamt,
  input  [31:0] X,
  input  [31:0] Y,
  input  [3:0] AluOP,
  output Equal,
  output [31:0] Result,
  output [31:0] Result_2
);

  wire [0:0] comparator_1_lt, comparator_2_lt;
  wire [31:0] adder_1_out, AND_out, divider_1_out, divider_1_rem, multiplier_1_cout, multiplier_1_out,
       NOR_out, OR_out, shifter_1_out, shifter_2_out, shifter_3_out, subtractor_1_out, XOR_out;

  assign AND_out = X & Y;  // AND_Gate AND, 32 bits wide
  assign OR_out = X | Y;  // OR_Gate OR, 32 bits wide
  Shifter #(.width(32)) shifter_1 (.in(Y), .\dist (shamt), .out(shifter_1_out));
  Shifter #(.width(32), .shift("ar")) shifter_2 (.in(Y), .\dist (shamt), .out(shifter_2_out));
  Shifter #(.width(32), .shift("lr")) shifter_3 (.in(Y), .\dist (shamt), .out(shifter_3_out));
  Multiplier #(.width(32)) multiplier_1 (.a(X), .b(Y), .out(multiplier_1_out), .cout(multiplier_1_cout));  // open: cin
  Divider #(.width(32)) divider_1 (.a(X), .b(Y), .out(divider_1_out), .rem(divider_1_rem));  // open: upper
  Adder #(.width(32)) adder_1 (.a(X), .b(Y), .out(adder_1_out));  // open: cin, cout
  Subtractor #(.width(32)) subtractor_1 (.a(X), .b(Y), .out(subtractor_1_out));  // open: bin, bout
  assign XOR_out = X ^ Y;  // XOR_Gate XOR, 32 bits wide
  assign NOR_out = ~(X | Y);  // NOR_Gate NOR, 32 bits wide
  Comparator #(.width(32)) comparator_1 (.a(X), .b(Y), .eq(Equal), .lt(comparator_1_lt[0]));  // open: gt
  Comparator #(.width(32), .mode("unsigned")) comparator_2 (.a(X), .b(Y), .lt(comparator_2_lt[0]));  // open: gt, eq
  Multiplexer #(.select(4), .width(32), .enable("false")) multiplexer_1 (
    .in0(shifter_1_out), .in1(shifter_2_out), .in2(shifter_3_out), .in3(multiplier_1_out),
    .in4(divider_1_out), .in5(adder_1_out), .in6(subtractor_1_out), .in7(AND_out), .in8(OR_out),
    .in9(XOR_out), .in10(NOR_out), .in11({{31{1'b0}}, comparator_1_lt[0]}),
    .in12({{31{1'b0}}, comparator_2_lt[0]}), .in13({32{1'b0}}), .in14({32{1'b0}}), .in15({32{1'b0}}),
    .out(Result), .sel(AluOP));
  Multiplexer #(.select(4), .width(32), .enable("false")) multiplexer_2 (
    .in0({32{1'b0}}), .in1({32{1'b0}}), .in2({32{1'b0}}), .in3(multiplier_1_cout), .in4(divider_1_rem),
    .in5({32{1'b0}}), .in6({32{1'b0}}), .in7({32{1'b0}}), .in8({32{1'b0}}), .in9({32{1'b0}}),
    .in10({32{1'b0}}), .in11({32{1'b0}}), .in12({32{1'b0}}), .in13({32{1'b0}}), .in14({32{1'b0}}),
    .in15({32{1'b0}}), .out(Result_2), .sel(AluOP));

  // Other names for the same wires on the sheet: Result2[31:0] = Result_2; S[3:0] = AluOP

  // Notes on the sheet:
  //   不要改变此引脚区域内容，也不要改变ALU封装形式
  //   输入引脚
  //   输出引脚
endmodule

module MIPS_Regifile (
  input  [31:0] Din,
  input  Clk,
  input  WE,
  input  [4:0] R1_num,
  input  [4:0] W_num,
  input  [4:0] R2_num,
  output [31:0] R1,
  output [31:0] R2
);

  // RegisterFile registerfile_1: pin names not known; wires that end beside it: Din, Clk, WE, W_num, R1_num, R2_num, R1, R2
endmodule

module \理想流水线  (
  output RegWrite,
  output MemWrite,
  output [31:0] IF_PC,
  output [31:0] ID_PC,
  output [31:0] EX_PC,
  output [31:0] M_PC,
  output [31:0] WB_PC,
  output [31:0] RDin,
  output [31:0] MDin,
  output [31:0] LedData
);

  wire AluSrc, and_1_out, and_2_out, and_3_out, and_4_out, and_5_out, and_6_out, and_7_out, Beq, Bne, CLK,
       clock_1_out, comparator_1_eq, comparator_1_lt, comparator_2_eq, counter_2_q, d_ff_1_q, Equal,
       ex_mem_1_halt_out, ex_mem_1_jal_out, ex_mem_1_memtoreg_out, ex_mem_1_regwrite_out, Go, Halt,
       id_ex_1_jal_out, id_ex_1_memtoreg_out, id_ex_1_memwrite_out, id_ex_1_regwrite_out, ID_JAL, IR1, IR2,
       IR3, JAL, JMP, JR, MemToReg, nand_1_out, not_1_out, not_2_out, not_3_out, not_4_out, not_5_out,
       not_6_out, not_7_out, or_1_out, or_2_out, RegDst, RST, SignedExt, Syscall, W1, W2, W3,
       \单周期硬布线控制器_1_alu_src , \单周期硬布线控制器_1_beq , \单周期硬布线控制器_1_bne , \单周期硬布线控制器_1_jmp , \单周期硬布线控制器_1_jr ,
       \单周期硬布线控制器_1_memtoreg , \单周期硬布线控制器_1_memwrite , \单周期硬布线控制器_1_regwrite , \单周期硬布线控制器_1_syscall ;
  wire [3:0] AluOP, \单周期硬布线控制器_1_alu_op ;
  wire [4:0] ex_mem_1_w__out, id_ex_1_shamt_out, id_ex_1_w__out, multiplexer_1_out, multiplexer_2_out,
       multiplexer_3_out, multiplexer_4_out, W_num;
  wire [12:0] CNT_num;
  wire [15:0] \LoadUse次数 , \总周期数 , \插入气泡数 , \无条件分支数 , \条件分支成功数 ;
  wire [31:0] adder_1_out, bit_extender_1_out, bit_extender_2_out, bit_extender_3_out, bit_extender_4_out,
       EX_IR, ex_mem_1_alu_out, ex_mem_1_pc_4_out, EX_PC_4, id_ex_1_a_out, id_ex_1_b_out, id_ex_1_imm_out,
       ID_IR, if_id_1_pc_4_out, IF_IR, \J跳转地址 , MEM_IR, mem_wb_1_alu_out, mem_wb_1_md_out, mips_alu_2_result,
       mips_alu_3_result, mips_regifile_1_r1, mips_regifile_1_r2, multiplexer_5_out, multiplexer_6_out,
       multiplexer_7_out, multiplexer_8_out, multiplexer_10_out, PC_4, PC_next, ram_1_data, shifter_1_out,
       shifter_2_out, shifter_3_out, WB_IR, WB_PC_4;

  Button \u_总复位  (.out(RST));
  Button _1 (.out(IR1));
  Button _2 (.out(IR2));
  Button _3 (.out(IR3));
  // Probe on \总周期数 
  // Probe on \总周期数 
  not not_1 (not_1_out, Halt);
  Button \u_继续运行  (.out(Go));
  LED led_1 (.in(W1));
  LED led_2 (.in(W2));
  LED led_3 (.in(W3));
  Register #(.width(32)) PC (.D(PC_next), .en(not_1_out), .Q(IF_PC), .clk(CLK), .clr(RST));
  Hex_Digit_Display hex_digit_display_1 (.value(LedData[31:28]));  // open: dp
  // Probe on IF_PC[19:0]
  // Mips_Probe mips_probe_1: pin names not known; wires that end beside it: IF_IR
  Hex_Digit_Display hex_digit_display_2 (.value(LedData[23:20]));  // open: dp
  Hex_Digit_Display hex_digit_display_3 (.value(LedData[27:24]));  // open: dp
  // Probe on ID_PC[19:0]
  // Mips_Probe mips_probe_2: pin names not known; wires that end beside it: ID_IR
  MIPS_ALU mips_alu_1 (.X(IF_PC), .Y(32'h4), .AluOP(4'b0101), .Result(PC_4));  // open: Equal, Result_2, shamt
  ROM #(.addrWidth(10), .dataWidth(32)) rom_1 (.addr(IF_PC[11:2]), .data(IF_IR));  // open: sel
  Hex_Digit_Display hex_digit_display_4 (.value(LedData[15:12]));  // open: dp
  Hex_Digit_Display hex_digit_display_5 (.value(LedData[19:16]));  // open: dp
  Hex_Digit_Display hex_digit_display_6 (.value(LedData[11:8]));  // open: dp
  Hex_Digit_Display hex_digit_display_7 (.value(LedData[7:4]));  // open: dp
  // Probe on EX_PC[19:0]
  // Mips_Probe mips_probe_3: pin names not known; wires that end beside it: EX_IR
  IF_ID if_id_1 (
    .IR_In(IF_IR), .CLK(CLK), .\异步清零 (RST), .\使能端_低电平有效 (Halt), .IR_Out(ID_IR), .PC_4_Out(if_id_1_pc_4_out),
    .PC_4_In(PC_4), .PC_In(IF_PC), .PC_Out(ID_PC));  // open: 同步清零, PJ_In, PJ_Out
  Hex_Digit_Display hex_digit_display_8 (.value(LedData[3:0]));  // open: dp
  Multiplexer #(.width(5), .enable("false")) multiplexer_1 (
    .in0(ID_IR[25:21]), .in1(5'b00010), .out(multiplexer_1_out), .sel(\单周期硬布线控制器_1_syscall ));
  Multiplexer #(.width(5), .enable("false")) multiplexer_2 (
    .in0(ID_IR[20:16]), .in1(5'b00100), .out(multiplexer_2_out), .sel(\单周期硬布线控制器_1_syscall ));
  Multiplexer #(.width(5), .enable("false")) multiplexer_3 (
    .in0(ID_IR[20:16]), .in1(ID_IR[15:11]), .out(multiplexer_3_out), .sel(RegDst));
  // Probe on \总周期数 
  // Probe on M_PC[19:0]
  // Mips_Probe mips_probe_4: pin names not known; wires that end beside it: MEM_IR
  \单周期硬布线控制器  \u_单周期硬布线控制器_1  (
    .Func(ID_IR[5:0]), .OP(ID_IR[31:26]), .ALU_OP(\单周期硬布线控制器_1_alu_op ), .MemToReg(\单周期硬布线控制器_1_memtoreg ),
    .MemWrite(\单周期硬布线控制器_1_memwrite ), .ALU_SRC(\单周期硬布线控制器_1_alu_src ), .RegWrite(\单周期硬布线控制器_1_regwrite ),
    .SysCALL(\单周期硬布线控制器_1_syscall ), .SignedExt(SignedExt), .RegDst(RegDst), .JR(\单周期硬布线控制器_1_jr ),
    .JMP(\单周期硬布线控制器_1_jmp ), .Beq(\单周期硬布线控制器_1_beq ), .JAL(ID_JAL), .Bne(\单周期硬布线控制器_1_bne ));
  Multiplexer #(.width(5), .enable("false")) multiplexer_4 (
    .in0(multiplexer_3_out), .in1({5{1'b1}}), .out(multiplexer_4_out), .sel(ID_JAL));
  assign bit_extender_1_out = {{16{1'b0}}, ID_IR[15:0]};  // Bit_Extender bit_extender_1
  assign bit_extender_2_out = {{16{ID_IR[15]}}, ID_IR[15:0]};  // Bit_Extender bit_extender_2
  assign bit_extender_3_out = {{6{1'b0}}, ID_IR[25:0]};  // Bit_Extender bit_extender_3
  Shifter #(.width(32)) shifter_1 (.in(bit_extender_3_out), .\dist (5'b00010), .out(shifter_1_out));
  Shifter #(.width(32)) shifter_2 (.in(bit_extender_4_out), .\dist (5'b11100), .out(shifter_2_out));
  assign bit_extender_4_out = {{28{1'b0}}, ID_PC[31:28]};  // Bit_Extender bit_extender_4
  // Probe on \总周期数 
  // Probe on \无条件分支数 
  // Probe on \条件分支成功数 
  // Probe on \插入气泡数 
  // Probe on \LoadUse次数 
  not not_2 (not_2_out, Halt);
  and and_1 (and_1_out, not_2_out, RegWrite);
  Multiplexer #(.width(32), .enable("false")) multiplexer_5 (
    .in0(bit_extender_1_out), .in1(bit_extender_2_out), .out(multiplexer_5_out), .sel(SignedExt));
  Adder #(.width(32)) adder_1 (.a(shifter_1_out), .b(shifter_2_out), .out(adder_1_out));  // open: cin, cout
  // Probe on IF_PC[11:0]
  // Probe on WB_PC[19:0]
  // Mips_Probe mips_probe_5: pin names not known; wires that end beside it: WB_IR
  MIPS_Regifile mips_regifile_1 (
    .Din(RDin), .Clk(CLK), .R1(mips_regifile_1_r1), .R2(mips_regifile_1_r2), .WE(and_1_out), .W_num(W_num),
    .R1_num(multiplexer_1_out), .R2_num(multiplexer_2_out));
  // Probe on ID_PC[11:0]
  // Probe on EX_PC[11:0]
  ID_EX id_ex_1 (
    .IR_In(ID_IR), .MemToReg_In(\单周期硬布线控制器_1_memtoreg ), .RegWrite_In(\单周期硬布线控制器_1_regwrite ),
    .PC_4_In(if_id_1_pc_4_out), .MemWrite_In(\单周期硬布线控制器_1_memwrite ), .AluOP_In(\单周期硬布线控制器_1_alu_op ),
    .A_In(mips_regifile_1_r1), .AluSrcB_In(\单周期硬布线控制器_1_alu_src ), .B_In(mips_regifile_1_r2),
    .Beq_In(\单周期硬布线控制器_1_beq ), .Bne_In(\单周期硬布线控制器_1_bne ), .Imm_In(multiplexer_5_out),
    .JR_In(\单周期硬布线控制器_1_jr ), .JMP_In(\单周期硬布线控制器_1_jmp ), .JAL_In(ID_JAL),
    .SysCall_In(\单周期硬布线控制器_1_syscall ), .CLK(CLK), .\异步清零 (RST), .\使能端_低电平有效 (Halt), .IR_Out(EX_IR),
    .MemToReg_Out(id_ex_1_memtoreg_out), .RegWrite_Out(id_ex_1_regwrite_out), .PC_4_Out(EX_PC_4),
    .MemWrite_Out(id_ex_1_memwrite_out), .AluOP_Out(AluOP), .A_Out(id_ex_1_a_out), .AluSrcB_Out(AluSrc),
    .B_Out(id_ex_1_b_out), .Beq_Out(Beq), .Bne_Out(Bne), .Imm_Out(id_ex_1_imm_out), .JR_Out(JR),
    .JMP_Out(JMP), .JAL_Out(id_ex_1_jal_out), .SysCall_Out(Syscall), .Shamt_In(ID_IR[10:6]),
    .Shamt_Out(id_ex_1_shamt_out), .W__In(multiplexer_4_out), .W__Out(id_ex_1_w__out), .PC_In(ID_PC),
    .PC_Out(EX_PC), .J_In(adder_1_out), .J_Out(\J跳转地址 ));  // open: 同步清零, Forward2_In, Forward2_Out, Forward1_In, Forward1_Out, PJ_eret_In, PJ_eret_Out
  // Probe on M_PC[11:0]
  D_Flip_Flop #(.trigger("high")) d_ff_1 (.Q(d_ff_1_q));  // open: clk, D, Qn, preset, en, reset
  // Probe on 13'hc
  // Probe on WB_PC[11:0]
  Comparator #(.width(13)) comparator_1 (
    .a(CNT_num), .b(13'hc), .eq(comparator_1_eq), .lt(comparator_1_lt));  // open: gt
  Clock clock_1 (.out(clock_1_out));
  Multiplexer #(.width(32), .enable("false")) multiplexer_6 (
    .in0(id_ex_1_b_out), .in1(id_ex_1_imm_out), .out(multiplexer_6_out), .sel(AluSrc));
  Shifter #(.width(32)) shifter_3 (.in(id_ex_1_imm_out), .\dist (5'b00010), .out(shifter_3_out));
  and and_2 (and_2_out, Equal, Beq);
  not not_3 (not_3_out, Equal);
  and and_3 (and_3_out, not_3_out, Bne);
  Comparator #(.width(32)) comparator_2 (.a(id_ex_1_a_out), .b(32'h22), .eq(comparator_2_eq));  // open: gt, lt
  nand nand_1 (nand_1_out, d_ff_1_q, comparator_1_eq);
  Counter #(.width(13), .max('h1fff), .ongoal("stay")) counter_1 (
    .count(comparator_1_lt), .Q(CNT_num), .clk(clock_1_out));  // open: load, D, carry, clr
  MIPS_ALU mips_alu_2 (
    .X(id_ex_1_a_out), .Y(multiplexer_6_out), .AluOP(AluOP), .Equal(Equal), .Result(mips_alu_2_result),
    .shamt(id_ex_1_shamt_out));  // open: Result_2
  MIPS_ALU mips_alu_3 (
    .X(EX_PC_4), .Y(shifter_3_out), .AluOP(4'b0101), .Result(mips_alu_3_result));  // open: Equal, Result_2, shamt
  or or_1 (or_1_out, and_2_out, and_3_out);
  and and_4 (and_4_out, Syscall, not_4_out);
  not not_4 (not_4_out, comparator_2_eq);
  and and_5 (and_5_out, Syscall, comparator_2_eq);
  assign CLK = nand_1_out ? clock_1_out : 1'bz;  // Controlled_Buffer controlled_buffer_1
  Multiplexer #(.width(32), .enable("false")) multiplexer_7 (
    .in0(PC_4), .in1(mips_alu_3_result), .out(multiplexer_7_out), .sel(or_1_out));
  Counter #(.width(1), .max('h1)) counter_2 (
    .load(and_4_out), .D(and_4_out), .count(1'b0), .Q(counter_2_q), .clk(CLK), .clr(or_2_out));  // open: carry
  or or_2 (or_2_out, Go, RST);
  Register #(.width(32)) register_1 (.D(id_ex_1_b_out), .en(and_5_out), .Q(LedData), .clk(CLK), .clr(RST));
  Pull_Resistor #(.pull(1)) pull_resistor_1 (.node(CLK));
  Multiplexer #(.width(32), .enable("false")) multiplexer_8 (
    .in0(multiplexer_7_out), .in1(id_ex_1_a_out), .out(multiplexer_8_out), .sel(JR));
  Multiplexer #(.width(32), .enable("false")) multiplexer_9 (
    .in0(multiplexer_8_out), .in1(\J跳转地址 ), .out(PC_next), .sel(and_6_out));
  and and_6 (and_6_out, JMP, not_5_out);
  EX_MEM ex_mem_1 (
    .IR_In(EX_IR), .MemToReg_In(id_ex_1_memtoreg_out), .RegWrite_In(id_ex_1_regwrite_out), .PC_4_In(EX_PC_4),
    .MemWrite_In(id_ex_1_memwrite_out), .B_In(id_ex_1_b_out), .ALU_In(mips_alu_2_result), .CLK(CLK),
    .\异步清零 (RST), .\使能端_低电平有效 (Halt), .IR_Out(MEM_IR), .MemToReg_Out(ex_mem_1_memtoreg_out),
    .RegWrite_Out(ex_mem_1_regwrite_out), .PC_4_Out(ex_mem_1_pc_4_out), .MemWrite_Out(MemWrite),
    .B_Out(MDin), .ALU_Out(ex_mem_1_alu_out), .JAL_In(id_ex_1_jal_out), .JAL_Out(ex_mem_1_jal_out),
    .Halt_In(counter_2_q), .Halt_Out(ex_mem_1_halt_out), .W__In(id_ex_1_w__out), .W__Out(ex_mem_1_w__out),
    .PC_In(EX_PC), .PC_Out(M_PC));  // open: 同步清零, eret_In, PJ_eret_Out
  not not_5 (not_5_out, JR);
  and and_7 (and_7_out, CLK, not_6_out);
  not not_6 (not_6_out, Halt);
  Counter #(.width(16), .max('hffff)) counter_3 (
    .Q(\总周期数 ), .clk(and_7_out), .clr(RST));  // open: load, D, count, carry
  not not_7 (not_7_out, Halt);
  RAM #(.addrWidth(10), .dataWidth(32), .bus("separate")) ram_1 (
    .addr(ex_mem_1_alu_out[11:2]), .din(MDin), .data(ram_1_data), .str(MemWrite), .sel(not_7_out), .clk(CLK),
    .clr(RST));  // open: ld
  MEM_WB mem_wb_1 (
    .IR_In(MEM_IR), .MemToReg_In(ex_mem_1_memtoreg_out), .PC_4_In(ex_mem_1_pc_4_out),
    .ALU_In(ex_mem_1_alu_out), .MD_In(ram_1_data), .CLK(CLK), .\异步清零 (RST), .\使能端_低电平有效 (Halt),
    .IR_Out(WB_IR), .MemToReg_Out(MemToReg), .PC_4_Out(WB_PC_4), .ALU_Out(mem_wb_1_alu_out),
    .MD_Out(mem_wb_1_md_out), .RegWrite_In(ex_mem_1_regwrite_out), .RegWrite_Out(RegWrite),
    .JAL_In(ex_mem_1_jal_out), .JAL_Out(JAL), .Halt_In(ex_mem_1_halt_out), .Halt_Out(Halt),
    .W__In(ex_mem_1_w__out), .W__Out(W_num), .PC_In(M_PC), .PC_Out(WB_PC));  // open: 同步清零, eret_In, eret_Out
  Multiplexer #(.width(32), .enable("false")) multiplexer_10 (
    .in0(mem_wb_1_alu_out), .in1(mem_wb_1_md_out), .out(multiplexer_10_out), .sel(MemToReg));
  Multiplexer #(.width(32), .enable("false")) multiplexer_11 (
    .in0(multiplexer_10_out), .in1(WB_PC_4), .out(RDin), .sel(JAL));

  // Other names for the same wires on the sheet: MEM_PC[31:0] = M_PC

  // Notes on the sheet:
  //   中断源
  //   时空图监测，可删除
  //   中断等待指示
  //   contents of rom_1 (hex, n*v repeats v):
  //   20100000 20110000 20120000 20130000 36100000 36310001 36520002 36730003 ae100000 ae110004 ae120008
  //   ae13000c 2002000a 20110000 20120000 20130000 c
  //   数码管输出
  //   OP
  //   Func
  //   rs
  //   rt
  //   rd
  //   shamt
  //   立即数I
  //   立即数J
  //   控制位
  //   流水调试日志用
  //   暂停节拍，不能为0
  //   可计数暂停的时钟源
  //   为方便自动评测，需要输出流水线各段保存的PC值，注意是PC不是PC+4，另外ID段寄存器写入信息，Mem段内存写入信息也要输出
endmodule

module \气泡流水线  (
  output RegWrite,
  output MemWrite,
  output [31:0] IF_PC,
  output [31:0] ID_PC,
  output [31:0] EX_PC,
  output [31:0] M_PC,
  output [31:0] WB_PC,
  output [31:0] RDin,
  output [31:0] MDin,
  output [31:0] LedData
);

  wire AluSrc, and_1_out, and_2_out, and_3_out, and_4_out, and_5_out, and_6_out, and_8_out, and_9_out,
       and_10_out, and_11_out, and_12_out, B, Beq, Blez, Bne, CLK, clock_1_out, comparator_3_eq,
       comparator_3_lt, comparator_4_eq, comparator_5_eq, comparator_6_gt, comparator_7_eq, counter_2_q,
       d_ff_1_q, Equal, ex_mem_1_halt_out, ex_mem_1_jal_out, ex_mem_1_memtoreg_out, EX_RegWrite, Go, Halt,
       id_ex_1_jal_out, id_ex_1_memtoreg_out, id_ex_1_memwrite_out, ID_JAL, IR1, IR2, IR3, JAL, JMP, JR,
       MEM_RegWrite, MemToReg, nand_1_out, not_1_out, not_2_out, not_3_out, not_4_out, not_5_out, not_6_out,
       not_7_out, not_8_out, not_9_out, not_10_out, not_11_out, not_12_out, or_1_out, or_2_out, or_3_out,
       or_5_out, Pause, R1_Used, R2_Used, RegDst, RST, SignedExt, SLLV, SRLV, Syscall, W1, W2, W3,
       \单周期硬布线控制器_1_alu_src , \单周期硬布线控制器_1_beq , \单周期硬布线控制器_1_bne , \单周期硬布线控制器_1_jmp , \单周期硬布线控制器_1_jr ,
       \单周期硬布线控制器_1_memtoreg , \单周期硬布线控制器_1_memwrite , \单周期硬布线控制器_1_regwrite , \单周期硬布线控制器_1_syscall , \气泡 ;
  wire [3:0] AluOP, \单周期硬布线控制器_1_alu_op ;
  wire [4:0] EX_WriteReg_num, id_ex_1_shamt_out, MEM_WriteReg_num, mips_regifile_1_r1, multiplexer_3_out,
       multiplexer_4_out, multiplexer_6_out, R1_num, R2_num, W_num;
  wire [5:0] Func;
  wire [12:0] CNT_num;
  wire [15:0] \LoadUse次数 , \总周期数 , \插入气泡数 , \无条件分支数 , \条件分支成功数 ;
  wire [31:0] adder_1_out, bit_extender_1_out, bit_extender_2_out, bit_extender_3_out, bit_extender_4_out,
       EX_IR, ex_mem_1_alu_out, ex_mem_1_b_out, ex_mem_1_pc_4_out, EX_PC_4, id_ex_1_a_out, id_ex_1_b_out,
       id_ex_1_imm_out, if_id_1_pc_4_out, IF_IR, \J跳转地址 , MDout, MEM_IR, mem_wb_1_alu_out, mem_wb_1_md_out,
       mips_alu_2_result, mips_alu_3_result, mips_regifile_1_r2, multiplexer_5_out, multiplexer_7_out,
       multiplexer_8_out, multiplexer_9_out, multiplexer_12_out, PC_4, PC_next, shifter_1_out, shifter_2_out,
       shifter_3_out, WB_IR, WB_PC_4;
  wire [31:5] mips_regifile_1_r1_2;
  wire [31:6] ID_IR;

  Button \u_总复位  (.out(RST));
  Button _1 (.out(IR1));
  Button _2 (.out(IR2));
  Button _3 (.out(IR3));
  // Probe on \总周期数 
  // Probe on \总周期数 
  and and_1 (and_1_out, not_1_out, not_2_out);
  not not_1 (not_1_out, Halt);
  not not_2 (not_2_out, Pause);
  Button \u_继续运行  (.out(Go));
  LED led_1 (.in(W1));
  LED led_2 (.in(W2));
  LED led_3 (.in(W3));
  Register #(.width(32)) PC (.D(PC_next), .en(and_1_out), .Q(IF_PC), .clk(CLK), .clr(RST));
  Hex_Digit_Display hex_digit_display_1 (.value(LedData[31:28]));  // open: dp
  // Probe on IF_PC[19:0]
  // Mips_Probe mips_probe_1: pin names not known; wires that end beside it: IF_IR
  \源寄存器使用情况  \u_源寄存器使用情况_1  (
    .OP0(ID_IR[26]), .OP1(ID_IR[27]), .OP2(ID_IR[28]), .OP3(ID_IR[29]), .OP4(ID_IR[30]), .OP5(ID_IR[31]),
    .F0(Func[0]), .F1(Func[1]), .F2(Func[2]), .F3(Func[3]), .F4(Func[4]), .F5(Func[5]), .R1_Used(R1_Used),
    .R2_Used(R2_Used));
  \数据相关检测  \u_数据相关检测_1  (
    .R1_Used(R1_Used), .R2_Used(R2_Used), .EX_RegWrite(EX_RegWrite), .MEM_RegWrite(MEM_RegWrite),
    .R1_num(R1_num), .R2_num(R2_num), .EX_WriteReg_num(EX_WriteReg_num), .MEM_WriteReg_num(MEM_WriteReg_num),
    .Pause(Pause));
  Hex_Digit_Display hex_digit_display_2 (.value(LedData[23:20]));  // open: dp
  Hex_Digit_Display hex_digit_display_3 (.value(LedData[27:24]));  // open: dp
  // Probe on ID_PC[19:0]
  // Mips_Probe mips_probe_2: pin names not known; wires that end beside it: {ID_IR, Func}
  MIPS_ALU mips_alu_1 (.X(IF_PC), .Y(32'h4), .AluOP(4'b0101), .Result(PC_4));  // open: Equal, Result_2, shamt
  ROM #(.addrWidth(10), .dataWidth(32)) rom_1 (.addr(IF_PC[11:2]), .data(IF_IR));  // open: sel
  Hex_Digit_Display hex_digit_display_4 (.value(LedData[19:16]));  // open: dp
  Hex_Digit_Display hex_digit_display_5 (.value(LedData[15:12]));  // open: dp
  or or_1 (or_1_out, Halt, Pause);
  Hex_Digit_Display hex_digit_display_6 (.value(LedData[11:8]));  // open: dp
  Hex_Digit_Display hex_digit_display_7 (.value(LedData[7:4]));  // open: dp
  // Probe on EX_PC[19:0]
  // Mips_Probe mips_probe_3: pin names not known; wires that end beside it: EX_IR
  IF_ID if_id_1 (
    .IR_In(IF_IR), .CLK(CLK), .\异步清零 (RST), .\使能端_低电平有效 (or_1_out), .IR_Out({ID_IR, Func}),
    .PC_4_Out(if_id_1_pc_4_out), .PC_4_In(PC_4), .PC_In(IF_PC), .PC_Out(ID_PC), .\同步清零 (\气泡 ));  // open: PJ_In, PJ_Out
  Hex_Digit_Display hex_digit_display_8 (.value(LedData[3:0]));  // open: dp
  Multiplexer #(.width(5), .enable("false")) multiplexer_1 (
    .in0(ID_IR[25:21]), .in1(5'b00010), .out(R1_num), .sel(\单周期硬布线控制器_1_syscall ));
  Multiplexer #(.width(5), .enable("false")) multiplexer_2 (
    .in0(ID_IR[20:16]), .in1(5'b00100), .out(R2_num), .sel(\单周期硬布线控制器_1_syscall ));
  Multiplexer #(.width(5), .enable("false")) multiplexer_3 (
    .in0(ID_IR[20:16]), .in1(ID_IR[15:11]), .out(multiplexer_3_out), .sel(RegDst));
  Comparator #(.width(6)) comparator_1 (.a(Func), .b(6'b000100), .eq(SLLV));  // open: gt, lt
  Comparator #(.width(6)) comparator_2 (.a(Func), .b(6'b000110), .eq(SRLV));  // open: gt, lt
  // Probe on \总周期数 
  // Probe on M_PC[19:0]
  // Mips_Probe mips_probe_4: pin names not known; wires that end beside it: MEM_IR
  \单周期硬布线控制器  \u_单周期硬布线控制器_1  (
    .Func(Func), .OP(ID_IR[31:26]), .ALU_OP(\单周期硬布线控制器_1_alu_op ), .MemToReg(\单周期硬布线控制器_1_memtoreg ),
    .MemWrite(\单周期硬布线控制器_1_memwrite ), .ALU_SRC(\单周期硬布线控制器_1_alu_src ), .RegWrite(\单周期硬布线控制器_1_regwrite ),
    .SysCALL(\单周期硬布线控制器_1_syscall ), .SignedExt(SignedExt), .RegDst(RegDst), .JR(\单周期硬布线控制器_1_jr ),
    .JMP(\单周期硬布线控制器_1_jmp ), .Beq(\单周期硬布线控制器_1_beq ), .JAL(ID_JAL), .Bne(\单周期硬布线控制器_1_bne ));
  Multiplexer #(.width(5), .enable("false")) multiplexer_4 (
    .in0(multiplexer_3_out), .in1({5{1'b1}}), .out(multiplexer_4_out), .sel(ID_JAL));
  or or_2 (or_2_out, SLLV, SRLV);
  assign bit_extender_1_out = {{16{1'b0}}, {ID_IR[15:6], Func}};  // Bit_Extender bit_extender_1
  assign bit_extender_2_out = {{16{ID_IR[15]}}, {ID_IR[15:6], Func}};  // Bit_Extender bit_extender_2
  Shifter #(.width(32)) shifter_1 (.in(bit_extender_3_out), .\dist (5'b00010), .out(shifter_1_out));
  assign bit_extender_3_out = {{6{1'b0}}, {ID_IR[25:6], Func}};  // Bit_Extender bit_extender_3
  assign bit_extender_4_out = {{28{1'b0}}, ID_PC[31:28]};  // Bit_Extender bit_extender_4
  Shifter #(.width(32)) shifter_2 (.in(bit_extender_4_out), .\dist (5'b11100), .out(shifter_2_out));
  // Probe on \总周期数 
  // Probe on \无条件分支数 
  // Probe on \条件分支成功数 
  // Probe on \插入气泡数 
  // Probe on \LoadUse次数 
  not not_3 (not_3_out, Halt);
  and and_2 (and_2_out, not_3_out, RegWrite);
  Multiplexer #(.width(32), .enable("false")) multiplexer_5 (
    .in0(bit_extender_1_out), .in1(bit_extender_2_out), .out(multiplexer_5_out), .sel(SignedExt));
  Adder #(.width(32)) adder_1 (.a(shifter_1_out), .b(shifter_2_out), .out(adder_1_out));  // open: cin, cout
  // Probe on IF_PC[11:0]
  // Probe on WB_PC[19:0]
  // Mips_Probe mips_probe_5: pin names not known; wires that end beside it: WB_IR
  MIPS_Regifile mips_regifile_1 (
    .Din(RDin), .Clk(CLK), .R1({mips_regifile_1_r1_2, mips_regifile_1_r1}), .R2(mips_regifile_1_r2),
    .WE(and_2_out), .W_num(W_num), .R1_num(R1_num), .R2_num(R2_num));
  Multiplexer #(.width(5), .enable("false")) multiplexer_6 (
    .in0(ID_IR[10:6]), .in1(mips_regifile_1_r1), .out(multiplexer_6_out), .sel(or_2_out));
  // Probe on EX_PC[11:0]
  // Probe on ID_PC[11:0]
  ID_EX id_ex_1 (
    .IR_In({ID_IR, Func}), .MemToReg_In(\单周期硬布线控制器_1_memtoreg ), .RegWrite_In(\单周期硬布线控制器_1_regwrite ),
    .PC_4_In(if_id_1_pc_4_out), .MemWrite_In(\单周期硬布线控制器_1_memwrite ), .AluOP_In(\单周期硬布线控制器_1_alu_op ),
    .A_In({mips_regifile_1_r1_2, mips_regifile_1_r1}), .AluSrcB_In(\单周期硬布线控制器_1_alu_src ),
    .B_In(mips_regifile_1_r2), .Beq_In(\单周期硬布线控制器_1_beq ), .Bne_In(\单周期硬布线控制器_1_bne ),
    .Imm_In(multiplexer_5_out), .JR_In(\单周期硬布线控制器_1_jr ), .JMP_In(\单周期硬布线控制器_1_jmp ), .JAL_In(ID_JAL),
    .SysCall_In(\单周期硬布线控制器_1_syscall ), .CLK(CLK), .\异步清零 (RST), .\使能端_低电平有效 (Halt), .IR_Out(EX_IR),
    .MemToReg_Out(id_ex_1_memtoreg_out), .RegWrite_Out(EX_RegWrite), .PC_4_Out(EX_PC_4),
    .MemWrite_Out(id_ex_1_memwrite_out), .AluOP_Out(AluOP), .A_Out(id_ex_1_a_out), .AluSrcB_Out(AluSrc),
    .B_Out(id_ex_1_b_out), .Beq_Out(Beq), .Bne_Out(Bne), .Imm_Out(id_ex_1_imm_out), .JR_Out(JR),
    .JMP_Out(JMP), .JAL_Out(id_ex_1_jal_out), .SysCall_Out(Syscall), .Shamt_In(multiplexer_6_out),
    .Shamt_Out(id_ex_1_shamt_out), .W__In(multiplexer_4_out), .W__Out(EX_WriteReg_num), .PC_In(ID_PC),
    .PC_Out(EX_PC), .\同步清零 (or_3_out), .J_In(adder_1_out), .J_Out(\J跳转地址 ));  // open: Forward2_In, Forward2_Out, Forward1_In, Forward1_Out, PJ_eret_In, PJ_eret_Out
  or or_3 (or_3_out, \气泡 , Pause);
  // Probe on nothing
  // Probe on M_PC[11:0]
  D_Flip_Flop #(.trigger("high")) d_ff_1 (.Q(d_ff_1_q));  // open: clk, D, Qn, preset, en, reset
  // Probe on 13'h190
  // Probe on WB_PC[11:0]
  Comparator #(.width(13)) comparator_3 (
    .a(CNT_num), .b(13'h190), .eq(comparator_3_eq), .lt(comparator_3_lt));  // open: gt
  Clock clock_1 (.out(clock_1_out));
  Multiplexer #(.width(32), .enable("false")) multiplexer_7 (
    .in0(id_ex_1_b_out), .in1(id_ex_1_imm_out), .out(multiplexer_7_out), .sel(AluSrc));
  Shifter #(.width(32)) shifter_3 (.in(id_ex_1_imm_out), .\dist (5'b00010), .out(shifter_3_out));
  and and_3 (and_3_out, Equal, Beq);
  not not_4 (not_4_out, Equal);
  and and_4 (and_4_out, not_4_out, Bne);
  Comparator #(.width(32)) comparator_4 (.a(id_ex_1_a_out), .b(32'h22), .eq(comparator_4_eq));  // open: gt, lt
  nand nand_1 (nand_1_out, d_ff_1_q, comparator_3_eq);
  Counter #(.width(13), .max('h1fff), .ongoal("stay")) counter_1 (
    .count(comparator_3_lt), .Q(CNT_num), .clk(clock_1_out));  // open: load, D, carry, clr
  MIPS_ALU mips_alu_2 (
    .X(id_ex_1_a_out), .Y(multiplexer_7_out), .AluOP(AluOP), .Equal(Equal), .Result(mips_alu_2_result),
    .shamt(id_ex_1_shamt_out));  // open: Result_2
  MIPS_ALU mips_alu_3 (
    .X(EX_PC_4), .Y(shifter_3_out), .AluOP(4'b0101), .Result(mips_alu_3_result));  // open: Equal, Result_2, shamt
  or or_4 (B, and_3_out, Blez, and_4_out);
  and and_5 (and_5_out, Syscall, not_5_out);
  not not_5 (not_5_out, comparator_4_eq);
  and and_6 (and_6_out, Syscall, comparator_4_eq);
  Comparator #(.width(6)) comparator_5 (.a(EX_IR[31:26]), .b(6'b000110), .eq(comparator_5_eq));  // open: gt, lt
  and and_7 (Blez, comparator_5_eq, not_6_out);
  not not_6 (not_6_out, comparator_6_gt);
  Comparator #(.width(32)) comparator_6 (.a(id_ex_1_a_out), .b({32{1'b0}}), .gt(comparator_6_gt));  // open: eq, lt
  assign CLK = nand_1_out ? clock_1_out : 1'bz;  // Controlled_Buffer controlled_buffer_1
  Multiplexer #(.width(32), .enable("false")) multiplexer_8 (
    .in0(PC_4), .in1(mips_alu_3_result), .out(multiplexer_8_out), .sel(B));
  Counter #(.width(1), .max('h1)) counter_2 (
    .load(and_5_out), .D(and_5_out), .count(1'b0), .Q(counter_2_q), .clk(CLK), .clr(or_5_out));  // open: carry
  or or_5 (or_5_out, Go, RST);
  Register #(.width(32)) register_1 (.D(id_ex_1_b_out), .en(and_6_out), .Q(LedData), .clk(CLK), .clr(RST));
  Pull_Resistor #(.pull(1)) pull_resistor_1 (.node(CLK));
  Multiplexer #(.width(32), .enable("false")) multiplexer_9 (
    .in0(multiplexer_8_out), .in1(id_ex_1_a_out), .out(multiplexer_9_out), .sel(JR));
  Multiplexer #(.width(32), .enable("false")) multiplexer_10 (
    .in0(multiplexer_9_out), .in1(\J跳转地址 ), .out(PC_next), .sel(and_8_out));
  and and_8 (and_8_out, JMP, not_7_out);
  or or_6 (\气泡 , B, JMP);
  EX_MEM ex_mem_1 (
    .IR_In(EX_IR), .MemToReg_In(id_ex_1_memtoreg_out), .RegWrite_In(EX_RegWrite), .PC_4_In(EX_PC_4),
    .MemWrite_In(id_ex_1_memwrite_out), .B_In(id_ex_1_b_out), .ALU_In(mips_alu_2_result), .CLK(CLK),
    .\异步清零 (RST), .\使能端_低电平有效 (Halt), .IR_Out(MEM_IR), .MemToReg_Out(ex_mem_1_memtoreg_out),
    .RegWrite_Out(MEM_RegWrite), .PC_4_Out(ex_mem_1_pc_4_out), .MemWrite_Out(MemWrite),
    .B_Out(ex_mem_1_b_out), .ALU_Out(ex_mem_1_alu_out), .JAL_In(id_ex_1_jal_out), .JAL_Out(ex_mem_1_jal_out),
    .Halt_In(counter_2_q), .Halt_Out(ex_mem_1_halt_out), .W__In(EX_WriteReg_num), .W__Out(MEM_WriteReg_num),
    .PC_In(EX_PC), .PC_Out(M_PC));  // open: 同步清零, eret_In, PJ_eret_Out
  not not_7 (not_7_out, JR);
  and and_9 (and_9_out, CLK, not_8_out);
  not not_8 (not_8_out, Halt);
  Counter #(.width(16), .max('hffff)) counter_3 (
    .Q(\总周期数 ), .clk(and_9_out), .clr(RST));  // open: load, D, count, carry
  not not_9 (not_9_out, Halt);
  Comparator #(.width(6)) comparator_7 (.a(MEM_IR[31:26]), .b(6'b101001), .eq(comparator_7_eq));  // open: gt, lt
  RAM #(.addrWidth(10), .dataWidth(32), .bus("separate")) ram_1 (
    .addr(ex_mem_1_alu_out[11:2]), .din(MDin), .data(MDout), .str(MemWrite), .sel(not_9_out), .clk(CLK),
    .clr(RST));  // open: ld
  Multiplexer #(.width(32), .enable("false")) multiplexer_11 (
    .in0(ex_mem_1_b_out), .in1({MDout[31:16], ex_mem_1_b_out[15:0]}), .out(MDin), .sel(comparator_7_eq));
  and and_10 (and_10_out, CLK, not_10_out);
  not not_10 (not_10_out, Halt);
  MEM_WB mem_wb_1 (
    .IR_In(MEM_IR), .MemToReg_In(ex_mem_1_memtoreg_out), .PC_4_In(ex_mem_1_pc_4_out),
    .ALU_In(ex_mem_1_alu_out), .MD_In(MDout), .CLK(CLK), .\异步清零 (RST), .\使能端_低电平有效 (Halt), .IR_Out(WB_IR),
    .MemToReg_Out(MemToReg), .PC_4_Out(WB_PC_4), .ALU_Out(mem_wb_1_alu_out), .MD_Out(mem_wb_1_md_out),
    .RegWrite_In(MEM_RegWrite), .RegWrite_Out(RegWrite), .JAL_In(ex_mem_1_jal_out), .JAL_Out(JAL),
    .Halt_In(ex_mem_1_halt_out), .Halt_Out(Halt), .W__In(MEM_WriteReg_num), .W__Out(W_num), .PC_In(M_PC),
    .PC_Out(WB_PC));  // open: 同步清零, eret_In, eret_Out
  Counter #(.width(16), .max('hffff)) counter_4 (
    .count(JMP), .Q(\无条件分支数 ), .clk(and_10_out), .clr(RST));  // open: load, D, carry
  Multiplexer #(.width(32), .enable("false")) multiplexer_12 (
    .in0(mem_wb_1_alu_out), .in1(mem_wb_1_md_out), .out(multiplexer_12_out), .sel(MemToReg));
  and and_11 (and_11_out, CLK, not_11_out);
  not not_11 (not_11_out, Halt);
  Multiplexer #(.width(32), .enable("false")) multiplexer_13 (
    .in0(multiplexer_12_out), .in1(WB_PC_4), .out(RDin), .sel(JAL));
  Counter #(.width(16), .max('hffff)) counter_5 (
    .count(B), .Q(\条件分支成功数 ), .clk(and_11_out), .clr(RST));  // open: load, D, carry
  and and_12 (and_12_out, CLK, not_12_out);
  not not_12 (not_12_out, Halt);
  Counter #(.width(16), .max('hffff)) counter_6 (
    .count(Pause), .Q(\插入气泡数 ), .clk(and_12_out), .clr(RST));  // open: load, D, carry

  // Other names for the same wires on the sheet: ID_IR[5:0] = Func; OP[5:0] = ID_IR[31:26]; MEM_PC[31:0] = M_PC

  // Notes on the sheet:
  //   中断源
  //   时空图监测，可删除
  //   中断等待指示
  //   contents of rom_1 (hex, n*v repeats v):
  //   20110001 8000c05 20110001 20120002 20130003 8000c09 20110001 20120002 20130003 8000c0d 20110001
  //   20120002 20130003 8000c11 20110001 20120002 20130003 c000cb8 20100001 20110001 118fc0 112020
  //   20020022 c 118882 12200001 8000c15 112020 20020022 c 20110001 118880 112020 20020022 c 12200001
  //   8000c1f 20110001 118fc0 112020 20020022 c 1188c3 112020 20020022 c 118903 112020 20020022 c 118903
  //   112020 20020022 c 118903 112020 20020022 c 118903 112020 20020022 c 118903 112020 20020022 c 118903
  //   112020 20020022 c 118903 112020 20020022 c 20100001 109fc0 139fc3 8021 2012000c 24160003 26100001
  //   3210000f 20080008 20090001 139900 2709825 132020 20020022 c 1094022 1500fff9 22100001 2018000f
  //   2188024 108700 20080008 20090001 139902 2709825 132021 20020022 c 1094022 1500fff9 108702 2c9b022
  //   12c00001 8000c50 4020 1084027 84400 3508ffff 82021 20020022 c 2010ffff 20110000 ae300000 22100001
  //   22310004 ae300000 22100001 22310004 ae300000 22100001 22310004 ae300000 22100001 22310004 ae300000
  //   22100001 22310004 ae300000 22100001 22310004 ae300000 22100001 22310004 ae300000 22100001 22310004
  //   ae300000 22100001 22310004 ae300000 22100001 22310004 ae300000 22100001 22310004 ae300000 22100001
  //   22310004 ae300000 22100001 22310004 ae300000 22100001 22310004 ae300000 22100001 22310004 ae300000
  //   22100001 22310004 22100001 8020 2011003c 8e130000 8e340000 274402a 11000002 ae330000 ae140000
  //   2231fffc 1611fff8 102020 20020022 c 22100004 2011003c 1611fff2 20020032 c 20100000 22100001 102020
  //   20020022 c 22100002 102020 20020022 c 22100003 102020 20020022 c 22100004 102020 20020022 c 22100005
  //   102020 20020022 c 22100006 102020 20020022 c 22100007 102020 20020022 c 22100008 102020 20020022
  //   20020022 c 3e00008
  //   数码管输出
  //   OP
  //   Func
  //   rs
  //   rt
  //   rd
  //   shamt
  //   立即数I
  //   立即数J
  //   控制位
  //   流水调试日志用
  //   暂停节拍，不能为0
  //   可计数暂停的时钟源
  //   为方便自动评测，需要输出流水线各段保存的PC值，注意是PC不是PC+4，另外ID段寄存器写入信息，Mem段内存写入信息也要输出
endmodule

module \单周期MIPS_单级中断  (
  input  IR1,
  input  IR2,
  input  IR3,
  output RegWrite,
  output MemWrite,
  output [31:0] PC,
  output [31:0] IR,
  output [31:0] RDin,
  output [31:0] MDin,
  output [31:0] LedData
);

  wire _1_out, _2_out, _3_out, and_1_out, and_2_out, and_3_out, and_5_out, and_6_out, and_7_out, and_8_out,
       and_10_out, and_11_out, and_12_out, B, BLEZ, CLK, clock_2_out, clock_3_out, clock_4_out,
       comparator_3_eq, comparator_5_eq, comparator_6_gt, comparator_7_eq, comparator_8_eq, comparator_9_eq,
       comparator_10_eq, comparator_12_eq, d_ff_1_q, d_ff_2_q, d_ff_3_q, eret, Go, Halt, IE, IR1_2_q,
       IR1_3_q, IR1_q, IR1_RST, IR1_t, IR2_RST, IR2_t, IR3_RST, IR3_t, IRA, IRB, IRC, JAL, JMP, JR,
       mips_alu_3_equal, not_1_out, not_2_out, not_3_out, not_4_out, not_5_out, not_6_out, not_7_out,
       not_8_out, not_9_out, or_4_out, or_5_out, or_6_out, or_7_out, or_8_out, or_11_out, or_14_out,
       priority_encoder_1_gs, RegDst, RST, SH, SignedExt, SLLV, SRLV, Syscall, W1, W2, W3, \中断 ,
       \单周期硬布线控制器_1_alu_src , \单周期硬布线控制器_1_beq , \单周期硬布线控制器_1_bne , \单周期硬布线控制器_1_memtoreg ;
  wire [1:0] IR_Num, register_2_q;
  wire [3:0] \单周期硬布线控制器_1_alu_op ;
  wire [4:0] multiplexer_4_out, multiplexer_5_out, multiplexer_6_out, multiplexer_7_out, multiplexer_11_out;
  wire [15:0] \总周期数 ;
  wire [31:0] bit_extender_1_out, bit_extender_2_out, bit_extender_3_out, bit_extender_4_out, EPC, \J跳转地址 ,
       MDout, mips_alu_2_result, mips_alu_3_result, multiplexer_1_out, multiplexer_2_out, multiplexer_10_out,
       multiplexer_13_out, multiplexer_16_out, PC_4, PC_B, PC_next, R1, R2, shifter_1_out, shifter_2_out,
       shifter_3_out, \入口地址 , \立即数I扩展 ;

  Clock clock_1 (.out(CLK));
  Button _1 (.out(_1_out));
  Button _2 (.out(_2_out));
  Button _3 (.out(_3_out));
  // Mips_Probe mips_probe_1: pin names not known; wires that end beside it: IR, CLK
  Button \u_继续运行  (.out(Go));
  LED led_1 (.in(W1));
  LED led_2 (.in(W2));
  LED led_3 (.in(W3));
  Comparator #(.width(6)) comparator_1 (.a(IR[5:0]), .b(6'b000100), .eq(SLLV));  // open: gt, lt
  Comparator #(.width(6)) comparator_2 (.a(IR[5:0]), .b(6'b000110), .eq(SRLV));  // open: gt, lt
  Comparator #(.width(32)) comparator_3 (.a(R1), .b(32'h22), .eq(comparator_3_eq));  // open: gt, lt
  not not_1 (not_1_out, Halt);
  MIPS_ALU mips_alu_1 (.X(PC), .Y(32'h4), .AluOP(4'b0101), .Result(PC_4));  // open: Equal, Result_2, shamt
  Multiplexer #(.width(32), .enable("false")) multiplexer_1 (
    .in0(PC_4), .in1(mips_alu_2_result), .out(multiplexer_1_out), .sel(B));
  Clock clock_2 (.out(clock_2_out));
  LED \_1号中断等待指示灯  (.in(W1));
  Clock clock_3 (.out(clock_3_out));
  LED \_2号中断等待指示灯  (.in(W2));
  Clock clock_4 (.out(clock_4_out));
  LED \_3号中断等待指示灯  (.in(W3));
  Hex_Digit_Display hex_digit_display_1 (.value(LedData[31:28]));  // open: dp
  and and_1 (and_1_out, Syscall, not_2_out);
  not not_2 (not_2_out, comparator_3_eq);
  and and_2 (and_2_out, Syscall, comparator_3_eq);
  Register #(.width(32)) u_PC (.D(PC_next), .en(not_1_out), .Q(PC), .clk(CLK), .clr(RST));
  Multiplexer #(.width(32), .enable("false")) multiplexer_2 (
    .in0(multiplexer_1_out), .in1(R1), .out(multiplexer_2_out), .sel(JR));
  or or_1 (W1, IR1_q, d_ff_1_q);
  or or_2 (W2, IR1_2_q, d_ff_2_q);
  or or_3 (W3, IR1_3_q, d_ff_3_q);
  Hex_Digit_Display hex_digit_display_2 (.value(LedData[27:24]));  // open: dp
  Hex_Digit_Display hex_digit_display_3 (.value(LedData[23:20]));  // open: dp
  Comparator #(.width(6)) comparator_4 (.a(IR[31:26]), .b(6'b101001), .eq(SH));  // open: gt, lt
  Comparator #(.width(6)) comparator_5 (.a(IR[31:26]), .b(6'b000110), .eq(comparator_5_eq));  // open: gt, lt
  not not_3 (not_3_out, comparator_6_gt);
  Comparator #(.width(32)) comparator_6 (.a(R1), .b({32{1'b0}}), .gt(comparator_6_gt));  // open: eq, lt
  Counter #(.width(1), .max('h1)) counter_1 (
    .load(and_1_out), .D(and_1_out), .count(1'b0), .Q(Halt), .clk(CLK), .clr(or_4_out));  // open: carry
  or or_4 (or_4_out, Go, RST);
  Register #(.width(32)) register_1 (.D(R2), .en(and_2_out), .Q(LedData), .clk(CLK), .clr(RST));
  Shifter #(.width(32)) shifter_1 (.in(\立即数I扩展 ), .\dist (5'b00010), .out(shifter_1_out));
  and and_3 (and_3_out, JMP, not_4_out);
  D_Flip_Flop d_ff_1 (.clk(IR1_t), .D(1'b1), .Q(d_ff_1_q), .reset(IR1_q));  // open: Qn, preset, en
  D_Flip_Flop d_ff_2 (.clk(IR2_t), .D(1'b1), .Q(d_ff_2_q), .reset(IR1_2_q));  // open: Qn, preset, en
  D_Flip_Flop d_ff_3 (.clk(IR3_t), .D(1'b1), .Q(d_ff_3_q), .reset(IR1_3_q));  // open: Qn, preset, en
  Comparator #(.width(16)) comparator_7 (.a(16'h23b), .b(\总周期数 ), .eq(comparator_7_eq));  // open: gt, lt
  Comparator #(.width(16)) comparator_8 (.a(\总周期数 ), .b(16'h1), .eq(comparator_8_eq));  // open: gt, lt
  Comparator #(.width(16)) comparator_9 (.a(\总周期数 ), .b(16'h4), .eq(comparator_9_eq));  // open: gt, lt
  Comparator #(.width(16)) comparator_10 (.a(\总周期数 ), .b(16'h7), .eq(comparator_10_eq));  // open: gt, lt
  Hex_Digit_Display hex_digit_display_4 (.value(LedData[15:12]));  // open: dp
  Hex_Digit_Display hex_digit_display_5 (.value(LedData[19:16]));  // open: dp
  and and_4 (BLEZ, comparator_5_eq, not_3_out);
  ROM #(.addrWidth(10), .dataWidth(32)) rom_1 (.addr(PC[11:2]), .data(IR));  // open: sel
  MIPS_ALU mips_alu_2 (
    .X(PC_4), .Y(shifter_1_out), .AluOP(4'b0101), .Result(mips_alu_2_result));  // open: Equal, Result_2, shamt
  Multiplexer #(.width(32), .enable("false")) multiplexer_3 (
    .in0(multiplexer_2_out), .in1(\J跳转地址 ), .out(PC_B), .sel(and_3_out));
  not not_4 (not_4_out, JR);
  or or_5 (or_5_out, d_ff_1_q, IR1_q);
  Pull_Resistor pull_resistor_1 (.node(IR1_RST));
  or or_6 (or_6_out, d_ff_2_q, IR1_2_q);
  Pull_Resistor pull_resistor_2 (.node(IR2_RST));
  or or_7 (or_7_out, d_ff_3_q, IR1_3_q);
  Pull_Resistor pull_resistor_3 (.node(IR3_RST));
  or or_8 (or_8_out, comparator_7_eq, comparator_8_eq);
  assign IRA = or_8_out ? ~CLK : 1'bz;  // Controlled_Inverter controlled_inverter_1
  assign IRB = comparator_9_eq ? ~CLK : 1'bz;  // Controlled_Inverter controlled_inverter_2
  assign IRC = comparator_10_eq ? ~CLK : 1'bz;  // Controlled_Inverter controlled_inverter_3
  Hex_Digit_Display hex_digit_display_6 (.value(LedData[7:4]));  // open: dp
  Hex_Digit_Display hex_digit_display_7 (.value(LedData[11:8]));  // open: dp
  // Probe on \总周期数 
  and and_5 (and_5_out, or_5_out, ~IR1_RST);  // AND_Gate
  and and_6 (and_6_out, or_6_out, ~IR2_RST);  // AND_Gate
  and and_7 (and_7_out, or_7_out, ~IR3_RST);  // AND_Gate
  Pull_Resistor pull_resistor_4 (.node(IRA));
  Pull_Resistor pull_resistor_5 (.node(IRB));
  Pull_Resistor pull_resistor_6 (.node(IRC));
  Hex_Digit_Display hex_digit_display_8 (.value(LedData[3:0]));  // open: dp
  \单周期硬布线控制器  \u_单周期硬布线控制器_1  (
    .Func(IR[5:0]), .OP(IR[31:26]), .ALU_OP(\单周期硬布线控制器_1_alu_op ), .MemToReg(\单周期硬布线控制器_1_memtoreg ),
    .MemWrite(MemWrite), .ALU_SRC(\单周期硬布线控制器_1_alu_src ), .RegWrite(RegWrite), .SysCALL(Syscall),
    .SignedExt(SignedExt), .RegDst(RegDst), .JR(JR), .JMP(JMP), .Beq(\单周期硬布线控制器_1_beq ), .JAL(JAL),
    .Bne(\单周期硬布线控制器_1_bne ));
  Multiplexer #(.width(5), .enable("false")) multiplexer_4 (
    .in0(IR[25:21]), .in1(5'b00010), .out(multiplexer_4_out), .sel(Syscall));
  Multiplexer #(.width(5), .enable("false")) multiplexer_5 (
    .in0(IR[20:16]), .in1(5'b00100), .out(multiplexer_5_out), .sel(Syscall));
  Multiplexer #(.width(5), .enable("false")) multiplexer_6 (
    .in0(IR[20:16]), .in1(IR[15:11]), .out(multiplexer_6_out), .sel(RegDst));
  assign bit_extender_1_out = {{6{1'b0}}, IR[25:0]};  // Bit_Extender bit_extender_1
  assign bit_extender_2_out = {{28{1'b0}}, PC_4[31:28]};  // Bit_Extender bit_extender_2
  D_Flip_Flop u_IR1 (.clk(clock_2_out), .D(and_5_out), .Q(IR1_q), .reset(RST));  // open: Qn, preset, en
  D_Flip_Flop IR1_2 (.clk(clock_3_out), .D(and_6_out), .Q(IR1_2_q), .reset(RST));  // open: Qn, preset, en
  D_Flip_Flop IR1_3 (.clk(clock_4_out), .D(and_7_out), .Q(IR1_3_q), .reset(RST));  // open: Qn, preset, en
  not not_5 (not_5_out, Halt);
  and and_8 (and_8_out, not_5_out, RegWrite);
  Multiplexer #(.width(5), .enable("false")) multiplexer_7 (
    .in0(multiplexer_6_out), .in1({5{1'b1}}), .out(multiplexer_7_out), .sel(JAL));
  assign bit_extender_3_out = {{16{1'b0}}, IR[15:0]};  // Bit_Extender bit_extender_3
  assign bit_extender_4_out = {{16{IR[15]}}, IR[15:0]};  // Bit_Extender bit_extender_4
  Shifter #(.width(32)) shifter_2 (.in(bit_extender_1_out), .\dist (5'b00010), .out(shifter_2_out));
  Shifter #(.width(32)) shifter_3 (.in(bit_extender_2_out), .\dist (5'b11100), .out(shifter_3_out));
  Priority_Encoder #(.select(2)) priority_encoder_1 (
    .in1(IR1_q), .in2(IR1_2_q), .in3(IR1_3_q), .out(IR_Num), .gs(priority_encoder_1_gs));  // open: in0, en_out, en_in
  Demultiplexer #(.select(2), .enable("false")) demultiplexer_1 (
    .out1(IR1_RST), .out2(IR2_RST), .out3(IR3_RST), .in(eret), .sel(register_2_q));  // open: out0
  Register #(.width(2)) register_2 (.D(IR_Num), .en(\中断 ), .Q(register_2_q), .clk(CLK), .clr(RST));
  or or_9 (IR1_t, IR1, IRA);
  MIPS_Regifile mips_regifile_1 (
    .Din(RDin), .Clk(CLK), .R1(R1), .R2(R2), .WE(and_8_out), .W_num(multiplexer_7_out),
    .R1_num(multiplexer_4_out), .R2_num(multiplexer_5_out));
  Multiplexer #(.width(32), .enable("false")) multiplexer_8 (
    .in0(bit_extender_3_out), .in1(bit_extender_4_out), .out(\立即数I扩展 ), .sel(SignedExt));
  Adder #(.width(32)) adder_1 (.a(shifter_2_out), .b(shifter_3_out), .out(\J跳转地址 ));  // open: cin, cout
  Multiplexer #(.select(2), .width(32), .enable("false")) multiplexer_9 (
    .in1(32'h30ac), .in2(32'h3150), .in3(32'h31f4), .out(\入口地址 ), .sel(IR_Num));  // open: in0
  and and_9 (\中断 , priority_encoder_1_gs, IE);
  or or_10 (IR2_t, IR2, IRB);
  Multiplexer #(.width(32), .enable("false")) multiplexer_10 (
    .in0(R2), .in1(\立即数I扩展 ), .out(multiplexer_10_out), .sel(\单周期硬布线控制器_1_alu_src ));
  or or_11 (or_11_out, SLLV, SRLV);
  Multiplexer #(.width(5), .enable("false")) multiplexer_11 (
    .in0(IR[10:6]), .in1(R1[4:0]), .out(multiplexer_11_out), .sel(or_11_out));
  or or_12 (IR3_t, IR3, IRC);
  not not_6 (not_6_out, mips_alu_3_equal);
  MIPS_ALU mips_alu_3 (
    .X(R1), .Y(multiplexer_10_out), .AluOP(\单周期硬布线控制器_1_alu_op ), .Equal(mips_alu_3_equal),
    .Result(mips_alu_3_result), .shamt(multiplexer_11_out));  // open: Result_2
  Multiplexer #(.width(32), .enable("false")) multiplexer_12 (
    .in0(multiplexer_16_out), .in1(PC_4), .out(RDin), .sel(JAL));
  Comparator #(.width(32)) comparator_11 (.a(IR), .b(32'h42000018), .eq(eret));  // open: gt, lt
  Register #(.width(32)) u_EPC (.D(PC_B), .en(\中断 ), .Q(EPC), .clk(CLK), .clr(RST));
  Multiplexer #(.width(32), .enable("false")) multiplexer_13 (
    .in0(PC_B), .in1(\入口地址 ), .out(multiplexer_13_out), .sel(\中断 ));
  Multiplexer #(.width(32), .enable("false")) multiplexer_14 (
    .in0(multiplexer_13_out), .in1(EPC), .out(PC_next), .sel(eret));
  and and_10 (and_10_out, mips_alu_3_equal, \单周期硬布线控制器_1_beq );
  or or_13 (B, BLEZ, and_10_out, and_11_out);
  and and_11 (and_11_out, not_6_out, \单周期硬布线控制器_1_bne );
  not not_7 (not_7_out, Halt);
  Comparator #(.width(16)) comparator_12 (.a(\总周期数 ), .b({16{1'b0}}), .eq(comparator_12_eq));  // open: gt, lt
  Button \u_总复位  (.out(RST));
  and and_12 (and_12_out, CLK, not_8_out);
  not not_8 (not_8_out, Halt);
  RAM #(.addrWidth(10), .dataWidth(32), .bus("separate")) ram_1 (
    .addr(mips_alu_3_result[11:2]), .din(MDin), .data(MDout), .str(MemWrite), .sel(not_7_out), .clk(CLK),
    .clr(RST));  // open: ld
  Multiplexer #(.width(32), .enable("false")) multiplexer_15 (
    .in0(R2), .in1({MDout[31:16], R2[15:0]}), .out(MDin), .sel(SH));
  not not_9 (not_9_out, \中断 );
  Register #(.width(1)) u_IE (.D(not_9_out), .en(or_14_out), .Q(IE), .clk(CLK), .clr(RST));
  or or_14 (or_14_out, \中断 , comparator_12_eq, eret);
  Counter #(.width(16), .max('hffff)) counter_2 (
    .Q(\总周期数 ), .clk(and_12_out), .clr(RST));  // open: load, D, count, carry
  Multiplexer #(.width(32), .enable("false")) multiplexer_16 (
    .in0(mips_alu_3_result), .in1(MDout), .out(multiplexer_16_out), .sel(\单周期硬布线控制器_1_memtoreg ));

  // Other names for the same wires on the sheet: Func[5:0] = IR[5:0]; OP[5:0] = IR[31:26];
  //   R2_H[31:0] = {MDout[31:16], R2[15:0]}

  // Notes on the sheet:
  //   中断源
  //   中断等待指示
  //   总复位信号应将除ROM以外所有存储组件全部清零
  //   单级中断测试信号
  //   先断开三个按钮和IRA~IRC的连接
  //   再加入这个电路
  //   指令存储器
  //   数码管输出
  //   指令字
  //   contents of rom_1 (hex, n*v repeats v):
  //   201d07d0 20100001 109fc0 139fc3 8021 2012000c 24160008 26100001 3210000f 20080008 20090001 139900
  //   2709825 132020 20020022 c 1094022 1500fff9 22100001 2018000f 2188024 108700 20080008 20090001 139902
  //   2709825 132021 20020022 c 1094022 1500fff9 108702 2c9b022 12c00001 8000c07 4020 1084027 84400
  //   3508ffff 82021 20020022 c 8000c01 afa20000 23bd0004 afa40000 23bd0004 afb00000 23bd0004 afb30000
  //   23bd0004 afb40000 23bd0004 afb50000 23bd0004 afb60000 23bd0004 20160001 20140003 20150001 168020
  //   108100 2149825 132020 20020022 c 1600fffa 295a022 1680fff7 23bdfffc 8fb60000 23bdfffc 8fb50000
  //   23bdfffc 8fb40000 23bdfffc 8fb30000 23bdfffc 8fb00000 23bdfffc 8fa40000 23bdfffc 8fa20000 42000018
  //   afa20000 23bd0004 afa40000 23bd0004 afb00000 23bd0004 afb30000 23bd0004 afb40000 23bd0004 afb50000
  //   23bd0004 afb60000 23bd0004 20160002 20140003 20150001 168020 108100 2149825 132020 20020022 c
  //   1600fffa 295a022 1680fff7 23bdfffc 8fb60000 23bdfffc 8fb50000 23bdfffc 8fb40000 23bdfffc 8fb30000
  //   23bdfffc 8fb00000 23bdfffc 8fa40000 23bdfffc 8fa20000 42000018 afa20000 23bd0004 afa40000 23bd0004
  //   afb00000 23bd0004 afb30000 23bd0004 afb40000 23bd0004 afb50000 23bd0004 afb60000 23bd0004 20160003
  //   20140003 20150001 168020 108100 2149825 132020 20020022 c 1600fffa 295a022 1680fff7 23bdfffc
  //   8fb60000 23bdfffc 8fb50000 23bdfffc 8fb40000 23bdfffc 8fb30000 23bdfffc 8fb00000 23bdfffc 8fa40000
  //   23bdfffc 8fa20000 42000018
  //   数码管输出应该用寄存器锁存，否则显示数据只能一闪而过
  //   OP
  //   Func
  //   rs
  //   rt
  //   rd
  //   shamt
  //   立即数I
  //   立即数J
  //   Reset 
  //   Reset 
  //   Reset 
  //   JMP
  //   JR
  //   OP
  //   Func
  //   Syscall
  //   Beq
  //   Bne
  //   MemToReg
  //   MemWrite
  //   AluOP
  //   AluSrcB
  //   RegWrite
  //   JAL
  //   RegDst
  //   为方便自动评测，需要输出PC，IR，寄存器堆写如数据RDin
  //   RAM写使能MemWrite、RAM写入数据MDin等信号
endmodule
module \单周期MIPS_多级中断  (
  input  IR1,
  input  IR2,
  input  IR3,
  output RegWrite,
  output MemWrite,
  output [31:0] PC,
  output [31:0] IR,
  output [31:0] RDin,
  output [31:0] MDin,
  output [31:0] LedData
);

  wire _1_out, _2_out, _3_out, and_1_out, and_2_out, and_4_out, and_5_out, and_6_out, and_7_out, and_8_out,
       and_10_out, and_11_out, and_12_out, and_13_out, and_14_out, and_15_out, and_16_out, and_17_out,
       and_18_out, B, BLEZ, CLK, clock_2_out, clock_3_out, clock_4_out, comparator_3_eq, comparator_5_eq,
       comparator_6_gt, comparator_7_eq, comparator_8_eq, comparator_9_eq, comparator_10_eq,
       comparator_11_eq, comparator_13_eq, comparator_14_eq, comparator_15_eq, comparator_16_lt,
       comparator_17_eq, d_ff_1_q, d_ff_2_q, d_ff_3_q, decoder_1_out1, decoder_1_out2, decoder_1_out3,
       decoder_2_out0, decoder_2_out1, decoder_2_out2, eret, Go, Halt, IE, IR1_2_q, IR1_3_q, IR1_q, IR1_RST,
       IR1_t, IR2_RST, IR2_t, IR3_RST, IR3_t, IRA, IRB, IRC, JAL, JMP, JR, mfc0, mips_alu_3_equal, mtc0,
       not_1_out, not_2_out, not_3_out, not_4_out, not_5_out, not_6_out, not_7_out, not_8_out, not_9_out,
       or_4_out, or_5_out, or_6_out, or_7_out, or_8_out, or_9_out, or_12_out, or_15_out, or_16_out,
       or_17_out, priority_encoder_1_gs, RegDst, RST, SH, SignedExt, SLLV, SRLV, Syscall, W1, W2, W3, \中断 ,
       \单周期硬布线控制器_1_alu_src , \单周期硬布线控制器_1_beq , \单周期硬布线控制器_1_bne , \单周期硬布线控制器_1_memtoreg ;
  wire [1:0] adder_2_out, exist, IR_Num, IR_Num_Now, IRNum1_q, IRNum2_q, IRNum3_q, multiplexer_19_out;
  wire [3:0] \单周期硬布线控制器_1_alu_op ;
  wire [4:0] multiplexer_4_out, multiplexer_5_out, multiplexer_6_out, multiplexer_7_out, multiplexer_13_out;
  wire [9:0] mips_alu_3_result_2;
  wire [15:0] \总周期数 ;
  wire [31:0] bit_extender_1_out, bit_extender_2_out, bit_extender_3_out, bit_extender_4_out, EPC, EPC1_q,
       EPC2_q, EPC3_q, \J跳转地址 , MDout, mips_alu_2_result, mips_alu_3_result, multiplexer_1_out,
       multiplexer_2_out, multiplexer_10_out, multiplexer_12_out, multiplexer_18_out, PC_4, PC_B, PC_next,
       R1, R2, shifter_1_out, shifter_2_out, shifter_3_out, \入口地址 , \立即数I扩展 ;

  Clock clock_1 (.out(CLK));
  Button _1 (.out(_1_out));
  Button _2 (.out(_2_out));
  Button _3 (.out(_3_out));
  Button \u_继续运行  (.out(Go));
  LED led_1 (.in(W1));
  LED led_2 (.in(W2));
  LED led_3 (.in(W3));
  Comparator #(.width(6)) comparator_1 (.a(IR[5:0]), .b(6'b000100), .eq(SLLV));  // open: gt, lt
  Comparator #(.width(6)) comparator_2 (.a(IR[5:0]), .b(6'b000110), .eq(SRLV));  // open: gt, lt
  Comparator #(.width(32)) comparator_3 (.a(R1), .b(32'h22), .eq(comparator_3_eq));  // open: gt, lt
  // Mips_Probe mips_probe_1: pin names not known; wires that end beside it: IR, CLK
  not not_1 (not_1_out, Halt);
  Multiplexer #(.width(32), .enable("false")) multiplexer_1 (
    .in0(PC_4), .in1(mips_alu_2_result), .out(multiplexer_1_out), .sel(B));
  LED \_1号中断等待指示灯  (.in(W1));
  LED \_2号中断等待指示灯  (.in(W2));
  LED \_3号中断等待指示灯  (.in(W3));
  Hex_Digit_Display hex_digit_display_1 (.value(LedData[31:28]));  // open: dp
  and and_1 (and_1_out, Syscall, not_2_out);
  not not_2 (not_2_out, comparator_3_eq);
  and and_2 (and_2_out, Syscall, comparator_3_eq);
  Register #(.width(32)) u_PC (.D(PC_next), .en(not_1_out), .Q(PC), .clk(CLK), .clr(RST));
  MIPS_ALU mips_alu_1 (.X(PC), .Y(32'h4), .AluOP(4'b0101), .Result(PC_4));  // open: Equal, Result_2, shamt
  Multiplexer #(.width(32), .enable("false")) multiplexer_2 (
    .in0(multiplexer_1_out), .in1(R1), .out(multiplexer_2_out), .sel(JR));
  Clock clock_2 (.out(clock_2_out));
  or or_1 (W1, IR1_q, d_ff_1_q);
  Clock clock_3 (.out(clock_3_out));
  or or_2 (W2, IR1_2_q, d_ff_2_q);
  Clock clock_4 (.out(clock_4_out));
  or or_3 (W3, IR1_3_q, d_ff_3_q);
  Hex_Digit_Display hex_digit_display_2 (.value(LedData[27:24]));  // open: dp
  Hex_Digit_Display hex_digit_display_3 (.value(LedData[23:20]));  // open: dp
  Comparator #(.width(6)) comparator_4 (.a(IR[31:26]), .b(6'b101001), .eq(SH));  // open: gt, lt
  Comparator #(.width(6)) comparator_5 (.a(IR[31:26]), .b(6'b000110), .eq(comparator_5_eq));  // open: gt, lt
  not not_3 (not_3_out, comparator_6_gt);
  Comparator #(.width(32)) comparator_6 (.a(R1), .b({32{1'b0}}), .gt(comparator_6_gt));  // open: eq, lt
  Counter #(.width(1), .max('h1)) counter_1 (
    .load(and_1_out), .D(and_1_out), .count(1'b0), .Q(Halt), .clk(CLK), .clr(or_4_out));  // open: carry
  or or_4 (or_4_out, Go, RST);
  Register #(.width(32)) register_1 (.D(R2), .en(and_2_out), .Q(LedData), .clk(CLK), .clr(RST));
  Shifter #(.width(32)) shifter_1 (.in(\立即数I扩展 ), .\dist (5'b00010), .out(shifter_1_out));
  D_Flip_Flop d_ff_1 (.clk(IR1_t), .D(1'b1), .Q(d_ff_1_q), .reset(IR1_q));  // open: Qn, preset, en
  D_Flip_Flop d_ff_2 (.clk(IR2_t), .D(1'b1), .Q(d_ff_2_q), .reset(IR1_2_q));  // open: Qn, preset, en
  D_Flip_Flop d_ff_3 (.clk(IR3_t), .D(1'b1), .Q(d_ff_3_q), .reset(IR1_3_q));  // open: Qn, preset, en
  Comparator #(.width(16)) comparator_7 (.a(16'h258), .b(\总周期数 ), .eq(comparator_7_eq));  // open: gt, lt
  Comparator #(.width(16)) comparator_8 (.a(\总周期数 ), .b(16'h1), .eq(comparator_8_eq));  // open: gt, lt
  Comparator #(.width(16)) comparator_9 (.a(\总周期数 ), .b(16'h4), .eq(comparator_9_eq));  // open: gt, lt
  Comparator #(.width(16)) comparator_10 (.a(\总周期数 ), .b(16'h7), .eq(comparator_10_eq));  // open: gt, lt
  Comparator #(.width(16)) comparator_11 (.a(\总周期数 ), .b(16'h241), .eq(comparator_11_eq));  // open: gt, lt
  Hex_Digit_Display hex_digit_display_4 (.value(LedData[15:12]));  // open: dp
  Hex_Digit_Display hex_digit_display_5 (.value(LedData[19:16]));  // open: dp
  and and_3 (BLEZ, comparator_5_eq, not_3_out);
  ROM #(.addrWidth(10), .dataWidth(32)) rom_1 (.addr(PC[11:2]), .data(IR));  // open: sel
  MIPS_ALU mips_alu_2 (
    .X(PC_4), .Y(shifter_1_out), .AluOP(4'b0101), .Result(mips_alu_2_result));  // open: Equal, Result_2, shamt
  Multiplexer #(.width(32), .enable("false")) multiplexer_3 (
    .in0(multiplexer_2_out), .in1(\J跳转地址 ), .out(PC_B), .sel(and_4_out));
  and and_4 (and_4_out, JMP, not_4_out);
  not not_4 (not_4_out, JR);
  or or_5 (or_5_out, d_ff_1_q, IR1_q);
  Pull_Resistor pull_resistor_1 (.node(IR1_RST));
  or or_6 (or_6_out, d_ff_2_q, IR1_2_q);
  Pull_Resistor pull_resistor_2 (.node(IR2_RST));
  or or_7 (or_7_out, d_ff_3_q, IR1_3_q);
  Pull_Resistor pull_resistor_3 (.node(IR3_RST));
  or or_8 (or_8_out, comparator_7_eq, comparator_8_eq);
  assign IRA = or_8_out ? ~CLK : 1'bz;  // Controlled_Inverter controlled_inverter_1
  assign IRB = comparator_9_eq ? ~CLK : 1'bz;  // Controlled_Inverter controlled_inverter_2
  or or_9 (or_9_out, comparator_10_eq, comparator_11_eq);
  assign IRC = or_9_out ? ~CLK : 1'bz;  // Controlled_Inverter controlled_inverter_3
  Hex_Digit_Display hex_digit_display_6 (.value(LedData[7:4]));  // open: dp
  Hex_Digit_Display hex_digit_display_7 (.value(LedData[11:8]));  // open: dp
  // Probe on \总周期数 
  and and_5 (and_5_out, or_5_out, ~IR1_RST);  // AND_Gate
  and and_6 (and_6_out, or_6_out, ~IR2_RST);  // AND_Gate
  and and_7 (and_7_out, or_7_out, ~IR3_RST);  // AND_Gate
  Pull_Resistor pull_resistor_4 (.node(IRA));
  Pull_Resistor pull_resistor_5 (.node(IRB));
  Pull_Resistor pull_resistor_6 (.node(IRC));
  Hex_Digit_Display hex_digit_display_8 (.value(LedData[3:0]));  // open: dp
  Multiplexer #(.width(5), .enable("false")) multiplexer_4 (
    .in0(IR[25:21]), .in1(5'b00010), .out(multiplexer_4_out), .sel(Syscall));
  Multiplexer #(.width(5), .enable("false")) multiplexer_5 (
    .in0(IR[20:16]), .in1(5'b00100), .out(multiplexer_5_out), .sel(Syscall));
  Multiplexer #(.width(5), .enable("false")) multiplexer_6 (
    .in0(IR[20:16]), .in1(IR[15:11]), .out(multiplexer_6_out), .sel(RegDst));
  assign bit_extender_1_out = {{6{1'b0}}, IR[25:0]};  // Bit_Extender bit_extender_1
  assign bit_extender_2_out = {{28{1'b0}}, PC_4[31:28]};  // Bit_Extender bit_extender_2
  D_Flip_Flop u_IR1 (.clk(clock_2_out), .D(and_5_out), .Q(IR1_q), .reset(RST));  // open: Qn, preset, en
  D_Flip_Flop IR1_2 (.clk(clock_3_out), .D(and_6_out), .Q(IR1_2_q), .reset(RST));  // open: Qn, preset, en
  D_Flip_Flop IR1_3 (.clk(clock_4_out), .D(and_7_out), .Q(IR1_3_q), .reset(RST));  // open: Qn, preset, en
  \单周期硬布线控制器  \u_单周期硬布线控制器_1  (
    .Func(IR[5:0]), .OP(IR[31:26]), .ALU_OP(\单周期硬布线控制器_1_alu_op ), .MemToReg(\单周期硬布线控制器_1_memtoreg ),
    .MemWrite(MemWrite), .ALU_SRC(\单周期硬布线控制器_1_alu_src ), .RegWrite(RegWrite), .SysCALL(Syscall),
    .SignedExt(SignedExt), .RegDst(RegDst), .JR(JR), .JMP(JMP), .Beq(\单周期硬布线控制器_1_beq ), .JAL(JAL),
    .Bne(\单周期硬布线控制器_1_bne ));
  not not_5 (not_5_out, Halt);
  Multiplexer #(.width(5), .enable("false")) multiplexer_7 (
    .in0(multiplexer_6_out), .in1({5{1'b1}}), .out(multiplexer_7_out), .sel(JAL));
  assign bit_extender_3_out = {{16{1'b0}}, IR[15:0]};  // Bit_Extender bit_extender_3
  assign bit_extender_4_out = {{16{IR[15]}}, IR[15:0]};  // Bit_Extender bit_extender_4
  Shifter #(.width(32)) shifter_2 (.in(bit_extender_1_out), .\dist (5'b00010), .out(shifter_2_out));
  Shifter #(.width(32)) shifter_3 (.in(bit_extender_2_out), .\dist (5'b11100), .out(shifter_3_out));
  Priority_Encoder #(.select(2)) priority_encoder_1 (
    .in1(IR1_q), .in2(IR1_2_q), .in3(IR1_3_q), .out(IR_Num), .gs(priority_encoder_1_gs));  // open: in0, en_out, en_in
  Demultiplexer #(.select(2), .enable("false")) demultiplexer_1 (
    .out1(IR1_RST), .out2(IR2_RST), .out3(IR3_RST), .in(eret), .sel(IR_Num));  // open: out0
  or or_10 (IR1_t, IR1, IRA);
  and and_8 (and_8_out, not_5_out, RegWrite);
  MIPS_Regifile mips_regifile_1 (
    .Din(RDin), .Clk(CLK), .R1(R1), .R2(R2), .WE(and_8_out), .W_num(multiplexer_7_out),
    .R1_num(multiplexer_4_out), .R2_num(multiplexer_5_out));
  Multiplexer #(.width(32), .enable("false")) multiplexer_8 (
    .in0(bit_extender_3_out), .in1(bit_extender_4_out), .out(\立即数I扩展 ), .sel(SignedExt));
  Adder #(.width(32)) adder_1 (.a(shifter_2_out), .b(shifter_3_out), .out(\J跳转地址 ));  // open: cin, cout
  Multiplexer #(.select(2), .width(32), .enable("false")) multiplexer_9 (
    .in1(32'h30ac), .in2(32'h3158), .in3(32'h3204), .out(\入口地址 ), .sel(IR_Num));  // open: in0
  and and_9 (\中断 , priority_encoder_1_gs, comparator_16_lt, IE);
  Multiplexer #(.width(32), .enable("false")) multiplexer_10 (
    .in0(PC_B), .in1(\入口地址 ), .out(multiplexer_10_out), .sel(\中断 ));
  or or_11 (IR2_t, IR2, IRB);
  Multiplexer #(.width(32), .enable("false")) multiplexer_11 (
    .in0(multiplexer_10_out), .in1(EPC), .out(PC_next), .sel(eret));
  Multiplexer #(.width(32), .enable("false")) multiplexer_12 (
    .in0(R2), .in1(\立即数I扩展 ), .out(multiplexer_12_out), .sel(\单周期硬布线控制器_1_alu_src ));
  or or_12 (or_12_out, SLLV, SRLV);
  Multiplexer #(.width(5), .enable("false")) multiplexer_13 (
    .in0(IR[10:6]), .in1(R1[4:0]), .out(multiplexer_13_out), .sel(or_12_out));
  Decoder #(.select(2), .enable("false")) decoder_1 (
    .out1(decoder_1_out1), .out2(decoder_1_out2), .out3(decoder_1_out3), .sel(IR_Num));  // open: out0
  Pull_Resistor pull_resistor_7 (.node(decoder_1_out1));
  Pull_Resistor pull_resistor_8 (.node(decoder_1_out2));
  Pull_Resistor pull_resistor_9 (.node(decoder_1_out3));
  Decoder #(.select(2), .enable("false")) decoder_2 (
    .out0(decoder_2_out0), .out1(decoder_2_out1), .out2(decoder_2_out2), .sel(exist));  // open: out3
  or or_13 (IR3_t, IR3, IRC);
  not not_6 (not_6_out, mips_alu_3_equal);
  MIPS_ALU mips_alu_3 (
    .X(R1), .Y(multiplexer_12_out), .AluOP(\单周期硬布线控制器_1_alu_op ), .Equal(mips_alu_3_equal),
    .Result({mips_alu_3_result[31:12], mips_alu_3_result_2, mips_alu_3_result[1:0]}),
    .shamt(multiplexer_13_out));  // open: Result_2
  Multiplexer #(.width(32), .enable("false")) multiplexer_14 (
    .in0(multiplexer_18_out), .in1(PC_4), .out(RDin), .sel(JAL));
  and and_10 (and_10_out, \中断 , decoder_1_out1);
  and and_11 (and_11_out, \中断 , decoder_1_out2);
  and and_12 (and_12_out, \中断 , decoder_1_out3);
  and and_13 (and_13_out, mips_alu_3_equal, \单周期硬布线控制器_1_beq );
  and and_14 (and_14_out, not_6_out, \单周期硬布线控制器_1_bne );
  Comparator #(.width(32)) comparator_12 (.a(IR), .b(32'h42000018), .eq(eret));  // open: gt, lt
  Register #(.width(32)) EPC1 (.D(PC_B), .en(and_10_out), .Q(EPC1_q), .clk(CLK), .clr(RST));
  Register #(.width(32)) EPC2 (.D(PC_B), .en(and_11_out), .Q(EPC2_q), .clk(CLK), .clr(RST));
  Register #(.width(32)) EPC3 (.D(PC_B), .en(and_12_out), .Q(EPC3_q), .clk(CLK), .clr(RST));
  Register #(.width(2)) IRNum1 (.D(IR_Num), .en(and_15_out), .Q(IRNum1_q), .clk(CLK), .clr(RST));
  and and_15 (and_15_out, \中断 , decoder_2_out0);
  Register #(.width(2)) IRNum2 (.D(IR_Num), .en(and_16_out), .Q(IRNum2_q), .clk(CLK), .clr(RST));
  and and_16 (and_16_out, \中断 , decoder_2_out1);
  Register #(.width(2)) IRNum3 (.D(IR_Num), .en(and_17_out), .Q(IRNum3_q), .clk(CLK), .clr(RST));
  and and_17 (and_17_out, \中断 , decoder_2_out2);
  or or_14 (B, BLEZ, and_13_out, and_14_out);
  not not_7 (not_7_out, Halt);
  Multiplexer #(.select(2), .width(32), .enable("false")) multiplexer_15 (
    .in1(EPC1_q), .in2(EPC2_q), .in3(EPC3_q), .out(EPC), .sel(IR_Num_Now));  // open: in0
  Button \u_总复位  (.out(RST));
  not not_8 (not_8_out, Halt);
  RAM #(.addrWidth(10), .dataWidth(32), .bus("separate")) ram_1 (
    .addr(mips_alu_3_result_2), .din(MDin), .data(MDout), .str(MemWrite), .sel(not_7_out), .clk(CLK),
    .clr(RST));  // open: ld
  Multiplexer #(.width(32), .enable("false")) multiplexer_16 (
    .in0(R2), .in1({MDout[31:16], R2[15:0]}), .out(MDin), .sel(SH));
  Multiplexer #(.select(2), .width(2), .enable("false")) multiplexer_17 (
    .in1(IRNum1_q), .in2(IRNum2_q), .in3(IRNum3_q), .out(IR_Num_Now), .sel(exist));  // open: in0
  Counter #(.width(16), .max('hffff)) counter_2 (
    .Q(\总周期数 ), .clk(and_18_out), .clr(RST));  // open: load, D, count, carry
  and and_18 (and_18_out, CLK, not_8_out);
  Multiplexer #(.width(32), .enable("false")) multiplexer_18 (
    .in0({mips_alu_3_result[31:12], mips_alu_3_result_2, mips_alu_3_result[1:0]}), .in1(MDout),
    .out(multiplexer_18_out), .sel(\单周期硬布线控制器_1_memtoreg ));
  Comparator #(.width(6)) comparator_13 (.a(IR[31:26]), .b(6'b010000), .eq(comparator_13_eq));  // open: gt, lt
  Comparator #(.width(5)) comparator_14 (.a(IR[25:21]), .b({5{1'b0}}), .eq(comparator_14_eq));  // open: gt, lt
  Comparator #(.width(5)) comparator_15 (.a(IR[25:21]), .b(5'b00100), .eq(comparator_15_eq));  // open: gt, lt
  Multiplexer #(.width(2), .enable("false")) multiplexer_19 (
    .in0(2'b11), .in1(2'b01), .out(multiplexer_19_out), .sel(\中断 ));
  Comparator #(.width(2), .mode("unsigned")) comparator_16 (
    .a(IR_Num_Now), .b(IR_Num), .lt(comparator_16_lt));  // open: gt, eq
  Pull_Resistor #(.pull(1)) pull_resistor_10 (.node(comparator_16_lt));
  and and_19 (mfc0, comparator_13_eq, comparator_14_eq);
  and and_20 (mtc0, comparator_13_eq, comparator_15_eq);
  or or_15 (or_15_out, mtc0, \中断 );
  Comparator #(.width(16)) comparator_17 (.a(\总周期数 ), .b({16{1'b0}}), .eq(comparator_17_eq));  // open: gt, lt
  Adder #(.width(2)) adder_2 (.a(exist), .b(multiplexer_19_out), .out(adder_2_out));  // open: cin, cout
  Register #(.width(2)) register_2 (.D(adder_2_out), .en(or_16_out), .Q(exist), .clk(CLK), .clr(RST));
  or or_16 (or_16_out, \中断 , eret);
  not not_9 (not_9_out, or_15_out);
  Register #(.width(1)) u_IE (.D(not_9_out), .en(or_17_out), .Q(IE), .clk(CLK), .clr(RST));
  or or_17 (or_17_out, \中断 , eret, mfc0, mtc0, comparator_17_eq);

  // Other names for the same wires on the sheet: Func[5:0] = IR[5:0]; rs[4:0] = IR[25:21]; OP[5:0] = IR[31:26];
  //   R2_H[31:0] = {MDout[31:16], R2[15:0]}

  // Notes on the sheet:
  //   中断源
  //   中断等待指示
  //   总复位信号应将除ROM以外所有存储组件全部清零
  //   多级中断信号产生
  //   指令存储器
  //   数码管输出
  //   指令字
  //   contents of rom_1 (hex, n*v repeats v):
  //   201d07d0 20100001 109fc0 139fc3 8021 2012000c 24160008 26100001 3210000f 20080008 20090001 139900
  //   2709825 132020 20020022 c 1094022 1500fff9 22100001 2018000f 2188024 108700 20080008 20090001 139902
  //   2709825 132021 20020022 c 1094022 1500fff9 108702 2c9b022 12c00001 8000c07 4020 1084027 84400
  //   3508ffff 82021 20020022 c 8000c01 afa20000 23bd0004 afa40000 23bd0004 afb00000 23bd0004 afb30000
  //   23bd0004 afb40000 23bd0004 afb50000 23bd0004 afb60000 23bd0004 40000000 20160001 20140003 20150001
  //   168020 108100 2149825 132020 20020022 c 1600fffa 295a022 1680fff7 40800000 23bdfffc 8fb60000
  //   23bdfffc 8fb50000 23bdfffc 8fb40000 23bdfffc 8fb30000 23bdfffc 8fb00000 23bdfffc 8fa40000 23bdfffc
  //   8fa20000 42000018 afa20000 23bd0004 afa40000 23bd0004 afb00000 23bd0004 afb30000 23bd0004 afb40000
  //   23bd0004 afb50000 23bd0004 afb60000 23bd0004 40000000 20160002 20140003 20150001 168020 108100
  //   2149825 132020 20020022 c 1600fffa 295a022 1680fff7 40800000 23bdfffc 8fb60000 23bdfffc 8fb50000
  //   23bdfffc 8fb40000 23bdfffc 8fb30000 23bdfffc 8fb00000 23bdfffc 8fa40000 23bdfffc 8fa20000 42000018
  //   afa20000 23bd0004 afa40000 23bd0004 afb00000 23bd0004 afb30000 23bd0004 afb40000 23bd0004 afb50000
  //   23bd0004 afb60000 23bd0004 40000000 20160003 20140003 20150001 168020 108100 2149825 132020 20020022
  //   c 1600fffa 295a022 1680fff7 40800000 23bdfffc 8fb60000 23bdfffc 8fb50000 23bdfffc 8fb40000 23bdfffc
  //   8fb30000 23bdfffc 8fb00000 23bdfffc 8fa40000 23bdfffc 8fa20000 42000018
  //   数码管输出应该用寄存器锁存，否则显示数据只能一闪而过
  //   OP
  //   Func
  //   rs
  //   rt
  //   rd
  //   shamt
  //   立即数I
  //   立即数J
  //   Reset 
  //   Reset 
  //   Reset 
  //   JMP
  //   JR
  //   OP
  //   Func
  //   Beq
  //   Bne
  //   MemToReg
  //   MemWrite
  //   AluOP
  //   AluSrcB
  //   RegWrite
  //   JAL
  //   RegDst
  //   Syscall
  //   为方便自动评测，需要输出PC，IR，寄存器堆写如数据RDin
  //   RAM写使能MemWrite、RAM写入数据MDin等信号
endmodule

module \流水中断  (
  output RegWrite,
  output MemWrite,
  output [31:0] IF_PC,
  output [31:0] ID_PC,
  output [31:0] EX_PC,
  output [31:0] M_PC,
  output [31:0] WB_PC,
  output [31:0] RDin,
  output [31:0] MDin,
  output [31:0] LedData
);

  wire AluSrc, and_1_out, and_2_out, and_3_out, and_4_out, and_5_out, and_6_out, and_8_out, and_9_out,
       and_10_out, and_11_out, and_12_out, and_13_out, and_14_out, and_15_out, B, Beq, Blez, Bne, CLK,
       clock_1_out, clock_2_out, clock_3_out, clock_4_out, comparator_3_eq, comparator_4_eq, comparator_4_lt,
       comparator_5_eq, comparator_6_eq, comparator_7_gt, comparator_8_eq, comparator_9_eq, counter_2_q,
       d_ff_1_q, d_ff_2_q, d_ff_3_q, d_ff_4_q, Equal, eret, ex_mem_1_halt_out, ex_mem_1_jal_out,
       ex_mem_1_pj_eret_out, EX_RegWrite, Go, Halt, id_ex_1_jal_out, id_ex_1_memtoreg_out,
       id_ex_1_memwrite_out, id_ex_1_pj_eret_out, ID_JAL, IE, IR1, IR1_2_q, IR1_3_q, IR1_q, IR1_RST, IR2,
       IR2_RST, IR3, IR3_RST, JAL, JMP, JR, Load_Use, MEM_MemToReg, MEM_RegWrite, MemToReg, nand_1_out,
       not_1_out, not_2_out, not_3_out, not_4_out, not_5_out, not_6_out, not_7_out, not_8_out, not_9_out,
       not_10_out, not_11_out, not_12_out, not_13_out, or_1_out, or_2_out, or_3_out, or_4_out, or_6_out,
       or_7_out, or_12_out, or_13_out, or_14_out, or_15_out, priority_encoder_1_gs, R1_Used, R2_Used, RegDst,
       RST, SignedExt, SLLV, SRLV, Syscall, W1, W2, W3, \中断 , \单周期硬布线控制器_1_alu_src , \单周期硬布线控制器_1_beq ,
       \单周期硬布线控制器_1_bne , \单周期硬布线控制器_1_jmp , \单周期硬布线控制器_1_jr , \单周期硬布线控制器_1_memtoreg ,
       \单周期硬布线控制器_1_memwrite , \单周期硬布线控制器_1_regwrite , \单周期硬布线控制器_1_syscall , \气泡 ;
  wire [1:0] id_ex_1_forward1_out, id_ex_1_forward2_out, ID_Forward1, ID_Forward2, IR_Num, register_2_q,
       register_3_q;
  wire [3:0] AluOP, \单周期硬布线控制器_1_alu_op ;
  wire [4:0] EX_WriteReg_num, id_ex_1_shamt_out, MEM_WriteReg_num, mips_regifile_1_r1, multiplexer_3_out,
       multiplexer_4_out, multiplexer_6_out, R1_num, R2_num, W_num;
  wire [5:0] Func;
  wire [12:0] CNT_num;
  wire [15:0] \LoadUse次数 , \总周期数 , \插入气泡数 , \无条件分支数 , \条件分支成功数 ;
  wire [31:0] adder_1_out, bit_extender_1_out, bit_extender_2_out, bit_extender_3_out, bit_extender_4_out,
       EPC, EX_IR, ex_mem_1_b_out, ex_mem_1_pc_4_out, EX_PC_4, id_ex_1_a_out, id_ex_1_b_out, id_ex_1_imm_out,
       if_id_1_pc_4_out, IF_IR, \J跳转地址 , MDout, MEM_ALU, MEM_IR, mips_alu_2_result, mips_alu_3_result,
       mips_regifile_1_r2, multiplexer_5_out, multiplexer_7_out, multiplexer_8_out, multiplexer_9_out,
       multiplexer_10_out, multiplexer_12_out, multiplexer_14_out, multiplexer_16_out, PC_4, PC_B, PC_next,
       shifter_1_out, shifter_2_out, shifter_3_out, WB_ALU, WB_IR, WB_MD, WB_PC_4, \入口地址 ;
  wire [31:5] mips_regifile_1_r1_2;
  wire [31:6] ID_IR;

  Button \u_总复位  (.out(RST));
  Button _1 (.out(IR1));
  Button _2 (.out(IR2));
  Button _3 (.out(IR3));
  // Probe on \总周期数 
  // Probe on \总周期数 
  and and_1 (and_1_out, not_1_out, not_2_out);
  not not_1 (not_1_out, Halt);
  not not_2 (not_2_out, Load_Use);
  Button \u_继续运行  (.out(Go));
  LED led_1 (.in(W1));
  LED led_2 (.in(W2));
  LED led_3 (.in(W3));
  Register #(.width(32)) PC (.D(PC_next), .en(and_1_out), .Q(IF_PC), .clk(CLK), .clr(RST));
  Hex_Digit_Display hex_digit_display_1 (.value(LedData[31:28]));  // open: dp
  // Probe on IF_PC[19:0]
  // Mips_Probe mips_probe_1: pin names not known; wires that end beside it: IF_IR
  \源寄存器使用情况  \u_源寄存器使用情况_1  (
    .OP0(ID_IR[26]), .OP1(ID_IR[27]), .OP2(ID_IR[28]), .OP3(ID_IR[29]), .OP4(ID_IR[30]), .OP5(ID_IR[31]),
    .F0(Func[0]), .F1(Func[1]), .F2(Func[2]), .F3(Func[3]), .F4(Func[4]), .F5(Func[5]), .R1_Used(R1_Used),
    .R2_Used(R2_Used));
  \重定向数据相关检测  \u_重定向数据相关检测_1  (
    .R1_Used(R1_Used), .R2_Used(R2_Used), .EX_RegWrite(EX_RegWrite), .MEM_RegWrite(MEM_RegWrite),
    .MEM_MemToReg(MEM_MemToReg), .R1_num(R1_num), .R2_num(R2_num), .EX_WriteReg_num(EX_WriteReg_num),
    .MEM_WriteReg_num(MEM_WriteReg_num), .Forward1(ID_Forward1), .EX_IR(EX_IR), .Load_Use(Load_Use),
    .Forward2(ID_Forward2));
  Hex_Digit_Display hex_digit_display_2 (.value(LedData[23:20]));  // open: dp
  Hex_Digit_Display hex_digit_display_3 (.value(LedData[27:24]));  // open: dp
  // Probe on ID_PC[19:0]
  // Mips_Probe mips_probe_2: pin names not known; wires that end beside it: {ID_IR, Func}
  MIPS_ALU mips_alu_1 (.X(IF_PC), .Y(32'h4), .AluOP(4'b0101), .Result(PC_4));  // open: Equal, Result_2, shamt
  ROM #(.addrWidth(10), .dataWidth(32)) rom_1 (.addr(IF_PC[11:2]), .data(IF_IR));  // open: sel
  Hex_Digit_Display hex_digit_display_4 (.value(LedData[19:16]));  // open: dp
  Hex_Digit_Display hex_digit_display_5 (.value(LedData[15:12]));  // open: dp
  or or_1 (or_1_out, \气泡 , eret, \中断 );
  or or_2 (or_2_out, Halt, Load_Use);
  Hex_Digit_Display hex_digit_display_6 (.value(LedData[7:4]));  // open: dp
  Hex_Digit_Display hex_digit_display_7 (.value(LedData[11:8]));  // open: dp
  // Probe on EX_PC[19:0]
  // Mips_Probe mips_probe_3: pin names not known; wires that end beside it: EX_IR
  IF_ID if_id_1 (
    .IR_In(IF_IR), .CLK(CLK), .\异步清零 (RST), .\使能端_低电平有效 (or_2_out), .IR_Out({ID_IR, Func}),
    .PC_4_Out(if_id_1_pc_4_out), .PC_4_In(PC_4), .PC_In(IF_PC), .PC_Out(ID_PC), .\同步清零 (or_1_out));  // open: PJ_In, PJ_Out
  Hex_Digit_Display hex_digit_display_8 (.value(LedData[3:0]));  // open: dp
  Multiplexer #(.width(5), .enable("false")) multiplexer_1 (
    .in0(ID_IR[25:21]), .in1(5'b00010), .out(R1_num), .sel(\单周期硬布线控制器_1_syscall ));
  Multiplexer #(.width(5), .enable("false")) multiplexer_2 (
    .in0(ID_IR[20:16]), .in1(5'b00100), .out(R2_num), .sel(\单周期硬布线控制器_1_syscall ));
  Multiplexer #(.width(5), .enable("false")) multiplexer_3 (
    .in0(ID_IR[20:16]), .in1(ID_IR[15:11]), .out(multiplexer_3_out), .sel(RegDst));
  Comparator #(.width(6)) comparator_1 (.a(Func), .b(6'b000100), .eq(SLLV));  // open: gt, lt
  Comparator #(.width(6)) comparator_2 (.a(Func), .b(6'b000110), .eq(SRLV));  // open: gt, lt
  // Probe on \总周期数 
  // Probe on M_PC[19:0]
  // Mips_Probe mips_probe_4: pin names not known; wires that end beside it: MEM_IR
  \单周期硬布线控制器  \u_单周期硬布线控制器_1  (
    .Func(Func), .OP(ID_IR[31:26]), .ALU_OP(\单周期硬布线控制器_1_alu_op ), .MemToReg(\单周期硬布线控制器_1_memtoreg ),
    .MemWrite(\单周期硬布线控制器_1_memwrite ), .ALU_SRC(\单周期硬布线控制器_1_alu_src ), .RegWrite(\单周期硬布线控制器_1_regwrite ),
    .SysCALL(\单周期硬布线控制器_1_syscall ), .SignedExt(SignedExt), .RegDst(RegDst), .JR(\单周期硬布线控制器_1_jr ),
    .JMP(\单周期硬布线控制器_1_jmp ), .Beq(\单周期硬布线控制器_1_beq ), .JAL(ID_JAL), .Bne(\单周期硬布线控制器_1_bne ));
  Multiplexer #(.width(5), .enable("false")) multiplexer_4 (
    .in0(multiplexer_3_out), .in1({5{1'b1}}), .out(multiplexer_4_out), .sel(ID_JAL));
  or or_3 (or_3_out, SLLV, SRLV);
  assign bit_extender_1_out = {{16{1'b0}}, {ID_IR[15:6], Func}};  // Bit_Extender bit_extender_1
  assign bit_extender_2_out = {{16{ID_IR[15]}}, {ID_IR[15:6], Func}};  // Bit_Extender bit_extender_2
  assign bit_extender_3_out = {{6{1'b0}}, {ID_IR[25:6], Func}};  // Bit_Extender bit_extender_3
  Shifter #(.width(32)) shifter_1 (.in(bit_extender_3_out), .\dist (5'b00010), .out(shifter_1_out));
  Shifter #(.width(32)) shifter_2 (.in(bit_extender_4_out), .\dist (5'b11100), .out(shifter_2_out));
  assign bit_extender_4_out = {{28{1'b0}}, ID_PC[31:28]};  // Bit_Extender bit_extender_4
  // Probe on \总周期数 
  // Probe on \无条件分支数 
  // Probe on \条件分支成功数 
  // Probe on \插入气泡数 
  // Probe on \LoadUse次数 
  Comparator #(.width(32)) comparator_3 (.a({ID_IR, Func}), .b(32'h42000018), .eq(comparator_3_eq));  // open: gt, lt
  not not_3 (not_3_out, Halt);
  and and_2 (and_2_out, not_3_out, RegWrite);
  Multiplexer #(.width(32), .enable("false")) multiplexer_5 (
    .in0(bit_extender_1_out), .in1(bit_extender_2_out), .out(multiplexer_5_out), .sel(SignedExt));
  Adder #(.width(32)) adder_1 (.a(shifter_1_out), .b(shifter_2_out), .out(adder_1_out));  // open: cin, cout
  // Probe on IF_PC[11:0]
  // Probe on WB_PC[19:0]
  // Mips_Probe mips_probe_5: pin names not known; wires that end beside it: WB_IR
  MIPS_Regifile mips_regifile_1 (
    .Din(RDin), .Clk(CLK), .R1({mips_regifile_1_r1_2, mips_regifile_1_r1}), .R2(mips_regifile_1_r2),
    .WE(and_2_out), .W_num(W_num), .R1_num(R1_num), .R2_num(R2_num));
  Multiplexer #(.width(5), .enable("false")) multiplexer_6 (
    .in0(ID_IR[10:6]), .in1(mips_regifile_1_r1), .out(multiplexer_6_out), .sel(or_3_out));
  // Probe on EX_PC[11:0]
  // Probe on ID_PC[11:0]
  ID_EX id_ex_1 (
    .IR_In({ID_IR, Func}), .MemToReg_In(\单周期硬布线控制器_1_memtoreg ), .RegWrite_In(\单周期硬布线控制器_1_regwrite ),
    .PC_4_In(if_id_1_pc_4_out), .MemWrite_In(\单周期硬布线控制器_1_memwrite ), .AluOP_In(\单周期硬布线控制器_1_alu_op ),
    .A_In({mips_regifile_1_r1_2, mips_regifile_1_r1}), .AluSrcB_In(\单周期硬布线控制器_1_alu_src ),
    .B_In(mips_regifile_1_r2), .Beq_In(\单周期硬布线控制器_1_beq ), .Bne_In(\单周期硬布线控制器_1_bne ),
    .Imm_In(multiplexer_5_out), .JR_In(\单周期硬布线控制器_1_jr ), .JMP_In(\单周期硬布线控制器_1_jmp ), .JAL_In(ID_JAL),
    .SysCall_In(\单周期硬布线控制器_1_syscall ), .CLK(CLK), .\异步清零 (RST), .\使能端_低电平有效 (Halt), .IR_Out(EX_IR),
    .MemToReg_Out(id_ex_1_memtoreg_out), .RegWrite_Out(EX_RegWrite), .PC_4_Out(EX_PC_4),
    .MemWrite_Out(id_ex_1_memwrite_out), .AluOP_Out(AluOP), .A_Out(id_ex_1_a_out), .AluSrcB_Out(AluSrc),
    .B_Out(id_ex_1_b_out), .Beq_Out(Beq), .Bne_Out(Bne), .Imm_Out(id_ex_1_imm_out), .JR_Out(JR),
    .JMP_Out(JMP), .JAL_Out(id_ex_1_jal_out), .SysCall_Out(Syscall), .Shamt_In(multiplexer_6_out),
    .Shamt_Out(id_ex_1_shamt_out), .W__In(multiplexer_4_out), .W__Out(EX_WriteReg_num), .PC_In(ID_PC),
    .PC_Out(EX_PC), .\同步清零 (or_4_out), .J_In(adder_1_out), .J_Out(\J跳转地址 ), .Forward2_In(ID_Forward2),
    .Forward2_Out(id_ex_1_forward2_out), .Forward1_In(ID_Forward1), .Forward1_Out(id_ex_1_forward1_out),
    .PJ_eret_In(comparator_3_eq), .PJ_eret_Out(id_ex_1_pj_eret_out));
  or or_4 (or_4_out, eret, \气泡 , Load_Use, \中断 );
  // Probe on M_PC[11:0]
  D_Flip_Flop #(.trigger("high")) d_ff_1 (.Q(d_ff_1_q));  // open: clk, D, Qn, preset, en, reset
  // Probe on 13'h344
  // Probe on WB_PC[11:0]
  Comparator #(.width(13)) comparator_4 (
    .a(CNT_num), .b(13'h344), .eq(comparator_4_eq), .lt(comparator_4_lt));  // open: gt
  Clock clock_1 (.out(clock_1_out));
  Multiplexer #(.select(2), .width(32), .enable("false")) multiplexer_7 (
    .in0(id_ex_1_b_out), .in1(WB_ALU), .in2(WB_MD), .in3(MEM_ALU), .out(multiplexer_7_out),
    .sel(id_ex_1_forward2_out));
  Shifter #(.width(32)) shifter_3 (.in(id_ex_1_imm_out), .\dist (5'b00010), .out(shifter_3_out));
  and and_3 (and_3_out, Equal, Beq);
  not not_4 (not_4_out, Equal);
  and and_4 (and_4_out, not_4_out, Bne);
  Comparator #(.width(32)) comparator_5 (.a(multiplexer_8_out), .b(32'h22), .eq(comparator_5_eq));  // open: gt, lt
  nand nand_1 (nand_1_out, d_ff_1_q, comparator_4_eq);
  Counter #(.width(13), .max('h1fff), .ongoal("stay")) counter_1 (
    .count(comparator_4_lt), .Q(CNT_num), .clk(clock_1_out));  // open: load, D, carry, clr
  Multiplexer #(.select(2), .width(32), .enable("false")) multiplexer_8 (
    .in0(id_ex_1_a_out), .in1(WB_ALU), .in2(WB_MD), .in3(MEM_ALU), .out(multiplexer_8_out),
    .sel(id_ex_1_forward1_out));
  Multiplexer #(.width(32), .enable("false")) multiplexer_9 (
    .in0(multiplexer_7_out), .in1(id_ex_1_imm_out), .out(multiplexer_9_out), .sel(AluSrc));
  MIPS_ALU mips_alu_2 (
    .X(EX_PC_4), .Y(shifter_3_out), .AluOP(4'b0101), .Result(mips_alu_2_result));  // open: Equal, Result_2, shamt
  or or_5 (B, and_3_out, Blez, and_4_out);
  and and_5 (and_5_out, Syscall, not_5_out);
  not not_5 (not_5_out, comparator_5_eq);
  and and_6 (and_6_out, Syscall, comparator_5_eq);
  Comparator #(.width(6)) comparator_6 (.a(EX_IR[31:26]), .b(6'b000110), .eq(comparator_6_eq));  // open: gt, lt
  and and_7 (Blez, comparator_6_eq, not_6_out);
  not not_6 (not_6_out, comparator_7_gt);
  Comparator #(.width(32)) comparator_7 (.a(multiplexer_8_out), .b({32{1'b0}}), .gt(comparator_7_gt));  // open: eq, lt
  assign CLK = nand_1_out ? clock_1_out : 1'bz;  // Controlled_Buffer controlled_buffer_1
  MIPS_ALU mips_alu_3 (
    .X(multiplexer_8_out), .Y(multiplexer_9_out), .AluOP(AluOP), .Equal(Equal), .Result(mips_alu_3_result),
    .shamt(id_ex_1_shamt_out));  // open: Result_2
  Multiplexer #(.width(32), .enable("false")) multiplexer_10 (
    .in0(PC_4), .in1(mips_alu_2_result), .out(multiplexer_10_out), .sel(B));
  Counter #(.width(1), .max('h1)) counter_2 (
    .load(and_5_out), .D(and_5_out), .count(1'b0), .Q(counter_2_q), .clk(CLK), .clr(or_6_out));  // open: carry
  or or_6 (or_6_out, Go, RST);
  Register #(.width(32)) register_1 (.D(multiplexer_7_out), .en(and_6_out), .Q(LedData), .clk(CLK), .clr(RST));
  Pull_Resistor #(.pull(1)) pull_resistor_1 (.node(CLK));
  or or_7 (or_7_out, \中断 , eret);
  Multiplexer #(.width(32), .enable("false")) multiplexer_11 (
    .in0(multiplexer_12_out), .in1(\J跳转地址 ), .out(PC_B), .sel(and_8_out));
  Multiplexer #(.width(32), .enable("false")) multiplexer_12 (
    .in0(multiplexer_10_out), .in1(multiplexer_8_out), .out(multiplexer_12_out), .sel(JR));
  and and_8 (and_8_out, JMP, not_7_out);
  or or_8 (\气泡 , B, JMP);
  EX_MEM ex_mem_1 (
    .IR_In(EX_IR), .MemToReg_In(id_ex_1_memtoreg_out), .RegWrite_In(EX_RegWrite), .PC_4_In(EX_PC_4),
    .MemWrite_In(id_ex_1_memwrite_out), .B_In(multiplexer_7_out), .ALU_In(mips_alu_3_result), .CLK(CLK),
    .\异步清零 (RST), .\使能端_低电平有效 (Halt), .IR_Out(MEM_IR), .MemToReg_Out(MEM_MemToReg),
    .RegWrite_Out(MEM_RegWrite), .PC_4_Out(ex_mem_1_pc_4_out), .MemWrite_Out(MemWrite),
    .B_Out(ex_mem_1_b_out), .ALU_Out(MEM_ALU), .JAL_In(id_ex_1_jal_out), .JAL_Out(ex_mem_1_jal_out),
    .Halt_In(counter_2_q), .Halt_Out(ex_mem_1_halt_out), .W__In(EX_WriteReg_num), .W__Out(MEM_WriteReg_num),
    .PC_In(EX_PC), .PC_Out(M_PC), .\同步清零 (or_7_out), .eret_In(id_ex_1_pj_eret_out),
    .PJ_eret_Out(ex_mem_1_pj_eret_out));
  not not_7 (not_7_out, JR);
  and and_9 (and_9_out, CLK, not_8_out);
  not not_8 (not_8_out, Halt);
  Counter #(.width(16), .max('hffff)) counter_3 (
    .Q(\总周期数 ), .clk(and_9_out), .clr(RST));  // open: load, D, count, carry
  not not_9 (not_9_out, Halt);
  Comparator #(.width(6)) comparator_8 (.a(MEM_IR[31:26]), .b(6'b101001), .eq(comparator_8_eq));  // open: gt, lt
  RAM #(.addrWidth(10), .dataWidth(32), .bus("separate")) ram_1 (
    .addr(MEM_ALU[11:2]), .din(MDin), .data(MDout), .str(MemWrite), .sel(not_9_out), .clk(CLK), .clr(RST));  // open: ld
  Multiplexer #(.width(32), .enable("false")) multiplexer_13 (
    .in0(ex_mem_1_b_out), .in1({MDout[31:16], ex_mem_1_b_out[15:0]}), .out(MDin), .sel(comparator_8_eq));
  and and_10 (and_10_out, CLK, not_10_out);
  not not_10 (not_10_out, Halt);
  MEM_WB mem_wb_1 (
    .IR_In(MEM_IR), .MemToReg_In(MEM_MemToReg), .PC_4_In(ex_mem_1_pc_4_out), .ALU_In(MEM_ALU), .MD_In(MDout),
    .CLK(CLK), .\异步清零 (RST), .\使能端_低电平有效 (Halt), .IR_Out(WB_IR), .MemToReg_Out(MemToReg), .PC_4_Out(WB_PC_4),
    .ALU_Out(WB_ALU), .MD_Out(WB_MD), .RegWrite_In(MEM_RegWrite), .RegWrite_Out(RegWrite),
    .JAL_In(ex_mem_1_jal_out), .JAL_Out(JAL), .Halt_In(ex_mem_1_halt_out), .Halt_Out(Halt),
    .W__In(MEM_WriteReg_num), .W__Out(W_num), .PC_In(M_PC), .PC_Out(WB_PC), .\同步清零 (\中断 ),
    .eret_In(ex_mem_1_pj_eret_out), .eret_Out(eret));
  Counter #(.width(16), .max('hffff)) counter_4 (
    .count(JMP), .Q(\无条件分支数 ), .clk(and_10_out), .clr(RST));  // open: load, D, carry
  Multiplexer #(.width(32), .enable("false")) multiplexer_14 (
    .in0(WB_ALU), .in1(WB_MD), .out(multiplexer_14_out), .sel(MemToReg));
  and and_11 (and_11_out, CLK, not_11_out);
  not not_11 (not_11_out, Halt);
  Multiplexer #(.width(32), .enable("false")) multiplexer_15 (
    .in0(multiplexer_14_out), .in1(WB_PC_4), .out(RDin), .sel(JAL));
  Counter #(.width(16), .max('hffff)) counter_5 (
    .count(B), .Q(\条件分支成功数 ), .clk(and_11_out), .clr(RST));  // open: load, D, carry
  Clock clock_2 (.out(clock_2_out));
  LED \_1号中断等待指示灯  (.in(W1));
  Clock clock_3 (.out(clock_3_out));
  LED \_2号中断等待指示灯  (.in(W2));
  Clock clock_4 (.out(clock_4_out));
  LED \_3号中断等待指示灯  (.in(W3));
  Demultiplexer #(.select(2), .enable("false")) demultiplexer_1 (
    .out1(IR1_RST), .out2(IR2_RST), .out3(IR3_RST), .in(eret), .sel(register_2_q));  // open: out0
  Register #(.width(2)) register_2 (.D(IR_Num), .en(\中断 ), .Q(register_2_q), .clk(CLK), .clr(RST));
  Multiplexer #(.width(32), .enable("false")) multiplexer_16 (
    .in0(PC_B), .in1(\入口地址 ), .out(multiplexer_16_out), .sel(\中断 ));
  and and_12 (and_12_out, CLK, not_12_out);
  not not_12 (not_12_out, Halt);
  D_Flip_Flop d_ff_2 (.clk(IR1), .D(1'b1), .Q(d_ff_2_q), .reset(IR1_q));  // open: Qn, preset, en
  or or_9 (W1, IR1_q, d_ff_2_q);
  D_Flip_Flop d_ff_3 (.clk(IR2), .D(1'b1), .Q(d_ff_3_q), .reset(IR1_2_q));  // open: Qn, preset, en
  or or_10 (W2, IR1_2_q, d_ff_3_q);
  D_Flip_Flop d_ff_4 (.clk(IR3), .D(1'b1), .Q(d_ff_4_q), .reset(IR1_3_q));  // open: Qn, preset, en
  or or_11 (W3, IR1_3_q, d_ff_4_q);
  Multiplexer #(.width(32), .enable("false")) multiplexer_17 (
    .in0(multiplexer_16_out), .in1(EPC), .out(PC_next), .sel(eret));
  Counter #(.width(16), .max('hffff)) counter_6 (
    .count(Load_Use), .Q(\LoadUse次数 ), .clk(and_12_out), .clr(RST));  // open: load, D, carry
  or or_12 (or_12_out, d_ff_2_q, IR1_q);
  and and_13 (and_13_out, or_12_out, ~IR1_RST);  // AND_Gate
  Pull_Resistor pull_resistor_2 (.node(IR1_RST));
  or or_13 (or_13_out, d_ff_3_q, IR1_2_q);
  and and_14 (and_14_out, or_13_out, ~IR2_RST);  // AND_Gate
  Pull_Resistor pull_resistor_3 (.node(IR2_RST));
  or or_14 (or_14_out, d_ff_4_q, IR1_3_q);
  and and_15 (and_15_out, or_14_out, ~IR3_RST);  // AND_Gate
  Pull_Resistor pull_resistor_4 (.node(IR3_RST));
  Register #(.width(32)) u_EPC (.D(WB_PC), .en(\中断 ), .Q(EPC), .clk(CLK), .clr(RST));
  D_Flip_Flop u_IR1 (.clk(clock_2_out), .D(and_13_out), .Q(IR1_q), .reset(RST));  // open: Qn, preset, en
  D_Flip_Flop IR1_2 (.clk(clock_3_out), .D(and_14_out), .Q(IR1_2_q), .reset(RST));  // open: Qn, preset, en
  D_Flip_Flop IR1_3 (.clk(clock_4_out), .D(and_15_out), .Q(IR1_3_q), .reset(RST));  // open: Qn, preset, en
  Comparator #(.width(16)) comparator_9 (.a(\总周期数 ), .b({16{1'b0}}), .eq(comparator_9_eq));  // open: gt, lt
  Priority_Encoder #(.select(2)) priority_encoder_1 (
    .in1(IR1_q), .in2(IR1_2_q), .in3(IR1_3_q), .out(IR_Num), .gs(priority_encoder_1_gs));  // open: in0, en_out, en_in
  Demultiplexer #(.select(2), .enable("false")) demultiplexer_2 (
    .out1(IR1_RST), .out2(IR2_RST), .out3(IR3_RST), .in(eret), .sel(register_3_q));  // open: out0
  Register #(.width(2)) register_3 (.D(IR_Num), .en(\中断 ), .Q(register_3_q), .clk(CLK), .clr(RST));
  not not_13 (not_13_out, \中断 );
  Register #(.width(1)) u_IE (.D(not_13_out), .en(or_15_out), .Q(IE), .clk(CLK), .clr(RST));
  or or_15 (or_15_out, \中断 , comparator_9_eq, eret);
  Multiplexer #(.select(2), .width(32), .enable("false")) multiplexer_18 (
    .in1(32'h30ac), .in2(32'h3150), .in3(32'h31f4), .out(\入口地址 ), .sel(IR_Num));  // open: in0
  and and_16 (\中断 , priority_encoder_1_gs, IE);

  // Other names for the same wires on the sheet: ID_IR[5:0] = Func; OP[5:0] = ID_IR[31:26]; MEM_PC[31:0] = M_PC

  // Notes on the sheet:
  //   中断源
  //   时空图监测，可删除
  //   中断等待指示
  //   contents of rom_1 (hex, n*v repeats v):
  //   201d07d0 20100001 109fc0 139fc3 8021 2012000c 24160008 26100001 3210000f 20080008 20090001 139900
  //   2709825 132020 20020022 c 1094022 1500fff9 22100001 2018000f 2188024 108700 20080008 20090001 139902
  //   2709825 132021 20020022 c 1094022 1500fff9 108702 2c9b022 12c00001 8000c07 4020 1084027 84400
  //   3508ffff 82021 20020022 c 8000c01 afa20000 23bd0004 afa40000 23bd0004 afb00000 23bd0004 afb30000
  //   23bd0004 afb40000 23bd0004 afb50000 23bd0004 afb60000 23bd0004 20160001 20140003 20150001 168020
  //   108100 2149825 132020 20020022 c 1600fffa 295a022 1680fff7 23bdfffc 8fb60000 23bdfffc 8fb50000
  //   23bdfffc 8fb40000 23bdfffc 8fb30000 23bdfffc 8fb00000 23bdfffc 8fa40000 23bdfffc 8fa20000 42000018
  //   afa20000 23bd0004 afa40000 23bd0004 afb00000 23bd0004 afb30000 23bd0004 afb40000 23bd0004 afb50000
  //   23bd0004 afb60000 23bd0004 20160002 20140003 20150001 168020 108100 2149825 132020 20020022 c
  //   1600fffa 295a022 1680fff7 23bdfffc 8fb60000 23bdfffc 8fb50000 23bdfffc 8fb40000 23bdfffc 8fb30000
  //   23bdfffc 8fb00000 23bdfffc 8fa40000 23bdfffc 8fa20000 42000018 afa20000 23bd0004 afa40000 23bd0004
  //   afb00000 23bd0004 afb30000 23bd0004 afb40000 23bd0004 afb50000 23bd0004 afb60000 23bd0004 20160003
  //   20140003 20150001 168020 108100 2149825 132020 20020022 c 1600fffa 295a022 1680fff7 23bdfffc
  //   8fb60000 23bdfffc 8fb50000 23bdfffc 8fb40000 23bdfffc 8fb30000 23bdfffc 8fb00000 23bdfffc 8fa40000
  //   23bdfffc 8fa20000 42000018
  //   数码管输出
  //   OP
  //   Func
  //   rs
  //   rt
  //   rd
  //   shamt
  //   立即数I
  //   立即数J
  //   控制位
  //   流水调试日志用
  //   暂停节拍，不能为0
  //   可计数暂停的时钟源
  //   为方便自动评测，需要输出流水线各段保存的PC值，注意是PC不是PC+4，另外ID段寄存器写入信息，Mem段内存写入信息也要输出
  //   Reset 
  //   Reset 
  //   Reset 
endmodule

module \动态分支预测  (
  output RegWrite,
  output MemWrite,
  output [31:0] IF_PC,
  output [31:0] ID_PC,
  output [31:0] EX_PC,
  output [31:0] M_PC,
  output [31:0] WB_PC,
  output [31:0] RDin,
  output [31:0] MDin,
  output [31:0] LedData
);

  wire AluSrc, and_1_out, and_2_out, and_3_out, and_4_out, and_5_out, and_6_out, and_7_out, and_8_out,
       and_10_out, and_11_out, and_12_out, and_13_out, and_14_out, and_15_out, B, Beq, Blez, Bne, CLK,
       clock_1_out, comparator_3_eq, comparator_3_lt, comparator_4_eq, comparator_5_eq, comparator_6_gt,
       comparator_7_eq, comparator_8_eq, counter_2_q, d_ff_1_q, Equal, ex_mem_1_halt_out, ex_mem_1_jal_out,
       EX_RegWrite, Fail, Go, Halt, id_ex_1_jal_out, id_ex_1_memtoreg_out, id_ex_1_memwrite_out, ID_JAL,
       ID_PredictJump, if_id_1_pj_out, IR1, IR2, IR3, JAL, JMP, JR, Load_Use, MEM_MemToReg, MEM_RegWrite,
       MemToReg, nand_1_out, not_1_out, not_2_out, not_3_out, not_4_out, not_5_out, not_6_out, not_7_out,
       not_8_out, not_9_out, not_11_out, not_12_out, not_13_out, not_14_out, not_15_out, not_16_out,
       or_1_out, or_2_out, or_3_out, or_4_out, or_5_out, or_6_out, or_8_out, PredictJump, R1_Used, R2_Used,
       RegDst, RST, SignedExt, SLLV, SRLV, Syscall, W1, W2, W3, \单周期硬布线控制器_1_alu_src , \单周期硬布线控制器_1_beq ,
       \单周期硬布线控制器_1_bne , \单周期硬布线控制器_1_jmp , \单周期硬布线控制器_1_jr , \单周期硬布线控制器_1_memtoreg ,
       \单周期硬布线控制器_1_memwrite , \单周期硬布线控制器_1_regwrite , \单周期硬布线控制器_1_syscall , \气泡 ;
  wire [1:0] id_ex_1_forward1_out, id_ex_1_forward2_out, ID_Forward1, ID_Forward2;
  wire [3:0] AluOP, \单周期硬布线控制器_1_alu_op ;
  wire [4:0] EX_WriteReg_num, id_ex_1_shamt_out, MEM_WriteReg_num, mips_regifile_1_r1, multiplexer_7_out,
       multiplexer_8_out, multiplexer_10_out, R1_num, R2_num, W_num;
  wire [5:0] Func;
  wire [12:0] CNT_num;
  wire [15:0] \LoadUse次数 , \总周期数 , \插入气泡数 , \无条件分支数 , \条件分支成功数 ;
  wire [31:0] adder_1_out, bht_1_jumpaddr, bit_extender_1_out, bit_extender_2_out, bit_extender_3_out,
       bit_extender_4_out, EX_IR, ex_mem_1_b_out, ex_mem_1_pc_4_out, EX_PC_4, id_ex_1_a_out, id_ex_1_b_out,
       id_ex_1_imm_out, if_id_1_pc_4_out, IF_IR, \J跳转地址 , MDout, MEM_ALU, MEM_IR, mips_alu_2_result,
       mips_alu_3_result, mips_regifile_1_r2, multiplexer_1_out, multiplexer_2_out, multiplexer_3_out,
       multiplexer_9_out, multiplexer_11_out, multiplexer_12_out, multiplexer_13_out, multiplexer_14_out,
       multiplexer_16_out, multiplexer_18_out, PC_4, PC_B, PC_next, shifter_1_out, shifter_2_out,
       shifter_3_out, WB_ALU, WB_IR, WB_MD, WB_PC_4;
  wire [31:5] mips_regifile_1_r1_2;
  wire [31:6] ID_IR;

  Button \u_总复位  (.out(RST));
  Button _1 (.out(IR1));
  Button _2 (.out(IR2));
  Button _3 (.out(IR3));
  // Probe on \总周期数 
  // Probe on \总周期数 
  and and_1 (and_1_out, not_2_out, not_1_out);
  not not_1 (not_1_out, Load_Use);
  not not_2 (not_2_out, Halt);
  Button \u_继续运行  (.out(Go));
  LED led_1 (.in(W1));
  LED led_2 (.in(W2));
  LED led_3 (.in(W3));
  Register #(.width(32)) PC (.D(PC_next), .en(and_1_out), .Q(IF_PC), .clk(CLK), .clr(RST));
  Multiplexer #(.width(32), .enable("false")) multiplexer_1 (
    .in0(PC_4), .in1(bht_1_jumpaddr), .out(multiplexer_1_out), .sel(ID_PredictJump));
  Multiplexer #(.width(32), .enable("false")) multiplexer_2 (
    .in0(EX_PC_4), .in1(PC_B), .out(multiplexer_2_out), .sel(and_3_out));
  Hex_Digit_Display hex_digit_display_1 (.value(LedData[31:28]));  // open: dp
  // Probe on IF_PC[19:0]
  // Mips_Probe mips_probe_1: pin names not known; wires that end beside it: IF_IR
  \源寄存器使用情况  \u_源寄存器使用情况_1  (
    .OP0(ID_IR[26]), .OP1(ID_IR[27]), .OP2(ID_IR[28]), .OP3(ID_IR[29]), .OP4(ID_IR[30]), .OP5(ID_IR[31]),
    .F0(Func[0]), .F1(Func[1]), .F2(Func[2]), .F3(Func[3]), .F4(Func[4]), .F5(Func[5]), .R1_Used(R1_Used),
    .R2_Used(R2_Used));
  \重定向数据相关检测  \u_重定向数据相关检测_1  (
    .R1_Used(R1_Used), .R2_Used(R2_Used), .EX_RegWrite(EX_RegWrite), .MEM_RegWrite(MEM_RegWrite),
    .MEM_MemToReg(MEM_MemToReg), .R1_num(R1_num), .R2_num(R2_num), .EX_WriteReg_num(EX_WriteReg_num),
    .MEM_WriteReg_num(MEM_WriteReg_num), .Forward1(ID_Forward1), .EX_IR(EX_IR), .Load_Use(Load_Use),
    .Forward2(ID_Forward2));
  and and_2 (and_2_out, or_1_out, not_3_out);
  BHT bht_1 (
    .Clk(CLK), .EX_Branch(and_2_out), .PC(IF_PC), .EX_PC(EX_PC), .EX_BranchAddr(PC_B),
    .EX_Branched(and_3_out), .JumpAddr(bht_1_jumpaddr), .PredictJump(ID_PredictJump));
  and and_3 (and_3_out, or_2_out, not_4_out);
  Multiplexer #(.width(32), .enable("false")) multiplexer_3 (
    .in0(multiplexer_1_out), .in1(multiplexer_2_out), .out(multiplexer_3_out), .sel(Fail));
  Hex_Digit_Display hex_digit_display_2 (.value(LedData[23:20]));  // open: dp
  Hex_Digit_Display hex_digit_display_3 (.value(LedData[27:24]));  // open: dp
  // Probe on ID_PC[19:0]
  // Mips_Probe mips_probe_2: pin names not known; wires that end beside it: {ID_IR, Func}
  MIPS_ALU mips_alu_1 (.X(IF_PC), .Y(32'h4), .AluOP(4'b0101), .Result(PC_4));  // open: Equal, Result_2, shamt
  ROM #(.addrWidth(10), .dataWidth(32)) rom_1 (.addr(IF_PC[11:2]), .data(IF_IR));  // open: sel
  or or_1 (or_1_out, Beq, Bne, Blez, JMP);
  not not_3 (not_3_out, JR);
  or or_2 (or_2_out, B, JMP);
  not not_4 (not_4_out, JR);
  Multiplexer #(.width(32), .enable("false")) multiplexer_4 (
    .in0(multiplexer_3_out), .in1(multiplexer_12_out), .out(PC_next), .sel(JR));
  Hex_Digit_Display hex_digit_display_4 (.value(LedData[15:12]));  // open: dp
  Hex_Digit_Display hex_digit_display_5 (.value(LedData[19:16]));  // open: dp
  or or_3 (or_3_out, Halt, Load_Use);
  Hex_Digit_Display hex_digit_display_6 (.value(LedData[11:8]));  // open: dp
  Hex_Digit_Display hex_digit_display_7 (.value(LedData[7:4]));  // open: dp
  // Probe on EX_PC[19:0]
  // Mips_Probe mips_probe_3: pin names not known; wires that end beside it: EX_IR
  IF_ID if_id_1 (
    .IR_In(IF_IR), .CLK(CLK), .\异步清零 (RST), .\使能端_低电平有效 (or_3_out), .IR_Out({ID_IR, Func}),
    .PC_4_Out(if_id_1_pc_4_out), .PC_4_In(PC_4), .PC_In(IF_PC), .PC_Out(ID_PC), .\同步清零 (Fail),
    .PJ_In(ID_PredictJump), .PJ_Out(if_id_1_pj_out));
  Hex_Digit_Display hex_digit_display_8 (.value(LedData[3:0]));  // open: dp
  Multiplexer #(.width(5), .enable("false")) multiplexer_5 (
    .in0(ID_IR[25:21]), .in1(5'b00010), .out(R1_num), .sel(\单周期硬布线控制器_1_syscall ));
  Multiplexer #(.width(5), .enable("false")) multiplexer_6 (
    .in0(ID_IR[20:16]), .in1(5'b00100), .out(R2_num), .sel(\单周期硬布线控制器_1_syscall ));
  Multiplexer #(.width(5), .enable("false")) multiplexer_7 (
    .in0(ID_IR[20:16]), .in1(ID_IR[15:11]), .out(multiplexer_7_out), .sel(RegDst));
  Comparator #(.width(6)) comparator_1 (.a(Func), .b(6'b000100), .eq(SLLV));  // open: gt, lt
  Comparator #(.width(6)) comparator_2 (.a(Func), .b(6'b000110), .eq(SRLV));  // open: gt, lt
  // Probe on \总周期数 
  // Probe on M_PC[19:0]
  // Mips_Probe mips_probe_4: pin names not known; wires that end beside it: MEM_IR
  \单周期硬布线控制器  \u_单周期硬布线控制器_1  (
    .Func(Func), .OP(ID_IR[31:26]), .ALU_OP(\单周期硬布线控制器_1_alu_op ), .MemToReg(\单周期硬布线控制器_1_memtoreg ),
    .MemWrite(\单周期硬布线控制器_1_memwrite ), .ALU_SRC(\单周期硬布线控制器_1_alu_src ), .RegWrite(\单周期硬布线控制器_1_regwrite ),
    .SysCALL(\单周期硬布线控制器_1_syscall ), .SignedExt(SignedExt), .RegDst(RegDst), .JR(\单周期硬布线控制器_1_jr ),
    .JMP(\单周期硬布线控制器_1_jmp ), .Beq(\单周期硬布线控制器_1_beq ), .JAL(ID_JAL), .Bne(\单周期硬布线控制器_1_bne ));
  Multiplexer #(.width(5), .enable("false")) multiplexer_8 (
    .in0(multiplexer_7_out), .in1({5{1'b1}}), .out(multiplexer_8_out), .sel(ID_JAL));
  or or_4 (or_4_out, SLLV, SRLV);
  assign bit_extender_1_out = {{16{1'b0}}, {ID_IR[15:6], Func}};  // Bit_Extender bit_extender_1
  assign bit_extender_2_out = {{16{ID_IR[15]}}, {ID_IR[15:6], Func}};  // Bit_Extender bit_extender_2
  assign bit_extender_3_out = {{6{1'b0}}, {ID_IR[25:6], Func}};  // Bit_Extender bit_extender_3
  Shifter #(.width(32)) shifter_1 (.in(bit_extender_3_out), .\dist (5'b00010), .out(shifter_1_out));
  Shifter #(.width(32)) shifter_2 (.in(bit_extender_4_out), .\dist (5'b11100), .out(shifter_2_out));
  assign bit_extender_4_out = {{28{1'b0}}, ID_PC[31:28]};  // Bit_Extender bit_extender_4
  // Probe on \总周期数 
  // Probe on \无条件分支数 
  // Probe on \条件分支成功数 
  // Probe on \插入气泡数 
  // Probe on \LoadUse次数 
  not not_5 (not_5_out, Halt);
  and and_4 (and_4_out, not_5_out, RegWrite);
  Multiplexer #(.width(32), .enable("false")) multiplexer_9 (
    .in0(bit_extender_1_out), .in1(bit_extender_2_out), .out(multiplexer_9_out), .sel(SignedExt));
  Adder #(.width(32)) adder_1 (.a(shifter_1_out), .b(shifter_2_out), .out(adder_1_out));  // open: cin, cout
  // Probe on IF_PC[11:0]
  // Probe on WB_PC[19:0]
  // Mips_Probe mips_probe_5: pin names not known; wires that end beside it: WB_IR
  MIPS_Regifile mips_regifile_1 (
    .Din(RDin), .Clk(CLK), .R1({mips_regifile_1_r1_2, mips_regifile_1_r1}), .R2(mips_regifile_1_r2),
    .WE(and_4_out), .W_num(W_num), .R1_num(R1_num), .R2_num(R2_num));
  Multiplexer #(.width(5), .enable("false")) multiplexer_10 (
    .in0(ID_IR[10:6]), .in1(mips_regifile_1_r1), .out(multiplexer_10_out), .sel(or_4_out));
  // Probe on ID_PC[11:0]
  // Probe on EX_PC[11:0]
  ID_EX id_ex_1 (
    .IR_In({ID_IR, Func}), .MemToReg_In(\单周期硬布线控制器_1_memtoreg ), .RegWrite_In(\单周期硬布线控制器_1_regwrite ),
    .PC_4_In(if_id_1_pc_4_out), .MemWrite_In(\单周期硬布线控制器_1_memwrite ), .AluOP_In(\单周期硬布线控制器_1_alu_op ),
    .A_In({mips_regifile_1_r1_2, mips_regifile_1_r1}), .AluSrcB_In(\单周期硬布线控制器_1_alu_src ),
    .B_In(mips_regifile_1_r2), .Beq_In(\单周期硬布线控制器_1_beq ), .Bne_In(\单周期硬布线控制器_1_bne ),
    .Imm_In(multiplexer_9_out), .JR_In(\单周期硬布线控制器_1_jr ), .JMP_In(\单周期硬布线控制器_1_jmp ), .JAL_In(ID_JAL),
    .SysCall_In(\单周期硬布线控制器_1_syscall ), .CLK(CLK), .\异步清零 (RST), .\使能端_低电平有效 (Halt), .IR_Out(EX_IR),
    .MemToReg_Out(id_ex_1_memtoreg_out), .RegWrite_Out(EX_RegWrite), .PC_4_Out(EX_PC_4),
    .MemWrite_Out(id_ex_1_memwrite_out), .AluOP_Out(AluOP), .A_Out(id_ex_1_a_out), .AluSrcB_Out(AluSrc),
    .B_Out(id_ex_1_b_out), .Beq_Out(Beq), .Bne_Out(Bne), .Imm_Out(id_ex_1_imm_out), .JR_Out(JR),
    .JMP_Out(JMP), .JAL_Out(id_ex_1_jal_out), .SysCall_Out(Syscall), .Shamt_In(multiplexer_10_out),
    .Shamt_Out(id_ex_1_shamt_out), .W__In(multiplexer_8_out), .W__Out(EX_WriteReg_num), .PC_In(ID_PC),
    .PC_Out(EX_PC), .\同步清零 (or_5_out), .J_In(adder_1_out), .J_Out(\J跳转地址 ), .Forward2_In(ID_Forward2),
    .Forward2_Out(id_ex_1_forward2_out), .Forward1_In(ID_Forward1), .Forward1_Out(id_ex_1_forward1_out),
    .PJ_eret_In(if_id_1_pj_out), .PJ_eret_Out(PredictJump));
  or or_5 (or_5_out, Fail, Load_Use);
  // Probe on M_PC[11:0]
  D_Flip_Flop #(.trigger("high")) d_ff_1 (.Q(d_ff_1_q));  // open: clk, D, Qn, preset, en, reset
  // Probe on 13'h344
  // Probe on WB_PC[11:0]
  Comparator #(.width(13)) comparator_3 (
    .a(CNT_num), .b(13'h344), .eq(comparator_3_eq), .lt(comparator_3_lt));  // open: gt
  Clock clock_1 (.out(clock_1_out));
  Multiplexer #(.select(2), .width(32), .enable("false")) multiplexer_11 (
    .in0(id_ex_1_b_out), .in1(WB_ALU), .in2(WB_MD), .in3(MEM_ALU), .out(multiplexer_11_out),
    .sel(id_ex_1_forward2_out));
  Shifter #(.width(32)) shifter_3 (.in(id_ex_1_imm_out), .\dist (5'b00010), .out(shifter_3_out));
  and and_5 (and_5_out, Equal, Beq);
  not not_6 (not_6_out, Equal);
  and and_6 (and_6_out, not_6_out, Bne);
  Comparator #(.width(32)) comparator_4 (.a(multiplexer_12_out), .b(32'h22), .eq(comparator_4_eq));  // open: gt, lt
  or or_6 (or_6_out, B, JMP);
  not not_7 (not_7_out, JR);
  nand nand_1 (nand_1_out, d_ff_1_q, comparator_3_eq);
  Counter #(.width(13), .max('h1fff), .ongoal("stay")) counter_1 (
    .count(comparator_3_lt), .Q(CNT_num), .clk(clock_1_out));  // open: load, D, carry, clr
  Multiplexer #(.select(2), .width(32), .enable("false")) multiplexer_12 (
    .in0(id_ex_1_a_out), .in1(WB_ALU), .in2(WB_MD), .in3(MEM_ALU), .out(multiplexer_12_out),
    .sel(id_ex_1_forward1_out));
  Multiplexer #(.width(32), .enable("false")) multiplexer_13 (
    .in0(multiplexer_11_out), .in1(id_ex_1_imm_out), .out(multiplexer_13_out), .sel(AluSrc));
  MIPS_ALU mips_alu_2 (
    .X(EX_PC_4), .Y(shifter_3_out), .AluOP(4'b0101), .Result(mips_alu_2_result));  // open: Equal, Result_2, shamt
  or or_7 (B, and_5_out, Blez, and_6_out);
  and and_7 (and_7_out, Syscall, not_8_out);
  not not_8 (not_8_out, comparator_4_eq);
  and and_8 (and_8_out, Syscall, comparator_4_eq);
  Comparator #(.width(6)) comparator_5 (.a(EX_IR[31:26]), .b(6'b000110), .eq(comparator_5_eq));  // open: gt, lt
  and and_9 (Blez, comparator_5_eq, not_9_out);
  not not_9 (not_9_out, comparator_6_gt);
  Comparator #(.width(32)) comparator_6 (.a(multiplexer_12_out), .b({32{1'b0}}), .gt(comparator_6_gt));  // open: eq, lt
  Comparator #(.width(1)) comparator_7 (.a(PredictJump), .b(and_10_out), .eq(comparator_7_eq));  // open: gt, lt
  and and_10 (and_10_out, or_6_out, not_7_out);
  assign CLK = nand_1_out ? clock_1_out : 1'bz;  // Controlled_Buffer controlled_buffer_1
  MIPS_ALU mips_alu_3 (
    .X(multiplexer_12_out), .Y(multiplexer_13_out), .AluOP(AluOP), .Equal(Equal), .Result(mips_alu_3_result),
    .shamt(id_ex_1_shamt_out));  // open: Result_2
  Multiplexer #(.width(32), .enable("false")) multiplexer_14 (
    .in0(PC_4), .in1(mips_alu_2_result), .out(multiplexer_14_out), .sel(B));
  Counter #(.width(1), .max('h1)) counter_2 (
    .load(and_7_out), .D(and_7_out), .count(1'b0), .Q(counter_2_q), .clk(CLK), .clr(or_8_out));  // open: carry
  or or_8 (or_8_out, Go, RST);
  Register #(.width(32)) register_1 (.D(multiplexer_11_out), .en(and_8_out), .Q(LedData), .clk(CLK), .clr(RST));
  not not_10 (Fail, comparator_7_eq);
  Pull_Resistor #(.pull(1)) pull_resistor_1 (.node(CLK));
  Multiplexer #(.width(32), .enable("false")) multiplexer_15 (
    .in0(multiplexer_16_out), .in1(\J跳转地址 ), .out(PC_B), .sel(and_11_out));
  Multiplexer #(.width(32), .enable("false")) multiplexer_16 (
    .in0(multiplexer_14_out), .in1(multiplexer_12_out), .out(multiplexer_16_out), .sel(JR));
  and and_11 (and_11_out, JMP, not_11_out);
  or or_9 (\气泡 , B, JMP);
  EX_MEM ex_mem_1 (
    .IR_In(EX_IR), .MemToReg_In(id_ex_1_memtoreg_out), .RegWrite_In(EX_RegWrite), .PC_4_In(EX_PC_4),
    .MemWrite_In(id_ex_1_memwrite_out), .B_In(multiplexer_11_out), .ALU_In(mips_alu_3_result), .CLK(CLK),
    .\异步清零 (RST), .\使能端_低电平有效 (Halt), .IR_Out(MEM_IR), .MemToReg_Out(MEM_MemToReg),
    .RegWrite_Out(MEM_RegWrite), .PC_4_Out(ex_mem_1_pc_4_out), .MemWrite_Out(MemWrite),
    .B_Out(ex_mem_1_b_out), .ALU_Out(MEM_ALU), .JAL_In(id_ex_1_jal_out), .JAL_Out(ex_mem_1_jal_out),
    .Halt_In(counter_2_q), .Halt_Out(ex_mem_1_halt_out), .W__In(EX_WriteReg_num), .W__Out(MEM_WriteReg_num),
    .PC_In(EX_PC), .PC_Out(M_PC));  // open: 同步清零, eret_In, PJ_eret_Out
  not not_11 (not_11_out, JR);
  and and_12 (and_12_out, CLK, not_12_out);
  not not_12 (not_12_out, Halt);
  Counter #(.width(16), .max('hffff)) counter_3 (
    .Q(\总周期数 ), .clk(and_12_out), .clr(RST));  // open: load, D, count, carry
  not not_13 (not_13_out, Halt);
  Comparator #(.width(6)) comparator_8 (.a(MEM_IR[31:26]), .b(6'b101001), .eq(comparator_8_eq));  // open: gt, lt
  RAM #(.addrWidth(10), .dataWidth(32), .bus("separate")) ram_1 (
    .addr(MEM_ALU[11:2]), .din(MDin), .data(MDout), .str(MemWrite), .sel(not_13_out), .clk(CLK), .clr(RST));  // open: ld
  Multiplexer #(.width(32), .enable("false")) multiplexer_17 (
    .in0(ex_mem_1_b_out), .in1({MDout[31:16], ex_mem_1_b_out[15:0]}), .out(MDin), .sel(comparator_8_eq));
  and and_13 (and_13_out, CLK, not_14_out);
  not not_14 (not_14_out, Halt);
  MEM_WB mem_wb_1 (
    .IR_In(MEM_IR), .MemToReg_In(MEM_MemToReg), .PC_4_In(ex_mem_1_pc_4_out), .ALU_In(MEM_ALU), .MD_In(MDout),
    .CLK(CLK), .\异步清零 (RST), .\使能端_低电平有效 (Halt), .IR_Out(WB_IR), .MemToReg_Out(MemToReg), .PC_4_Out(WB_PC_4),
    .ALU_Out(WB_ALU), .MD_Out(WB_MD), .RegWrite_In(MEM_RegWrite), .RegWrite_Out(RegWrite),
    .JAL_In(ex_mem_1_jal_out), .JAL_Out(JAL), .Halt_In(ex_mem_1_halt_out), .Halt_Out(Halt),
    .W__In(MEM_WriteReg_num), .W__Out(W_num), .PC_In(M_PC), .PC_Out(WB_PC));  // open: 同步清零, eret_In, eret_Out
  Counter #(.width(16), .max('hffff)) counter_4 (
    .count(JMP), .Q(\无条件分支数 ), .clk(and_13_out), .clr(RST));  // open: load, D, carry
  Multiplexer #(.width(32), .enable("false")) multiplexer_18 (
    .in0(WB_ALU), .in1(WB_MD), .out(multiplexer_18_out), .sel(MemToReg));
  and and_14 (and_14_out, CLK, not_15_out);
  not not_15 (not_15_out, Halt);
  Multiplexer #(.width(32), .enable("false")) multiplexer_19 (
    .in0(multiplexer_18_out), .in1(WB_PC_4), .out(RDin), .sel(JAL));
  Counter #(.width(16), .max('hffff)) counter_5 (
    .count(B), .Q(\条件分支成功数 ), .clk(and_14_out), .clr(RST));  // open: load, D, carry
  and and_15 (and_15_out, CLK, not_16_out);
  not not_16 (not_16_out, Halt);
  Counter #(.width(16), .max('hffff)) counter_6 (
    .count(Load_Use), .Q(\LoadUse次数 ), .clk(and_15_out), .clr(RST));  // open: load, D, carry

  // Other names for the same wires on the sheet: ID_IR[5:0] = Func; OP[5:0] = ID_IR[31:26]; MEM_PC[31:0] = M_PC;
  //   PC[31:0] = IF_PC

  // Notes on the sheet:
  //   中断源
  //   时空图监测，可删除
  //   中断等待指示
  //   contents of rom_1 (hex, n*v repeats v):
  //   20110001 8000c05 20110001 20120002 20130003 8000c09 20110001 20120002 20130003 8000c0d 20110001
  //   20120002 20130003 8000c11 20110001 20120002 20130003 c000cb8 20100001 20110001 118fc0 112020
  //   20020022 c 118882 12200001 8000c15 112020 20020022 c 20110001 118880 112020 20020022 c 12200001
  //   8000c1f 20110001 118fc0 112020 20020022 c 1188c3 112020 20020022 c 118903 112020 20020022 c 118903
  //   112020 20020022 c 118903 112020 20020022 c 118903 112020 20020022 c 118903 112020 20020022 c 118903
  //   112020 20020022 c 118903 112020 20020022 c 20100001 109fc0 139fc3 8021 2012000c 24160003 26100001
  //   3210000f 20080008 20090001 139900 2709825 132020 20020022 c 1094022 1500fff9 22100001 2018000f
  //   2188024 108700 20080008 20090001 139902 2709825 132021 20020022 c 1094022 1500fff9 108702 2c9b022
  //   12c00001 8000c50 4020 1084027 84400 3508ffff 82021 20020022 c 2010ffff 20110000 ae300000 22100001
  //   22310004 ae300000 22100001 22310004 ae300000 22100001 22310004 ae300000 22100001 22310004 ae300000
  //   22100001 22310004 ae300000 22100001 22310004 ae300000 22100001 22310004 ae300000 22100001 22310004
  //   ae300000 22100001 22310004 ae300000 22100001 22310004 ae300000 22100001 22310004 ae300000 22100001
  //   22310004 ae300000 22100001 22310004 ae300000 22100001 22310004 ae300000 22100001 22310004 ae300000
  //   22100001 22310004 22100001 8020 2011003c 8e130000 8e340000 274402a 11000002 ae330000 ae140000
  //   2231fffc 1611fff8 102020 20020022 c 22100004 2011003c 1611fff2 20020032 c 20100000 22100001 102020
  //   20020022 c 22100002 102020 20020022 c 22100003 102020 20020022 c 22100004 102020 20020022 c 22100005
  //   102020 20020022 c 22100006 102020 20020022 c 22100007 102020 20020022 c 22100008 102020 20020022
  //   20020022 c 3e00008
  //   数码管输出
  //   OP
  //   Func
  //   rs
  //   rt
  //   rd
  //   shamt
  //   立即数I
  //   立即数J
  //   控制位
  //   流水调试日志用
  //   暂停节拍，不能为0
  //   可计数暂停的时钟源
  //   为方便自动评测，需要输出流水线各段保存的PC值，注意是PC不是PC+4，另外ID段寄存器写入信息，Mem段内存写入信息也要输出
endmodule

module \封装正确性测试  (
);

  wire IR1, IR2, IR3, MemW, RegW;
  wire [31:0] EX_PC, ID_PC, IF_PC, IR, LED, MDin, MDinr, MEM_PC, PC, RDin, RDinr, WB_PC;

  \单周期MIPS  \u_单周期mips_1  (
    .RegWrite(RegW), .MemWrite(MemW), .PC(PC), .IR(IR), .RDin(RDin), .MDin(MDin), .LedData(LED));  // open: IR1, IR2, IR3
  \气泡流水线  \u_气泡流水线_1  (
    .RegWrite(RegW), .MemWrite(MemW), .IF_PC(IF_PC), .ID_PC(ID_PC), .EX_PC(EX_PC), .M_PC(MEM_PC),
    .WB_PC(WB_PC), .RDin(RDinr), .MDin(MDinr), .LedData(LED));
  \单周期MIPS_单级中断  \u_单周期mips_单级中断_1  (
    .IR1(IR1), .IR2(IR2), .IR3(IR3), .RegWrite(RegW), .MemWrite(MemW), .PC(PC), .IR(IR), .RDin(RDin),
    .MDin(MDin), .LedData(LED));
  \理想流水线  \u_理想流水线_1  (
    .RegWrite(RegW), .MemWrite(MemW), .IF_PC(IF_PC), .ID_PC(ID_PC), .EX_PC(EX_PC), .M_PC(MEM_PC),
    .WB_PC(WB_PC), .RDin(RDinr), .MDin(MDinr), .LedData(LED));
  \气泡流水线  \u_气泡流水线_2  (
    .RegWrite(RegW), .MemWrite(MemW), .IF_PC(IF_PC), .ID_PC(ID_PC), .EX_PC(EX_PC), .M_PC(MEM_PC),
    .WB_PC(WB_PC), .RDin(RDinr), .MDin(MDinr), .LedData(LED));
  \单周期MIPS_多级中断  \u_单周期mips_多级中断_1  (
    .IR1(IR1), .IR2(IR2), .IR3(IR3), .RegWrite(RegW), .MemWrite(MemW), .PC(PC), .IR(IR), .RDin(RDin),
    .MDin(MDin), .LedData(LED));

  // Notes on the sheet:
  //   单周期封装测试
  //   气泡流水封装测试
  //   单周期+单级中断封装测试
  //   请检查上面封装有无位宽不匹配，引脚标签是否和连接的标签相对应，否则无法在educoder平台上正确测试
  //   理想流水封装测试
  //   重定向流水封装测试
  //   单周期+多级中断封装测试
endmodule

module IF_ID (
  input  PJ_In,
  input  [31:0] PC_In,
  input  [31:0] IR_In,
  input  [31:0] PC_4_In,
  input  \同步清零 ,
  input  CLK,
  input  \异步清零 ,
  input  \使能端_低电平有效 ,
  output PJ_Out,
  output [31:0] PC_Out,
  output [31:0] IR_Out,
  output [31:0] PC_4_Out
);

  wire multiplexer_1_out, not_1_out;
  wire [31:0] multiplexer_2_out, multiplexer_3_out, multiplexer_4_out;

  not not_1 (not_1_out, \使能端_低电平有效 );
  Multiplexer #(.enable("false")) multiplexer_1 (.in0(PJ_In), .in1(1'b0), .out(multiplexer_1_out), .sel(\同步清零 ));
  Multiplexer #(.width(32), .enable("false")) multiplexer_2 (
    .in0(PC_In), .in1({32{1'b0}}), .out(multiplexer_2_out), .sel(\同步清零 ));
  Multiplexer #(.width(32), .enable("false")) multiplexer_3 (
    .in0(IR_In), .in1({32{1'b0}}), .out(multiplexer_3_out), .sel(\同步清零 ));
  Multiplexer #(.width(32), .enable("false")) multiplexer_4 (
    .in0(PC_4_In), .in1({32{1'b0}}), .out(multiplexer_4_out), .sel(\同步清零 ));
  Pull_Resistor pull_resistor_1 (.node(\同步清零 ));
  Register #(.width(1)) register_1 (.D(multiplexer_1_out), .en(not_1_out), .Q(PJ_Out), .clk(CLK), .clr(\异步清零 ));
  Register #(.width(32)) register_2 (.D(multiplexer_2_out), .en(not_1_out), .Q(PC_Out), .clk(CLK), .clr(\异步清零 ));
  Register #(.width(32)) register_3 (.D(multiplexer_3_out), .en(not_1_out), .Q(IR_Out), .clk(CLK), .clr(\异步清零 ));
  Register #(.width(32)) register_4 (.D(multiplexer_4_out), .en(not_1_out), .Q(PC_4_Out), .clk(CLK), .clr(\异步清零 ));
endmodule

module ID_EX (
  input  [1:0] Forward1_In,
  input  PJ_eret_In,
  input  [1:0] Forward2_In,
  input  [31:0] PC_In,
  input  [31:0] J_In,
  input  [31:0] IR_In,
  input  MemToReg_In,
  input  RegWrite_In,
  input  [31:0] PC_4_In,
  input  MemWrite_In,
  input  [3:0] AluOP_In,
  input  [31:0] A_In,
  input  AluSrcB_In,
  input  [31:0] B_In,
  input  Beq_In,
  input  Bne_In,
  input  [31:0] Imm_In,
  input  JR_In,
  input  [4:0] Shamt_In,
  input  JMP_In,
  input  [4:0] W__In,
  input  JAL_In,
  input  SysCall_In,
  input  \同步清零 ,
  input  CLK,
  input  \异步清零 ,
  input  \使能端_低电平有效 ,
  output [1:0] Forward1_Out,
  output PJ_eret_Out,
  output [1:0] Forward2_Out,
  output [31:0] PC_Out,
  output [31:0] J_Out,
  output [31:0] IR_Out,
  output MemToReg_Out,
  output RegWrite_Out,
  output [31:0] PC_4_Out,
  output MemWrite_Out,
  output [3:0] AluOP_Out,
  output [31:0] A_Out,
  output AluSrcB_Out,
  output [31:0] B_Out,
  output Beq_Out,
  output Bne_Out,
  output [31:0] Imm_Out,
  output JR_Out,
  output [4:0] Shamt_Out,
  output JMP_Out,
  output [4:0] W__Out,
  output JAL_Out,
  output SysCall_Out
);

  wire multiplexer_1_out, multiplexer_13_out, multiplexer_14_out, multiplexer_15_out, multiplexer_17_out,
       multiplexer_18_out, multiplexer_19_out, multiplexer_20_out, multiplexer_21_out, multiplexer_22_out,
       multiplexer_23_out, not_1_out;
  wire [1:0] multiplexer_10_out, multiplexer_11_out;
  wire [3:0] multiplexer_16_out;
  wire [4:0] multiplexer_8_out, multiplexer_9_out;
  wire [31:0] multiplexer_2_out, multiplexer_3_out, multiplexer_4_out, multiplexer_5_out, multiplexer_6_out,
       multiplexer_7_out, multiplexer_12_out;

  not not_1 (not_1_out, \使能端_低电平有效 );
  Multiplexer #(.enable("false")) multiplexer_1 (.in0(PJ_eret_In), .in1(1'b0), .out(multiplexer_1_out), .sel(\同步清零 ));
  Multiplexer #(.width(32), .enable("false")) multiplexer_2 (
    .in0(PC_In), .in1({32{1'b0}}), .out(multiplexer_2_out), .sel(\同步清零 ));
  Multiplexer #(.width(32), .enable("false")) multiplexer_3 (
    .in0(IR_In), .in1({32{1'b0}}), .out(multiplexer_3_out), .sel(\同步清零 ));
  Multiplexer #(.width(32), .enable("false")) multiplexer_4 (
    .in0(PC_4_In), .in1({32{1'b0}}), .out(multiplexer_4_out), .sel(\同步清零 ));
  Multiplexer #(.width(32), .enable("false")) multiplexer_5 (
    .in0(A_In), .in1({32{1'b0}}), .out(multiplexer_5_out), .sel(\同步清零 ));
  Multiplexer #(.width(32), .enable("false")) multiplexer_6 (
    .in0(B_In), .in1({32{1'b0}}), .out(multiplexer_6_out), .sel(\同步清零 ));
  Multiplexer #(.width(32), .enable("false")) multiplexer_7 (
    .in0(Imm_In), .in1({32{1'b0}}), .out(multiplexer_7_out), .sel(\同步清零 ));
  Multiplexer #(.width(5), .enable("false")) multiplexer_8 (
    .in0(Shamt_In), .in1({5{1'b0}}), .out(multiplexer_8_out), .sel(\同步清零 ));
  Multiplexer #(.width(5), .enable("false")) multiplexer_9 (
    .in0(W__In), .in1({5{1'b0}}), .out(multiplexer_9_out), .sel(\同步清零 ));
  Pull_Resistor pull_resistor_1 (.node(\同步清零 ));
  Register #(.width(1)) register_1 (.D(multiplexer_1_out), .en(not_1_out), .Q(PJ_eret_Out), .clk(CLK), .clr(\异步清零 ));
  Register #(.width(32)) register_2 (.D(multiplexer_2_out), .en(not_1_out), .Q(PC_Out), .clk(CLK), .clr(\异步清零 ));
  Register #(.width(32)) register_3 (.D(multiplexer_3_out), .en(not_1_out), .Q(IR_Out), .clk(CLK), .clr(\异步清零 ));
  Register #(.width(32)) register_4 (.D(multiplexer_4_out), .en(not_1_out), .Q(PC_4_Out), .clk(CLK), .clr(\异步清零 ));
  Register #(.width(32)) register_5 (.D(multiplexer_5_out), .en(not_1_out), .Q(A_Out), .clk(CLK), .clr(\异步清零 ));
  Register #(.width(32)) register_6 (.D(multiplexer_6_out), .en(not_1_out), .Q(B_Out), .clk(CLK), .clr(\异步清零 ));
  Register #(.width(32)) register_7 (.D(multiplexer_7_out), .en(not_1_out), .Q(Imm_Out), .clk(CLK), .clr(\异步清零 ));
  Register #(.width(5)) register_8 (.D(multiplexer_8_out), .en(not_1_out), .Q(Shamt_Out), .clk(CLK), .clr(\异步清零 ));
  Register #(.width(5)) register_9 (.D(multiplexer_9_out), .en(not_1_out), .Q(W__Out), .clk(CLK), .clr(\异步清零 ));
  Multiplexer #(.width(2), .enable("false")) multiplexer_10 (
    .in0(Forward1_In), .in1(2'b00), .out(multiplexer_10_out), .sel(\同步清零 ));
  Multiplexer #(.width(2), .enable("false")) multiplexer_11 (
    .in0(Forward2_In), .in1(2'b00), .out(multiplexer_11_out), .sel(\同步清零 ));
  Multiplexer #(.width(32), .enable("false")) multiplexer_12 (
    .in0(J_In), .in1({32{1'b0}}), .out(multiplexer_12_out), .sel(\同步清零 ));
  Multiplexer #(.enable("false")) multiplexer_13 (
    .in0(MemToReg_In), .in1(1'b0), .out(multiplexer_13_out), .sel(\同步清零 ));
  Multiplexer #(.enable("false")) multiplexer_14 (
    .in0(RegWrite_In), .in1(1'b0), .out(multiplexer_14_out), .sel(\同步清零 ));
  Multiplexer #(.enable("false")) multiplexer_15 (
    .in0(MemWrite_In), .in1(1'b0), .out(multiplexer_15_out), .sel(\同步清零 ));
  Multiplexer #(.width(4), .enable("false")) multiplexer_16 (
    .in0(AluOP_In), .in1(4'b0000), .out(multiplexer_16_out), .sel(\同步清零 ));
  Multiplexer #(.enable("false")) multiplexer_17 (.in0(AluSrcB_In), .in1(1'b0), .out(multiplexer_17_out), .sel(\同步清零 ));
  Multiplexer #(.enable("false")) multiplexer_18 (.in0(Beq_In), .in1(1'b0), .out(multiplexer_18_out), .sel(\同步清零 ));
  Multiplexer #(.enable("false")) multiplexer_19 (.in0(Bne_In), .in1(1'b0), .out(multiplexer_19_out), .sel(\同步清零 ));
  Multiplexer #(.enable("false")) multiplexer_20 (.in0(JR_In), .in1(1'b0), .out(multiplexer_20_out), .sel(\同步清零 ));
  Multiplexer #(.enable("false")) multiplexer_21 (.in0(JMP_In), .in1(1'b0), .out(multiplexer_21_out), .sel(\同步清零 ));
  Multiplexer #(.enable("false")) multiplexer_22 (.in0(JAL_In), .in1(1'b0), .out(multiplexer_22_out), .sel(\同步清零 ));
  Multiplexer #(.enable("false")) multiplexer_23 (.in0(SysCall_In), .in1(1'b0), .out(multiplexer_23_out), .sel(\同步清零 ));
  Register #(.width(2)) register_10 (.D(multiplexer_10_out), .en(not_1_out), .Q(Forward1_Out), .clk(CLK), .clr(\异步清零 ));
  Register #(.width(2)) register_11 (.D(multiplexer_11_out), .en(not_1_out), .Q(Forward2_Out), .clk(CLK), .clr(\异步清零 ));
  Register #(.width(32)) register_12 (.D(multiplexer_12_out), .en(not_1_out), .Q(J_Out), .clk(CLK), .clr(\异步清零 ));
  Register #(.width(1)) register_13 (.D(multiplexer_13_out), .en(not_1_out), .Q(MemToReg_Out), .clk(CLK), .clr(\异步清零 ));
  Register #(.width(1)) register_14 (.D(multiplexer_14_out), .en(not_1_out), .Q(RegWrite_Out), .clk(CLK), .clr(\异步清零 ));
  Register #(.width(1)) register_15 (.D(multiplexer_15_out), .en(not_1_out), .Q(MemWrite_Out), .clk(CLK), .clr(\异步清零 ));
  Register #(.width(4)) register_16 (.D(multiplexer_16_out), .en(not_1_out), .Q(AluOP_Out), .clk(CLK), .clr(\异步清零 ));
  Register #(.width(1)) register_17 (.D(multiplexer_17_out), .en(not_1_out), .Q(AluSrcB_Out), .clk(CLK), .clr(\异步清零 ));
  Register #(.width(1)) register_18 (.D(multiplexer_18_out), .en(not_1_out), .Q(Beq_Out), .clk(CLK), .clr(\异步清零 ));
  Register #(.width(1)) register_19 (.D(multiplexer_19_out), .en(not_1_out), .Q(Bne_Out), .clk(CLK), .clr(\异步清零 ));
  Register #(.width(1)) register_20 (.D(multiplexer_20_out), .en(not_1_out), .Q(JR_Out), .clk(CLK), .clr(\异步清零 ));
  Register #(.width(1)) register_21 (.D(multiplexer_21_out), .en(not_1_out), .Q(JMP_Out), .clk(CLK), .clr(\异步清零 ));
  Register #(.width(1)) register_22 (.D(multiplexer_22_out), .en(not_1_out), .Q(JAL_Out), .clk(CLK), .clr(\异步清零 ));
  Register #(.width(1)) register_23 (.D(multiplexer_23_out), .en(not_1_out), .Q(SysCall_Out), .clk(CLK), .clr(\异步清零 ));
endmodule

module EX_MEM (
  input  [31:0] PC_In,
  input  eret_In,
  input  [31:0] IR_In,
  input  MemToReg_In,
  input  RegWrite_In,
  input  [31:0] PC_4_In,
  input  MemWrite_In,
  input  JAL_In,
  input  [31:0] B_In,
  input  Halt_In,
  input  [31:0] ALU_In,
  input  [4:0] W__In,
  input  \同步清零 ,
  input  CLK,
  input  \异步清零 ,
  input  \使能端_低电平有效 ,
  output [31:0] PC_Out,
  output PJ_eret_Out,
  output [31:0] IR_Out,
  output MemToReg_Out,
  output RegWrite_Out,
  output [31:0] PC_4_Out,
  output MemWrite_Out,
  output JAL_Out,
  output [31:0] B_Out,
  output Halt_Out,
  output [31:0] ALU_Out,
  output [4:0] W__Out
);

  wire multiplexer_6_out, multiplexer_7_out, multiplexer_8_out, multiplexer_9_out, multiplexer_10_out,
       multiplexer_11_out, not_1_out;
  wire [4:0] multiplexer_12_out;
  wire [31:0] multiplexer_1_out, multiplexer_2_out, multiplexer_3_out, multiplexer_4_out, multiplexer_5_out;

  not not_1 (not_1_out, \使能端_低电平有效 );
  Multiplexer #(.width(32), .enable("false")) multiplexer_1 (
    .in0(PC_In), .in1({32{1'b0}}), .out(multiplexer_1_out), .sel(\同步清零 ));
  Multiplexer #(.width(32), .enable("false")) multiplexer_2 (
    .in0(IR_In), .in1({32{1'b0}}), .out(multiplexer_2_out), .sel(\同步清零 ));
  Multiplexer #(.width(32), .enable("false")) multiplexer_3 (
    .in0(PC_4_In), .in1({32{1'b0}}), .out(multiplexer_3_out), .sel(\同步清零 ));
  Multiplexer #(.width(32), .enable("false")) multiplexer_4 (
    .in0(B_In), .in1({32{1'b0}}), .out(multiplexer_4_out), .sel(\同步清零 ));
  Multiplexer #(.width(32), .enable("false")) multiplexer_5 (
    .in0(ALU_In), .in1({32{1'b0}}), .out(multiplexer_5_out), .sel(\同步清零 ));
  Pull_Resistor pull_resistor_1 (.node(\同步清零 ));
  Register #(.width(32)) register_1 (.D(multiplexer_1_out), .en(not_1_out), .Q(PC_Out), .clk(CLK), .clr(\异步清零 ));
  Register #(.width(32)) register_2 (.D(multiplexer_2_out), .en(not_1_out), .Q(IR_Out), .clk(CLK), .clr(\异步清零 ));
  Register #(.width(32)) register_3 (.D(multiplexer_3_out), .en(not_1_out), .Q(PC_4_Out), .clk(CLK), .clr(\异步清零 ));
  Register #(.width(32)) register_4 (.D(multiplexer_4_out), .en(not_1_out), .Q(B_Out), .clk(CLK), .clr(\异步清零 ));
  Register #(.width(32)) register_5 (.D(multiplexer_5_out), .en(not_1_out), .Q(ALU_Out), .clk(CLK), .clr(\异步清零 ));
  Multiplexer #(.enable("false")) multiplexer_6 (.in0(eret_In), .in1(1'b0), .out(multiplexer_6_out), .sel(\同步清零 ));
  Multiplexer #(.enable("false")) multiplexer_7 (.in0(MemToReg_In), .in1(1'b0), .out(multiplexer_7_out), .sel(\同步清零 ));
  Multiplexer #(.enable("false")) multiplexer_8 (.in0(RegWrite_In), .in1(1'b0), .out(multiplexer_8_out), .sel(\同步清零 ));
  Multiplexer #(.enable("false")) multiplexer_9 (.in0(MemWrite_In), .in1(1'b0), .out(multiplexer_9_out), .sel(\同步清零 ));
  Multiplexer #(.enable("false")) multiplexer_10 (.in0(JAL_In), .in1(1'b0), .out(multiplexer_10_out), .sel(\同步清零 ));
  Multiplexer #(.enable("false")) multiplexer_11 (.in0(Halt_In), .in1(1'b0), .out(multiplexer_11_out), .sel(\同步清零 ));
  Multiplexer #(.width(5), .enable("false")) multiplexer_12 (
    .in0(W__In), .in1({5{1'b0}}), .out(multiplexer_12_out), .sel(\同步清零 ));
  Register #(.width(1)) register_6 (.D(multiplexer_6_out), .en(not_1_out), .Q(PJ_eret_Out), .clk(CLK), .clr(\异步清零 ));
  Register #(.width(1)) register_7 (.D(multiplexer_7_out), .en(not_1_out), .Q(MemToReg_Out), .clk(CLK), .clr(\异步清零 ));
  Register #(.width(1)) register_8 (.D(multiplexer_8_out), .en(not_1_out), .Q(RegWrite_Out), .clk(CLK), .clr(\异步清零 ));
  Register #(.width(1)) register_9 (.D(multiplexer_9_out), .en(not_1_out), .Q(MemWrite_Out), .clk(CLK), .clr(\异步清零 ));
  Register #(.width(1)) register_10 (.D(multiplexer_10_out), .en(not_1_out), .Q(JAL_Out), .clk(CLK), .clr(\异步清零 ));
  Register #(.width(1)) register_11 (.D(multiplexer_11_out), .en(not_1_out), .Q(Halt_Out), .clk(CLK), .clr(\异步清零 ));
  Register #(.width(5)) register_12 (.D(multiplexer_12_out), .en(not_1_out), .Q(W__Out), .clk(CLK), .clr(\异步清零 ));
endmodule

module MEM_WB (
  input  [31:0] PC_In,
  input  eret_In,
  input  [31:0] IR_In,
  input  MemToReg_In,
  input  RegWrite_In,
  input  [31:0] PC_4_In,
  input  JAL_In,
  input  Halt_In,
  input  [31:0] ALU_In,
  input  [4:0] W__In,
  input  [31:0] MD_In,
  input  \同步清零 ,
  input  CLK,
  input  \异步清零 ,
  input  \使能端_低电平有效 ,
  output [31:0] PC_Out,
  output eret_Out,
  output [31:0] IR_Out,
  output MemToReg_Out,
  output RegWrite_Out,
  output [31:0] PC_4_Out,
  output JAL_Out,
  output Halt_Out,
  output [31:0] ALU_Out,
  output [4:0] W__Out,
  output [31:0] MD_Out
);

  wire multiplexer_6_out, multiplexer_7_out, multiplexer_8_out, multiplexer_9_out, multiplexer_10_out,
       not_1_out;
  wire [4:0] multiplexer_11_out;
  wire [31:0] multiplexer_1_out, multiplexer_2_out, multiplexer_3_out, multiplexer_4_out, multiplexer_5_out;

  not not_1 (not_1_out, \使能端_低电平有效 );
  Multiplexer #(.width(32), .enable("false")) multiplexer_1 (
    .in0(PC_In), .in1({32{1'b0}}), .out(multiplexer_1_out), .sel(\同步清零 ));
  Multiplexer #(.width(32), .enable("false")) multiplexer_2 (
    .in0(IR_In), .in1({32{1'b0}}), .out(multiplexer_2_out), .sel(\同步清零 ));
  Multiplexer #(.width(32), .enable("false")) multiplexer_3 (
    .in0(PC_4_In), .in1({32{1'b0}}), .out(multiplexer_3_out), .sel(\同步清零 ));
  Multiplexer #(.width(32), .enable("false")) multiplexer_4 (
    .in0(ALU_In), .in1({32{1'b0}}), .out(multiplexer_4_out), .sel(\同步清零 ));
  Multiplexer #(.width(32), .enable("false")) multiplexer_5 (
    .in0(MD_In), .in1({32{1'b0}}), .out(multiplexer_5_out), .sel(\同步清零 ));
  Pull_Resistor pull_resistor_1 (.node(\同步清零 ));
  Register #(.width(32)) register_1 (.D(multiplexer_1_out), .en(not_1_out), .Q(PC_Out), .clk(CLK), .clr(\异步清零 ));
  Register #(.width(32)) register_2 (.D(multiplexer_2_out), .en(not_1_out), .Q(IR_Out), .clk(CLK), .clr(\异步清零 ));
  Register #(.width(32)) register_3 (.D(multiplexer_3_out), .en(not_1_out), .Q(PC_4_Out), .clk(CLK), .clr(\异步清零 ));
  Register #(.width(32)) register_4 (.D(multiplexer_4_out), .en(not_1_out), .Q(ALU_Out), .clk(CLK), .clr(\异步清零 ));
  Register #(.width(32)) register_5 (.D(multiplexer_5_out), .en(not_1_out), .Q(MD_Out), .clk(CLK), .clr(\异步清零 ));
  Multiplexer #(.enable("false")) multiplexer_6 (.in0(eret_In), .in1(1'b0), .out(multiplexer_6_out), .sel(\同步清零 ));
  Multiplexer #(.enable("false")) multiplexer_7 (.in0(MemToReg_In), .in1(1'b0), .out(multiplexer_7_out), .sel(\同步清零 ));
  Multiplexer #(.enable("false")) multiplexer_8 (.in0(RegWrite_In), .in1(1'b0), .out(multiplexer_8_out), .sel(\同步清零 ));
  Multiplexer #(.enable("false")) multiplexer_9 (.in0(JAL_In), .in1(1'b0), .out(multiplexer_9_out), .sel(\同步清零 ));
  Multiplexer #(.enable("false")) multiplexer_10 (.in0(Halt_In), .in1(1'b0), .out(multiplexer_10_out), .sel(\同步清零 ));
  Multiplexer #(.width(5), .enable("false")) multiplexer_11 (
    .in0(W__In), .in1({5{1'b0}}), .out(multiplexer_11_out), .sel(\同步清零 ));
  Register #(.width(1)) register_6 (.D(multiplexer_6_out), .en(not_1_out), .Q(eret_Out), .clk(CLK), .clr(\异步清零 ));
  Register #(.width(1)) register_7 (.D(multiplexer_7_out), .en(not_1_out), .Q(MemToReg_Out), .clk(CLK), .clr(\异步清零 ));
  Register #(.width(1)) register_8 (.D(multiplexer_8_out), .en(not_1_out), .Q(RegWrite_Out), .clk(CLK), .clr(\异步清零 ));
  Register #(.width(1)) register_9 (.D(multiplexer_9_out), .en(not_1_out), .Q(JAL_Out), .clk(CLK), .clr(\异步清零 ));
  Register #(.width(1)) register_10 (.D(multiplexer_10_out), .en(not_1_out), .Q(Halt_Out), .clk(CLK), .clr(\异步清零 ));
  Register #(.width(5)) register_11 (.D(multiplexer_11_out), .en(not_1_out), .Q(W__Out), .clk(CLK), .clr(\异步清零 ));
endmodule

module \源寄存器使用情况  (
  input  OP0,
  input  OP1,
  input  OP2,
  input  OP3,
  input  OP4,
  input  OP5,
  input  F0,
  input  F1,
  input  F2,
  input  F3,
  input  F4,
  input  F5,
  output R1_Used,
  output R2_Used
);

  wire and_1_out, and_2_out, and_3_out, and_4_out, and_5_out, and_6_out, and_7_out, and_8_out, and_9_out,
       and_10_out, and_11_out, and_12_out, and_13_out, and_14_out, and_15_out, and_16_out, and_17_out,
       and_18_out, and_19_out, and_20_out, not_1_out, not_2_out, not_3_out, not_4_out, not_5_out, not_6_out,
       not_7_out, not_8_out, not_9_out, not_10_out, not_11_out, not_12_out, not_13_out, not_14_out,
       not_15_out, not_16_out, not_17_out, not_18_out, not_19_out, not_20_out, not_21_out, not_22_out,
       not_23_out, not_24_out, not_25_out, not_26_out, not_27_out, not_28_out, not_29_out, not_30_out,
       not_31_out, not_32_out, not_33_out, not_34_out, not_35_out, not_36_out, not_37_out, not_38_out,
       not_39_out, not_40_out, not_41_out, not_42_out, not_43_out, not_44_out, not_45_out, not_46_out,
       not_47_out, not_48_out, not_49_out, not_50_out, not_51_out, not_52_out, not_53_out, not_54_out,
       not_55_out, not_56_out, not_57_out, not_58_out, not_59_out, not_60_out, not_61_out, not_62_out,
       not_63_out, not_64_out, not_65_out, not_66_out, not_67_out, not_68_out, not_69_out, not_70_out,
       not_71_out, not_72_out, not_73_out, not_74_out, not_75_out, not_76_out, not_77_out, not_78_out,
       not_79_out, not_80_out, not_81_out, not_82_out, not_83_out, not_84_out, not_85_out, not_86_out,
       not_87_out, not_88_out, not_89_out, not_90_out, not_91_out, not_92_out, not_93_out, not_94_out,
       not_95_out, not_96_out, not_97_out, not_98_out, not_99_out, not_100_out, not_101_out, not_102_out,
       not_103_out, not_104_out, not_105_out, not_106_out, not_107_out, not_108_out, not_109_out,
       not_110_out, not_111_out, not_112_out, not_113_out, not_114_out, not_115_out, not_116_out,
       not_117_out, not_118_out, not_119_out, not_120_out, not_121_out, not_122_out, not_123_out;

  not not_1 (not_1_out, OP0);
  not not_2 (not_2_out, OP1);
  not not_3 (not_3_out, OP4);
  not not_4 (not_4_out, OP5);
  not not_5 (not_5_out, F0);
  not not_6 (not_6_out, F2);
  not not_7 (not_7_out, F3);
  not not_8 (not_8_out, F4);
  not not_9 (not_9_out, OP0);
  not not_10 (not_10_out, OP1);
  not not_11 (not_11_out, OP4);
  not not_12 (not_12_out, OP5);
  not not_13 (not_13_out, F1);
  not not_14 (not_14_out, F3);
  not not_15 (not_15_out, F4);
  not not_16 (not_16_out, OP0);
  not not_17 (not_17_out, OP1);
  not not_18 (not_18_out, OP4);
  not not_19 (not_19_out, OP5);
  not not_20 (not_20_out, F0);
  not not_21 (not_21_out, F1);
  not not_22 (not_22_out, F4);
  not not_23 (not_23_out, F5);
  not not_24 (not_24_out, OP0);
  not not_25 (not_25_out, OP1);
  not not_26 (not_26_out, OP4);
  not not_27 (not_27_out, OP5);
  not not_28 (not_28_out, F0);
  not not_29 (not_29_out, F3);
  not not_30 (not_30_out, F4);
  not not_31 (not_31_out, F5);
  not not_32 (not_32_out, OP0);
  not not_33 (not_33_out, OP1);
  not not_34 (not_34_out, OP4);
  not not_35 (not_35_out, OP5);
  not not_36 (not_36_out, F2);
  not not_37 (not_37_out, F4);
  not not_38 (not_38_out, OP0);
  not not_39 (not_39_out, OP1);
  not not_40 (not_40_out, OP4);
  not not_41 (not_41_out, OP5);
  not not_42 (not_42_out, F3);
  not not_43 (not_43_out, F4);
  not not_44 (not_44_out, OP0);
  not not_45 (not_45_out, OP2);
  not not_46 (not_46_out, OP4);
  not not_47 (not_47_out, OP5);
  not not_48 (not_48_out, OP0);
  not not_49 (not_49_out, OP3);
  not not_50 (not_50_out, OP4);
  not not_51 (not_51_out, OP5);
  not not_52 (not_52_out, OP1);
  not not_53 (not_53_out, OP4);
  not not_54 (not_54_out, OP5);
  not not_55 (not_55_out, OP1);
  not not_56 (not_56_out, OP2);
  not not_57 (not_57_out, OP4);
  not not_58 (not_58_out, OP2);
  not not_59 (not_59_out, OP4);
  not not_60 (not_60_out, OP0);
  not not_61 (not_61_out, OP1);
  not not_62 (not_62_out, OP3);
  not not_63 (not_63_out, OP4);
  not not_64 (not_64_out, OP5);
  not not_65 (not_65_out, F0);
  not not_66 (not_66_out, F2);
  not not_67 (not_67_out, F3);
  not not_68 (not_68_out, F4);
  not not_69 (not_69_out, OP0);
  not not_70 (not_70_out, OP1);
  not not_71 (not_71_out, OP3);
  not not_72 (not_72_out, OP4);
  not not_73 (not_73_out, OP5);
  not not_74 (not_74_out, F0);
  not not_75 (not_75_out, F3);
  not not_76 (not_76_out, F4);
  not not_77 (not_77_out, F5);
  not not_78 (not_78_out, OP0);
  not not_79 (not_79_out, OP1);
  not not_80 (not_80_out, OP3);
  not not_81 (not_81_out, OP4);
  not not_82 (not_82_out, OP5);
  not not_83 (not_83_out, F1);
  not not_84 (not_84_out, F3);
  not not_85 (not_85_out, F4);
  not not_86 (not_86_out, OP0);
  not not_87 (not_87_out, OP1);
  not not_88 (not_88_out, OP3);
  not not_89 (not_89_out, OP4);
  not not_90 (not_90_out, OP5);
  not not_91 (not_91_out, F0);
  not not_92 (not_92_out, F1);
  not not_93 (not_93_out, F4);
  not not_94 (not_94_out, F5);
  not not_95 (not_95_out, OP0);
  not not_96 (not_96_out, OP1);
  not not_97 (not_97_out, OP3);
  not not_98 (not_98_out, OP4);
  not not_99 (not_99_out, OP5);
  not not_100 (not_100_out, F2);
  not not_101 (not_101_out, F3);
  not not_102 (not_102_out, F4);
  not not_103 (not_103_out, F5);
  not not_104 (not_104_out, OP0);
  not not_105 (not_105_out, OP1);
  not not_106 (not_106_out, OP3);
  not not_107 (not_107_out, OP4);
  not not_108 (not_108_out, OP5);
  not not_109 (not_109_out, F2);
  not not_110 (not_110_out, F4);
  not not_111 (not_111_out, OP0);
  not not_112 (not_112_out, OP1);
  not not_113 (not_113_out, OP3);
  not not_114 (not_114_out, OP4);
  not not_115 (not_115_out, OP5);
  not not_116 (not_116_out, F3);
  not not_117 (not_117_out, F4);
  not not_118 (not_118_out, OP1);
  not not_119 (not_119_out, OP3);
  not not_120 (not_120_out, OP4);
  not not_121 (not_121_out, OP5);
  not not_122 (not_122_out, OP2);
  not not_123 (not_123_out, OP4);
  and and_1 (and_1_out, not_1_out, not_2_out, not_3_out, not_4_out, not_5_out, not_6_out, not_7_out, not_8_out, F5);
  and and_2 (and_2_out, not_9_out, not_10_out, not_11_out, not_12_out, not_13_out, not_14_out, not_15_out, F5);
  and and_3 (and_3_out, not_16_out, not_17_out, not_18_out, not_19_out, not_20_out, not_21_out, F3, not_22_out, not_23_out);
  and and_4 (and_4_out, not_24_out, not_25_out, not_26_out, not_27_out, not_28_out, F2, not_29_out, not_30_out, not_31_out);
  and and_5 (and_5_out, not_32_out, not_33_out, not_34_out, not_35_out, F1, not_36_out, F3, not_37_out, F5);
  and and_6 (and_6_out, not_38_out, not_39_out, not_40_out, not_41_out, F0, F2, not_42_out, not_43_out, F5);
  and and_7 (and_7_out, not_44_out, not_45_out, OP3, not_46_out, not_47_out);
  and and_8 (and_8_out, not_48_out, OP2, not_49_out, not_50_out, not_51_out);
  and and_9 (and_9_out, not_52_out, OP2, not_53_out, not_54_out);
  and and_10 (and_10_out, OP0, not_55_out, not_56_out, OP3, not_57_out);
  and and_11 (and_11_out, OP0, OP1, not_58_out, not_59_out, OP5);
  and and_12 (and_12_out, not_60_out, not_61_out, not_62_out, not_63_out, not_64_out, not_65_out, not_66_out, not_67_out, not_68_out);
  and and_13 (and_13_out, not_69_out, not_70_out, not_71_out, not_72_out, not_73_out, not_74_out, not_75_out, not_76_out, not_77_out);
  and and_14 (and_14_out, not_78_out, not_79_out, not_80_out, not_81_out, not_82_out, not_83_out, not_84_out, not_85_out, F5);
  and and_15 (and_15_out, not_86_out, not_87_out, not_88_out, not_89_out, not_90_out, not_91_out, not_92_out, F2, not_93_out, not_94_out);
  and and_16 (and_16_out, not_95_out, not_96_out, not_97_out, not_98_out, not_99_out, F1, not_100_out, not_101_out, not_102_out, not_103_out);
  and and_17 (and_17_out, not_104_out, not_105_out, not_106_out, not_107_out, not_108_out, F1, not_109_out, F3, not_110_out, F5);
  and and_18 (and_18_out, not_111_out, not_112_out, not_113_out, not_114_out, not_115_out, F0, F2, not_116_out, not_117_out, F5);
  and and_19 (and_19_out, not_118_out, OP2, not_119_out, not_120_out, not_121_out);
  and and_20 (and_20_out, OP0, not_122_out, OP3, not_123_out, OP5);
  or or_1 (R1_Used, and_1_out, and_2_out, and_3_out, and_4_out, and_5_out, and_6_out, and_7_out, and_8_out, and_9_out, and_10_out, and_11_out);
  or or_2 (R2_Used, and_12_out, and_13_out, and_14_out, and_15_out, and_16_out, and_17_out, and_18_out, and_19_out, and_20_out);
endmodule

module \数据相关检测  (
  input  R1_Used,
  input  R2_Used,
  input  EX_RegWrite,
  input  MEM_RegWrite,
  input  [4:0] R1_num,
  input  [4:0] R2_num,
  input  [4:0] EX_WriteReg_num,
  input  [4:0] MEM_WriteReg_num,
  output Pause
);

  wire and_1_out, and_2_out, and_3_out, and_4_out, and_5_out, and_6_out, comparator_1_eq, comparator_2_eq,
       comparator_3_eq, comparator_4_eq, comparator_5_eq, comparator_6_eq, comparator_7_eq, comparator_8_eq,
       not_1_out, not_2_out, not_3_out, not_4_out, or_1_out, or_2_out;

  not not_1 (not_1_out, comparator_1_eq);
  Comparator #(.width(5)) comparator_1 (.a(R1_num), .b({5{1'b0}}), .eq(comparator_1_eq));  // open: gt, lt
  Comparator #(.width(5)) comparator_2 (.a(R1_num), .b(EX_WriteReg_num), .eq(comparator_2_eq));  // open: gt, lt
  not not_2 (not_2_out, comparator_3_eq);
  Comparator #(.width(5)) comparator_3 (.a(R2_num), .b({5{1'b0}}), .eq(comparator_3_eq));  // open: gt, lt
  Comparator #(.width(5)) comparator_4 (.a(R2_num), .b(EX_WriteReg_num), .eq(comparator_4_eq));  // open: gt, lt
  not not_3 (not_3_out, comparator_5_eq);
  Comparator #(.width(5)) comparator_5 (.a(R1_num), .b({5{1'b0}}), .eq(comparator_5_eq));  // open: gt, lt
  Comparator #(.width(5)) comparator_6 (.a(R1_num), .b(MEM_WriteReg_num), .eq(comparator_6_eq));  // open: gt, lt
  Comparator #(.width(5)) comparator_7 (.a(R2_num), .b({5{1'b0}}), .eq(comparator_7_eq));  // open: gt, lt
  not not_4 (not_4_out, comparator_7_eq);
  Comparator #(.width(5)) comparator_8 (.a(R2_num), .b(MEM_WriteReg_num), .eq(comparator_8_eq));  // open: gt, lt
  and and_1 (and_1_out, not_1_out, comparator_2_eq, R1_Used);
  and and_2 (and_2_out, not_2_out, comparator_4_eq, R2_Used);
  and and_3 (and_3_out, not_3_out, comparator_6_eq, R1_Used);
  and and_4 (and_4_out, not_4_out, comparator_8_eq, R2_Used);
  or or_1 (or_1_out, and_1_out, and_2_out);
  and and_5 (and_5_out, or_1_out, EX_RegWrite);
  or or_2 (or_2_out, and_3_out, and_4_out);
  and and_6 (and_6_out, or_2_out, MEM_RegWrite);
  or or_3 (Pause, and_5_out, and_6_out);
endmodule

// 重定向检测
module \重定向数据相关检测  (
  input  R1_Used,
  input  R2_Used,
  input  EX_RegWrite,
  input  MEM_RegWrite,
  input  MEM_MemToReg,
  input  [4:0] R1_num,
  input  [4:0] R2_num,
  input  [4:0] EX_WriteReg_num,
  input  [4:0] MEM_WriteReg_num,
  input  [31:0] EX_IR,
  output Load_Use,
  output [1:0] Forward1,
  output [1:0] Forward2
);

  wire and_1_out, and_2_out, and_3_out, and_4_out, and_9_out, and_10_out, comparator_1_eq, comparator_2_eq,
       comparator_3_eq, comparator_4_eq, comparator_5_eq, comparator_6_eq, comparator_7_eq, comparator_8_eq,
       comparator_9_eq, not_1_out, not_2_out, not_3_out, not_4_out, or_1_out, R1_EX, R1_MEM, R2_EX, R2_MEM;
  wire [1:0] multiplexer_1_out, multiplexer_2_out, multiplexer_3_out, multiplexer_4_out, multiplexer_5_out,
       multiplexer_6_out;

  Comparator #(.width(5)) comparator_1 (.a(R1_num), .b({5{1'b0}}), .eq(comparator_1_eq));  // open: gt, lt
  Comparator #(.width(5)) comparator_2 (.a(R1_num), .b(EX_WriteReg_num), .eq(comparator_2_eq));  // open: gt, lt
  Comparator #(.width(5)) comparator_3 (.a(R2_num), .b({5{1'b0}}), .eq(comparator_3_eq));  // open: gt, lt
  Comparator #(.width(5)) comparator_4 (.a(R2_num), .b(EX_WriteReg_num), .eq(comparator_4_eq));  // open: gt, lt
  Comparator #(.width(5)) comparator_5 (.a(R1_num), .b({5{1'b0}}), .eq(comparator_5_eq));  // open: gt, lt
  Comparator #(.width(5)) comparator_6 (.a(R1_num), .b(MEM_WriteReg_num), .eq(comparator_6_eq));  // open: gt, lt
  Comparator #(.width(5)) comparator_7 (.a(R2_num), .b({5{1'b0}}), .eq(comparator_7_eq));  // open: gt, lt
  Comparator #(.width(5)) comparator_8 (.a(R2_num), .b(MEM_WriteReg_num), .eq(comparator_8_eq));  // open: gt, lt
  not not_1 (not_1_out, comparator_1_eq);
  and and_1 (and_1_out, not_1_out, comparator_2_eq, R1_Used);
  not not_2 (not_2_out, comparator_3_eq);
  and and_2 (and_2_out, not_2_out, comparator_4_eq, R2_Used);
  not not_3 (not_3_out, comparator_5_eq);
  and and_3 (and_3_out, not_3_out, comparator_6_eq, R1_Used);
  not not_4 (not_4_out, comparator_7_eq);
  and and_4 (and_4_out, not_4_out, comparator_8_eq, R2_Used);
  and and_5 (R1_EX, and_1_out, EX_RegWrite);
  and and_6 (R2_EX, and_2_out, EX_RegWrite);
  and and_7 (R1_MEM, and_3_out, MEM_RegWrite);
  and and_8 (R2_MEM, and_4_out, MEM_RegWrite);
  Multiplexer #(.width(2), .enable("false")) multiplexer_1 (
    .in0(2'b00), .in1(2'b01), .out(multiplexer_1_out), .sel(R1_MEM));
  and and_9 (and_9_out, R1_MEM, MEM_MemToReg);
  Multiplexer #(.width(2), .enable("false")) multiplexer_2 (
    .in0(2'b00), .in1(2'b01), .out(multiplexer_2_out), .sel(R2_MEM));
  and and_10 (and_10_out, R2_MEM, MEM_MemToReg);
  Comparator #(.width(6)) comparator_9 (.a(EX_IR[31:26]), .b(6'b100011), .eq(comparator_9_eq));  // open: gt, lt
  and and_11 (Load_Use, comparator_9_eq, or_1_out);
  or or_1 (or_1_out, R1_EX, R2_EX);
  Multiplexer #(.width(2), .enable("false")) multiplexer_3 (
    .in0(multiplexer_4_out), .in1(2'b11), .out(multiplexer_3_out), .sel(R1_EX));
  Multiplexer #(.width(2), .enable("false")) multiplexer_4 (
    .in0(multiplexer_1_out), .in1(2'b10), .out(multiplexer_4_out), .sel(and_9_out));
  Multiplexer #(.width(2), .enable("false")) multiplexer_5 (
    .in0(multiplexer_2_out), .in1(2'b10), .out(multiplexer_5_out), .sel(and_10_out));
  Multiplexer #(.width(2), .enable("false")) multiplexer_6 (
    .in0(multiplexer_5_out), .in1(2'b11), .out(multiplexer_6_out), .sel(R2_EX));
  Multiplexer #(.width(2), .enable("false")) multiplexer_7 (
    .in0(multiplexer_3_out), .in1(2'b00), .out(Forward1), .sel(Load_Use));
  Multiplexer #(.width(2), .enable("false")) multiplexer_8 (
    .in0(multiplexer_6_out), .in1(2'b00), .out(Forward2), .sel(Load_Use));
endmodule
module BHT (
  input  Clk,
  input  EX_Branch,
  input  [31:0] PC,
  input  [31:0] EX_PC,
  input  [31:0] EX_BranchAddr,
  input  EX_Branched,
  output [31:0] JumpAddr,
  output PredictJump
);

  wire A0, A1, A2, A3, A4, A5, A6, A7, and_1_out, comparator_1_eq, comparator_2_eq, comparator_3_eq,
       comparator_4_eq, comparator_5_eq, comparator_6_eq, comparator_7_eq, comparator_8_eq, comparator_9_eq,
       comparator_10_eq, comparator_11_eq, comparator_12_eq, comparator_13_eq, comparator_14_eq,
       comparator_15_eq, comparator_16_eq, decoder_1_out0, decoder_1_out1, decoder_1_out2, decoder_1_out3,
       decoder_1_out4, decoder_1_out5, decoder_1_out6, decoder_1_out7, decoder_2_out0, decoder_2_out1,
       decoder_2_out2, decoder_2_out3, decoder_2_out4, decoder_2_out5, decoder_2_out6, decoder_2_out7,
       EX_Hit, EX_Miss, IF_Hit, IF_Miss, L0, L1, L2, L3, L4, L5, L6, L7, M0, M1, M2, M3, M4, M5, M6, M7,
       not_1_out, not_2_out, not_3_out, not_4_out, not_5_out, not_6_out, not_7_out, not_8_out, or_1_out,
       or_2_out, or_3_out, or_4_out, or_5_out, or_6_out, or_7_out, or_8_out, or_9_out, or_10_out, or_11_out,
       or_12_out, or_13_out, or_14_out, or_17_out, or_18_out, priority_encoder_1_gs, V0, V1, V2, V3, V4, V5,
       V6, V7, WriteL0, WriteL1, WriteL2, WriteL3, WriteL4, WriteL5, WriteL6, WriteL7;
  wire [0:0] controlled_buffer_1_out, controlled_buffer_2_out, controlled_buffer_3_out,
       controlled_buffer_4_out, controlled_buffer_5_out, controlled_buffer_6_out, controlled_buffer_7_out,
       controlled_buffer_8_out;
  wire [1:0] adder_1_out, adder_2_out, adder_3_out, adder_4_out, adder_5_out, adder_6_out, adder_7_out,
       adder_8_out, multiplexer_1_out, multiplexer_2_out, multiplexer_3_out, multiplexer_4_out,
       multiplexer_5_out, multiplexer_6_out, multiplexer_7_out, multiplexer_8_out, multiplexer_9_out,
       multiplexer_10_out, multiplexer_11_out, multiplexer_12_out, multiplexer_13_out, multiplexer_14_out,
       multiplexer_15_out, multiplexer_16_out, multiplexer_17_out, multiplexer_18_out, multiplexer_19_out,
       multiplexer_20_out, multiplexer_21_out, multiplexer_22_out, multiplexer_23_out, multiplexer_24_out,
       multiplexer_25_out, multiplexer_26_out, multiplexer_27_out, multiplexer_28_out, multiplexer_29_out,
       multiplexer_30_out, multiplexer_31_out, multiplexer_32_out, multiplexer_33_out, multiplexer_34_out,
       multiplexer_35_out, multiplexer_36_out, multiplexer_37_out, multiplexer_38_out, multiplexer_39_out,
       multiplexer_40_out, Predict0, Predict1, Predict2, Predict3, Predict4, Predict5, Predict6, Predict7;
  wire [2:0] max3_1_max_num, max3_2_max_num, max3_3_max_num, max3_4_max_num, max3_5_max_num, max3_6_max_num,
       max3_7_max_num, priority_encoder_1_out;
  wire [15:0] C0, C1, C2, C3, C4, C5, C6, C7, max3_1_max, max3_2_max, max3_3_max, max3_4_max, max3_5_max,
       max3_6_max;
  wire [31:0] Tag0, Tag1, Tag2, Tag3, Tag4, Tag5, Tag6, Tag7, \分支目标地址_2_q , \分支目标地址_3_q , \分支目标地址_4_q ,
       \分支目标地址_5_q , \分支目标地址_6_q , \分支目标地址_7_q , \分支目标地址_8_q , \分支目标地址_q ;

  Register #(.width(1)) VALID (.D(1'b1), .en(WriteL0), .Q(V0), .clk(Clk));  // open: clr
  Register #(.width(1)) VALID_2 (.D(1'b1), .en(WriteL1), .Q(V1), .clk(Clk));  // open: clr
  Register #(.width(1)) VALID_3 (.D(1'b1), .en(WriteL2), .Q(V2), .clk(Clk));  // open: clr
  Register #(.width(1)) VALID_4 (.D(1'b1), .en(WriteL3), .Q(V3), .clk(Clk));  // open: clr
  Register #(.width(1)) VALID_5 (.D(1'b1), .en(WriteL4), .Q(V4), .clk(Clk));  // open: clr
  Register #(.width(1)) VALID_6 (.D(1'b1), .en(WriteL5), .Q(V5), .clk(Clk));  // open: clr
  Register #(.width(1)) VALID_7 (.D(1'b1), .en(WriteL6), .Q(V6), .clk(Clk));  // open: clr
  Register #(.width(1)) VALID_8 (.D(1'b1), .en(WriteL7), .Q(V7), .clk(Clk));  // open: clr
  not not_1 (not_1_out, V0);
  not not_2 (not_2_out, V1);
  not not_3 (not_3_out, V2);
  not not_4 (not_4_out, V3);
  not not_5 (not_5_out, V4);
  not not_6 (not_6_out, V5);
  not not_7 (not_7_out, V6);
  not not_8 (not_8_out, V7);
  MAX3 max3_1 (.Y(C1), .X(C0), .Y_num(3'b001), .X_num(3'b000), .MAX(max3_1_max), .Max_num(max3_1_max_num));
  MAX3 max3_2 (.Y(C3), .X(C2), .Y_num(3'b011), .X_num(3'b010), .MAX(max3_2_max), .Max_num(max3_2_max_num));
  MAX3 max3_3 (.Y(C5), .X(C4), .Y_num(3'b101), .X_num(3'b100), .MAX(max3_3_max), .Max_num(max3_3_max_num));
  MAX3 max3_4 (.Y(C7), .X(C6), .Y_num(3'b111), .X_num(3'b110), .MAX(max3_4_max), .Max_num(max3_4_max_num));
  Pull_Resistor pull_resistor_1 (.node(PredictJump));
  assign {PredictJump, controlled_buffer_1_out[0]} = L0 ? Predict0 : 2'bz;  // Controlled_Buffer controlled_buffer_1
  assign {PredictJump, controlled_buffer_2_out[0]} = L1 ? Predict1 : 2'bz;  // Controlled_Buffer controlled_buffer_2
  assign {PredictJump, controlled_buffer_3_out[0]} = L2 ? Predict2 : 2'bz;  // Controlled_Buffer controlled_buffer_3
  assign {PredictJump, controlled_buffer_4_out[0]} = L3 ? Predict3 : 2'bz;  // Controlled_Buffer controlled_buffer_4
  assign {PredictJump, controlled_buffer_5_out[0]} = L4 ? Predict4 : 2'bz;  // Controlled_Buffer controlled_buffer_5
  assign {PredictJump, controlled_buffer_6_out[0]} = L5 ? Predict5 : 2'bz;  // Controlled_Buffer controlled_buffer_6
  assign {PredictJump, controlled_buffer_7_out[0]} = L6 ? Predict6 : 2'bz;  // Controlled_Buffer controlled_buffer_7
  assign {PredictJump, controlled_buffer_8_out[0]} = L7 ? Predict7 : 2'bz;  // Controlled_Buffer controlled_buffer_8
  Priority_Encoder priority_encoder_1 (
    .in0(not_1_out), .in1(not_2_out), .in2(not_3_out), .in3(not_4_out), .in4(not_5_out), .in5(not_6_out),
    .in6(not_7_out), .in7(not_8_out), .out(priority_encoder_1_out), .gs(priority_encoder_1_gs));  // open: en_in, en_out
  MAX3 max3_5 (
    .Y(max3_2_max), .X(max3_1_max), .Y_num(max3_2_max_num), .X_num(max3_1_max_num), .MAX(max3_5_max),
    .Max_num(max3_5_max_num));
  MAX3 max3_6 (
    .Y(max3_4_max), .X(max3_3_max), .Y_num(max3_4_max_num), .X_num(max3_3_max_num), .MAX(max3_6_max),
    .Max_num(max3_6_max_num));
  and and_1 (and_1_out, V0, V1, V2, V3, V4, V5, V6, V7);
  or or_1 (or_1_out, L1, L2, L3, L4, L5, L6, L7, WriteL1, WriteL2, WriteL3, WriteL4, WriteL5, WriteL6, WriteL7);
  or or_2 (or_2_out, L0, L1, L2, L3, L5, L6, L7, WriteL0, WriteL1, WriteL2, WriteL3, WriteL5, WriteL6, WriteL7);
  Register #(.width(32)) \u_分支指令地址  (.D(EX_PC), .en(WriteL0), .Q(Tag0), .clk(Clk));  // open: clr
  Register #(.width(32)) \u_分支指令地址_2  (.D(EX_PC), .en(WriteL1), .Q(Tag1), .clk(Clk));  // open: clr
  Register #(.width(32)) \u_分支指令地址_3  (.D(EX_PC), .en(WriteL2), .Q(Tag2), .clk(Clk));  // open: clr
  Register #(.width(32)) \u_分支指令地址_4  (.D(EX_PC), .en(WriteL3), .Q(Tag3), .clk(Clk));  // open: clr
  Register #(.width(32)) \u_分支指令地址_5  (.D(EX_PC), .en(WriteL4), .Q(Tag4), .clk(Clk));  // open: clr
  Register #(.width(32)) \u_分支指令地址_6  (.D(EX_PC), .en(WriteL5), .Q(Tag5), .clk(Clk));  // open: clr
  Register #(.width(32)) \u_分支指令地址_7  (.D(EX_PC), .en(WriteL6), .Q(Tag6), .clk(Clk));  // open: clr
  Register #(.width(32)) \u_分支指令地址_8  (.D(EX_PC), .en(WriteL7), .Q(Tag7), .clk(Clk));  // open: clr
  Decoder #(.select(3), .disabled(0)) decoder_1 (
    .out0(decoder_1_out0), .out1(decoder_1_out1), .out2(decoder_1_out2), .out3(decoder_1_out3),
    .out4(decoder_1_out4), .out5(decoder_1_out5), .out6(decoder_1_out6), .out7(decoder_1_out7),
    .sel(priority_encoder_1_out), .en(priority_encoder_1_gs));
  Decoder #(.select(3), .disabled(0)) decoder_2 (
    .out0(decoder_2_out0), .out1(decoder_2_out1), .out2(decoder_2_out2), .out3(decoder_2_out3),
    .out4(decoder_2_out4), .out5(decoder_2_out5), .out6(decoder_2_out6), .out7(decoder_2_out7),
    .sel(max3_7_max_num), .en(and_1_out));
  MAX3 max3_7 (
    .Y(max3_6_max), .X(max3_5_max), .Y_num(max3_6_max_num), .X_num(max3_5_max_num), .Max_num(max3_7_max_num));  // open: MAX
  Multiplexer #(.width(2), .enable("false")) multiplexer_1 (
    .in0(2'b00), .in1(2'b01), .out(multiplexer_1_out), .sel(EX_Branched));
  Multiplexer #(.width(2), .enable("false")) multiplexer_2 (
    .in0(2'b11), .in1(2'b01), .out(multiplexer_2_out), .sel(EX_Branched));
  Multiplexer #(.width(2), .enable("false")) multiplexer_3 (
    .in0(2'b01), .in1(2'b00), .out(multiplexer_3_out), .sel(EX_Branched));
  Multiplexer #(.width(2), .enable("false")) multiplexer_4 (
    .in0(2'b01), .in1(2'b11), .out(multiplexer_4_out), .sel(EX_Branched));
  Multiplexer #(.width(2), .enable("false")) multiplexer_5 (
    .in0(2'b00), .in1(2'b01), .out(multiplexer_5_out), .sel(EX_Branched));
  Multiplexer #(.width(2), .enable("false")) multiplexer_6 (
    .in0(2'b11), .in1(2'b01), .out(multiplexer_6_out), .sel(EX_Branched));
  Multiplexer #(.width(2), .enable("false")) multiplexer_7 (
    .in0(2'b01), .in1(2'b00), .out(multiplexer_7_out), .sel(EX_Branched));
  Multiplexer #(.width(2), .enable("false")) multiplexer_8 (
    .in0(2'b01), .in1(2'b11), .out(multiplexer_8_out), .sel(EX_Branched));
  Counter #(.width(16), .max('hffff)) \u_置换标记  (.count(A0), .Q(C0), .clk(Clk), .clr(L0));  // open: load, D, carry
  Counter #(.width(16), .max('hffff)) \u_置换标记_2  (.count(A1), .Q(C1), .clk(Clk), .clr(L1));  // open: load, D, carry
  Counter #(.width(16), .max('hffff)) \u_置换标记_3  (.count(A2), .Q(C2), .clk(Clk), .clr(L2));  // open: load, D, carry
  Counter #(.width(16), .max('hffff)) \u_置换标记_4  (.count(A3), .Q(C3), .clk(Clk), .clr(L3));  // open: load, D, carry
  Counter #(.width(16), .max('hffff)) \u_置换标记_5  (.count(A4), .Q(C4), .clk(Clk), .clr(L4));  // open: load, D, carry
  Counter #(.width(16), .max('hffff)) \u_置换标记_6  (.count(A5), .Q(C5), .clk(Clk), .clr(L5));  // open: load, D, carry
  Counter #(.width(16), .max('hffff)) \u_置换标记_7  (.count(A6), .Q(C6), .clk(Clk), .clr(L6));  // open: load, D, carry
  Counter #(.width(16), .max('hffff)) \u_置换标记_8  (.count(A7), .Q(C7), .clk(Clk), .clr(L7));  // open: load, D, carry
  and and_2 (A0, or_1_out, V0);
  and and_3 (A4, or_2_out, V4);
  Multiplexer #(.select(2), .width(2), .enable("false")) multiplexer_9 (
    .in0(multiplexer_1_out), .in1(multiplexer_2_out), .in2(multiplexer_3_out), .in3(multiplexer_4_out),
    .out(multiplexer_9_out), .sel(Predict0));
  Adder #(.width(2)) adder_1 (.a(Predict0), .b(multiplexer_9_out), .out(adder_1_out));  // open: cin, cout
  Adder #(.width(2)) adder_2 (.a(Predict4), .b(multiplexer_10_out), .out(adder_2_out));  // open: cin, cout
  Multiplexer #(.select(2), .width(2), .enable("false")) multiplexer_10 (
    .in0(multiplexer_5_out), .in1(multiplexer_6_out), .in2(multiplexer_7_out), .in3(multiplexer_8_out),
    .out(multiplexer_10_out), .sel(Predict4));
  or or_3 (or_3_out, decoder_1_out0, decoder_2_out0);
  or or_4 (or_4_out, decoder_1_out1, decoder_2_out1);
  or or_5 (or_5_out, decoder_1_out2, decoder_2_out2);
  or or_6 (or_6_out, decoder_1_out3, decoder_2_out3);
  or or_7 (or_7_out, decoder_1_out4, decoder_2_out4);
  or or_8 (or_8_out, decoder_1_out5, decoder_2_out5);
  or or_9 (or_9_out, decoder_1_out6, decoder_2_out6);
  or or_10 (or_10_out, decoder_1_out7, decoder_2_out7);
  Register #(.width(2)) \u_分支预测历史位  (.D(adder_1_out), .en(M0), .Q(Predict0), .clk(Clk));  // open: clr
  Register #(.width(2)) \u_分支预测历史位_2  (.D(adder_2_out), .en(M4), .Q(Predict4), .clk(Clk));  // open: clr
  assign JumpAddr = L0 ? \分支目标地址_q  : 32'bz;  // Controlled_Buffer controlled_buffer_9
  Register #(.width(32)) \u_分支目标地址  (.D(EX_BranchAddr), .en(WriteL0), .Q(\分支目标地址_q ), .clk(Clk));  // open: clr
  assign JumpAddr = L1 ? \分支目标地址_2_q  : 32'bz;  // Controlled_Buffer controlled_buffer_10
  Register #(.width(32)) \u_分支目标地址_2  (.D(EX_BranchAddr), .en(WriteL1), .Q(\分支目标地址_2_q ), .clk(Clk));  // open: clr
  Register #(.width(32)) \u_分支目标地址_3  (.D(EX_BranchAddr), .en(WriteL2), .Q(\分支目标地址_3_q ), .clk(Clk));  // open: clr
  assign JumpAddr = L2 ? \分支目标地址_3_q  : 32'bz;  // Controlled_Buffer controlled_buffer_11
  assign JumpAddr = L3 ? \分支目标地址_4_q  : 32'bz;  // Controlled_Buffer controlled_buffer_12
  Register #(.width(32)) \u_分支目标地址_4  (.D(EX_BranchAddr), .en(WriteL3), .Q(\分支目标地址_4_q ), .clk(Clk));  // open: clr
  assign JumpAddr = L4 ? \分支目标地址_5_q  : 32'bz;  // Controlled_Buffer controlled_buffer_13
  Register #(.width(32)) \u_分支目标地址_5  (.D(EX_BranchAddr), .en(WriteL4), .Q(\分支目标地址_5_q ), .clk(Clk));  // open: clr
  assign JumpAddr = L5 ? \分支目标地址_6_q  : 32'bz;  // Controlled_Buffer controlled_buffer_14
  Register #(.width(32)) \u_分支目标地址_6  (.D(EX_BranchAddr), .en(WriteL5), .Q(\分支目标地址_6_q ), .clk(Clk));  // open: clr
  Register #(.width(32)) \u_分支目标地址_7  (.D(EX_BranchAddr), .en(WriteL6), .Q(\分支目标地址_7_q ), .clk(Clk));  // open: clr
  assign JumpAddr = L6 ? \分支目标地址_7_q  : 32'bz;  // Controlled_Buffer controlled_buffer_15
  Register #(.width(32)) \u_分支目标地址_8  (.D(EX_BranchAddr), .en(WriteL7), .Q(\分支目标地址_8_q ), .clk(Clk));  // open: clr
  assign JumpAddr = L7 ? \分支目标地址_8_q  : 32'bz;  // Controlled_Buffer controlled_buffer_16
  and and_4 (WriteL0, or_3_out, EX_Miss, EX_Branch);
  and and_5 (WriteL1, or_4_out, EX_Miss, EX_Branch);
  and and_6 (WriteL2, or_5_out, EX_Miss, EX_Branch);
  and and_7 (WriteL3, or_6_out, EX_Miss, EX_Branch);
  and and_8 (WriteL4, or_7_out, EX_Miss, EX_Branch);
  and and_9 (WriteL5, or_8_out, EX_Miss, EX_Branch);
  and and_10 (WriteL6, or_9_out, EX_Miss, EX_Branch);
  and and_11 (WriteL7, or_10_out, EX_Miss, EX_Branch);
  or or_11 (or_11_out, L0, L2, L3, L4, L5, L6, L7, WriteL0, WriteL2, WriteL3, WriteL4, WriteL5, WriteL6, WriteL7);
  or or_12 (or_12_out, L0, L1, L2, L3, L4, L6, L7, WriteL0, WriteL1, WriteL2, WriteL3, WriteL4, WriteL6, WriteL7);
  and and_12 (A1, or_11_out, V1);
  and and_13 (A5, or_12_out, V5);
  Multiplexer #(.width(2), .enable("false")) multiplexer_11 (
    .in0(2'b00), .in1(2'b01), .out(multiplexer_11_out), .sel(EX_Branched));
  Multiplexer #(.width(2), .enable("false")) multiplexer_12 (
    .in0(2'b11), .in1(2'b01), .out(multiplexer_12_out), .sel(EX_Branched));
  Multiplexer #(.width(2), .enable("false")) multiplexer_13 (
    .in0(2'b01), .in1(2'b00), .out(multiplexer_13_out), .sel(EX_Branched));
  Multiplexer #(.width(2), .enable("false")) multiplexer_14 (
    .in0(2'b01), .in1(2'b11), .out(multiplexer_14_out), .sel(EX_Branched));
  Multiplexer #(.width(2), .enable("false")) multiplexer_15 (
    .in0(2'b00), .in1(2'b01), .out(multiplexer_15_out), .sel(EX_Branched));
  Multiplexer #(.width(2), .enable("false")) multiplexer_16 (
    .in0(2'b11), .in1(2'b01), .out(multiplexer_16_out), .sel(EX_Branched));
  Multiplexer #(.width(2), .enable("false")) multiplexer_17 (
    .in0(2'b01), .in1(2'b00), .out(multiplexer_17_out), .sel(EX_Branched));
  Multiplexer #(.width(2), .enable("false")) multiplexer_18 (
    .in0(2'b01), .in1(2'b11), .out(multiplexer_18_out), .sel(EX_Branched));
  Multiplexer #(.select(2), .width(2), .enable("false")) multiplexer_19 (
    .in0(multiplexer_11_out), .in1(multiplexer_12_out), .in2(multiplexer_13_out), .in3(multiplexer_14_out),
    .out(multiplexer_19_out), .sel(Predict1));
  Multiplexer #(.select(2), .width(2), .enable("false")) multiplexer_20 (
    .in0(multiplexer_15_out), .in1(multiplexer_16_out), .in2(multiplexer_17_out), .in3(multiplexer_18_out),
    .out(multiplexer_20_out), .sel(Predict5));
  Comparator #(.width(32)) comparator_1 (.a(PC), .b(Tag0), .eq(comparator_1_eq));  // open: gt, lt
  Comparator #(.width(32)) comparator_2 (.a(PC), .b(Tag1), .eq(comparator_2_eq));  // open: gt, lt
  Comparator #(.width(32)) comparator_3 (.a(PC), .b(Tag2), .eq(comparator_3_eq));  // open: gt, lt
  Comparator #(.width(32)) comparator_4 (.a(PC), .b(Tag3), .eq(comparator_4_eq));  // open: gt, lt
  Comparator #(.width(32)) comparator_5 (.a(PC), .b(Tag4), .eq(comparator_5_eq));  // open: gt, lt
  Comparator #(.width(32)) comparator_6 (.a(PC), .b(Tag5), .eq(comparator_6_eq));  // open: gt, lt
  Comparator #(.width(32)) comparator_7 (.a(PC), .b(Tag6), .eq(comparator_7_eq));  // open: gt, lt
  Comparator #(.width(32)) comparator_8 (.a(PC), .b(Tag7), .eq(comparator_8_eq));  // open: gt, lt
  Comparator #(.width(32)) comparator_9 (.a(EX_PC), .b(Tag0), .eq(comparator_9_eq));  // open: gt, lt
  Comparator #(.width(32)) comparator_10 (.a(EX_PC), .b(Tag1), .eq(comparator_10_eq));  // open: gt, lt
  Comparator #(.width(32)) comparator_11 (.a(EX_PC), .b(Tag2), .eq(comparator_11_eq));  // open: gt, lt
  Comparator #(.width(32)) comparator_12 (.a(EX_PC), .b(Tag3), .eq(comparator_12_eq));  // open: gt, lt
  Comparator #(.width(32)) comparator_13 (.a(EX_PC), .b(Tag4), .eq(comparator_13_eq));  // open: gt, lt
  Comparator #(.width(32)) comparator_14 (.a(EX_PC), .b(Tag5), .eq(comparator_14_eq));  // open: gt, lt
  Comparator #(.width(32)) comparator_15 (.a(EX_PC), .b(Tag6), .eq(comparator_15_eq));  // open: gt, lt
  Comparator #(.width(32)) comparator_16 (.a(EX_PC), .b(Tag7), .eq(comparator_16_eq));  // open: gt, lt
  Register #(.width(2)) \u_分支预测历史位_3  (.D(adder_3_out), .en(M1), .Q(Predict1), .clk(Clk));  // open: clr
  Adder #(.width(2)) adder_3 (.a(Predict1), .b(multiplexer_19_out), .out(adder_3_out));  // open: cin, cout
  Adder #(.width(2)) adder_4 (.a(Predict5), .b(multiplexer_20_out), .out(adder_4_out));  // open: cin, cout
  or or_13 (or_13_out, L0, L1, L3, L4, L5, L6, L7, WriteL0, WriteL1, WriteL3, WriteL4, WriteL5, WriteL6, WriteL7);
  or or_14 (or_14_out, L0, L1, L2, L3, L4, L5, L7, WriteL0, WriteL1, WriteL2, WriteL3, WriteL4, WriteL5, WriteL7);
  Register #(.width(2)) \u_分支预测历史位_4  (.D(adder_4_out), .en(M5), .Q(Predict5), .clk(Clk));  // open: clr
  and and_14 (L0, comparator_1_eq, V0);
  and and_15 (L1, comparator_2_eq, V1);
  and and_16 (L2, comparator_3_eq, V2);
  and and_17 (L3, comparator_4_eq, V3);
  and and_18 (L4, comparator_5_eq, V4);
  and and_19 (L5, comparator_6_eq, V5);
  and and_20 (L6, comparator_7_eq, V6);
  and and_21 (L7, comparator_8_eq, V7);
  and and_22 (M0, comparator_9_eq, V0);
  and and_23 (M1, comparator_10_eq, V1);
  and and_24 (M2, comparator_11_eq, V2);
  and and_25 (M3, comparator_12_eq, V3);
  and and_26 (M4, comparator_13_eq, V4);
  and and_27 (M5, comparator_14_eq, V5);
  and and_28 (M6, comparator_15_eq, V6);
  and and_29 (M7, comparator_16_eq, V7);
  and and_30 (A2, or_13_out, V2);
  and and_31 (A6, or_14_out, V6);
  or or_15 (IF_Hit, L0, L1, L2, L3, L4, L5, L6, L7);
  or or_16 (EX_Hit, M0, M1, M2, M3, M4, M5, M6, M7);
  Multiplexer #(.width(2), .enable("false")) multiplexer_21 (
    .in0(2'b00), .in1(2'b01), .out(multiplexer_21_out), .sel(EX_Branched));
  Multiplexer #(.width(2), .enable("false")) multiplexer_22 (
    .in0(2'b11), .in1(2'b01), .out(multiplexer_22_out), .sel(EX_Branched));
  Multiplexer #(.width(2), .enable("false")) multiplexer_23 (
    .in0(2'b01), .in1(2'b00), .out(multiplexer_23_out), .sel(EX_Branched));
  Multiplexer #(.width(2), .enable("false")) multiplexer_24 (
    .in0(2'b01), .in1(2'b11), .out(multiplexer_24_out), .sel(EX_Branched));
  Multiplexer #(.width(2), .enable("false")) multiplexer_25 (
    .in0(2'b00), .in1(2'b01), .out(multiplexer_25_out), .sel(EX_Branched));
  Multiplexer #(.width(2), .enable("false")) multiplexer_26 (
    .in0(2'b11), .in1(2'b01), .out(multiplexer_26_out), .sel(EX_Branched));
  Multiplexer #(.width(2), .enable("false")) multiplexer_27 (
    .in0(2'b01), .in1(2'b00), .out(multiplexer_27_out), .sel(EX_Branched));
  Multiplexer #(.width(2), .enable("false")) multiplexer_28 (
    .in0(2'b01), .in1(2'b11), .out(multiplexer_28_out), .sel(EX_Branched));
  not not_9 (IF_Miss, IF_Hit);
  not not_10 (EX_Miss, EX_Hit);
  Adder #(.width(2)) adder_5 (.a(Predict2), .b(multiplexer_29_out), .out(adder_5_out));  // open: cin, cout
  Multiplexer #(.select(2), .width(2), .enable("false")) multiplexer_29 (
    .in0(multiplexer_21_out), .in1(multiplexer_22_out), .in2(multiplexer_23_out), .in3(multiplexer_24_out),
    .out(multiplexer_29_out), .sel(Predict2));
  Multiplexer #(.select(2), .width(2), .enable("false")) multiplexer_30 (
    .in0(multiplexer_25_out), .in1(multiplexer_26_out), .in2(multiplexer_27_out), .in3(multiplexer_28_out),
    .out(multiplexer_30_out), .sel(Predict6));
  or or_17 (or_17_out, L0, L1, L2, L4, L5, L6, L7, WriteL0, WriteL1, WriteL2, WriteL4, WriteL5, WriteL6, WriteL7);
  or or_18 (or_18_out, L0, L1, L2, L3, L4, L5, L6, WriteL0, WriteL1, WriteL2, WriteL3, WriteL4, WriteL5, WriteL6);
  Register #(.width(2)) \u_分支预测历史位_5  (.D(adder_5_out), .en(M2), .Q(Predict2), .clk(Clk));  // open: clr
  Adder #(.width(2)) adder_6 (.a(Predict6), .b(multiplexer_30_out), .out(adder_6_out));  // open: cin, cout
  Register #(.width(2)) \u_分支预测历史位_6  (.D(adder_6_out), .en(M6), .Q(Predict6), .clk(Clk));  // open: clr
  and and_32 (A3, or_17_out, V3);
  and and_33 (A7, or_18_out, V7);
  Multiplexer #(.width(2), .enable("false")) multiplexer_31 (
    .in0(2'b00), .in1(2'b01), .out(multiplexer_31_out), .sel(EX_Branched));
  Multiplexer #(.width(2), .enable("false")) multiplexer_32 (
    .in0(2'b11), .in1(2'b01), .out(multiplexer_32_out), .sel(EX_Branched));
  Multiplexer #(.width(2), .enable("false")) multiplexer_33 (
    .in0(2'b01), .in1(2'b00), .out(multiplexer_33_out), .sel(EX_Branched));
  Multiplexer #(.width(2), .enable("false")) multiplexer_34 (
    .in0(2'b01), .in1(2'b11), .out(multiplexer_34_out), .sel(EX_Branched));
  Multiplexer #(.width(2), .enable("false")) multiplexer_35 (
    .in0(2'b00), .in1(2'b01), .out(multiplexer_35_out), .sel(EX_Branched));
  Multiplexer #(.width(2), .enable("false")) multiplexer_36 (
    .in0(2'b11), .in1(2'b01), .out(multiplexer_36_out), .sel(EX_Branched));
  Multiplexer #(.width(2), .enable("false")) multiplexer_37 (
    .in0(2'b01), .in1(2'b00), .out(multiplexer_37_out), .sel(EX_Branched));
  Multiplexer #(.width(2), .enable("false")) multiplexer_38 (
    .in0(2'b01), .in1(2'b11), .out(multiplexer_38_out), .sel(EX_Branched));
  Multiplexer #(.select(2), .width(2), .enable("false")) multiplexer_39 (
    .in0(multiplexer_31_out), .in1(multiplexer_32_out), .in2(multiplexer_33_out), .in3(multiplexer_34_out),
    .out(multiplexer_39_out), .sel(Predict3));
  Multiplexer #(.select(2), .width(2), .enable("false")) multiplexer_40 (
    .in0(multiplexer_35_out), .in1(multiplexer_36_out), .in2(multiplexer_37_out), .in3(multiplexer_38_out),
    .out(multiplexer_40_out), .sel(Predict7));
  Adder #(.width(2)) adder_7 (.a(Predict3), .b(multiplexer_39_out), .out(adder_7_out));  // open: cin, cout
  Adder #(.width(2)) adder_8 (.a(Predict7), .b(multiplexer_40_out), .out(adder_8_out));  // open: cin, cout
  Register #(.width(2)) \u_分支预测历史位_7  (.D(adder_7_out), .en(M3), .Q(Predict3), .clk(Clk));  // open: clr
  Register #(.width(2)) \u_分支预测历史位_8  (.D(adder_8_out), .en(M7), .Q(Predict7), .clk(Clk));  // open: clr

  // Other names for the same wires on the sheet: Tag[31:0] = EX_PC

  // Notes on the sheet:
  //   Cache槽
  //   读缺失逻辑/块载入逻辑
  //   查找逻辑
endmodule

module MAX3 (
  input  [15:0] Y,
  input  [15:0] X,
  input  [2:0] Y_num,
  input  [2:0] X_num,
  output [15:0] MAX,
  output [2:0] Max_num
);

  wire comparator_1_eq, comparator_1_gt, or_1_out;

  Multiplexer #(.width(16), .enable("false")) multiplexer_1 (.in0(Y), .in1(X), .out(MAX), .sel(or_1_out));
  Comparator #(.width(16), .mode("unsigned")) comparator_1 (
    .a(X), .b(Y), .gt(comparator_1_gt), .eq(comparator_1_eq));  // open: lt
  or or_1 (or_1_out, comparator_1_gt, comparator_1_eq);
  Multiplexer #(.width(3), .enable("false")) multiplexer_2 (.in0(Y_num), .in1(X_num), .out(Max_num), .sel(or_1_out));

  // Notes on the sheet:
  //   输出两个输入中的较大值，并输出较大值的3位编号
endmodule
